// Logisim project SuperAlu.circ as structural Verilog: 6 circuits, main circuit main
module main (
  input  [1:0] in_1,
  input  _0___disattiva,
  input  [4:0] in_3,
  input  [31:0] in_4,
  input  [31:0] in_5,
  input  [2:0] in_6,
  input  in_7,
  output [31:0] out_8,
  output [1:0] CF,
  output out_10
);

  wire and_1_out, decoder_1_out0, full_adder_1_s, multiplexer_2_out, multiplexer_3_out, not_1_out, not_3_out,
       not_4_out, or_1_out, or_2_out, or_3_out;
  wire [31:0] controlled_buffer_1_out, controlled_buffer_2_out, controlled_buffer_3_out,
       demultiplexer_1_out0, demultiplexer_1_out1, demultiplexer_2_out0, demultiplexer_2_out1,
       multiplier_1_out, rete_pre_elaborazione_1_out_4, rete_pre_elaborazione_1_out_5, sommatore_32b_1_out_5;

  Decoder #(.select(2), .enable("false")) decoder_1 (.out0(decoder_1_out0), .sel(in_1));  // open: out1, out2, out3
  Demultiplexer #(.width(32), .enable("false")) demultiplexer_1 (
    .out0(demultiplexer_1_out0), .out1(demultiplexer_1_out1), .in(in_4), .sel(_0___disattiva));
  Demultiplexer #(.width(32), .enable("false")) demultiplexer_2 (
    .out0(demultiplexer_2_out0), .out1(demultiplexer_2_out1), .in(in_5), .sel(_0___disattiva));
  assign controlled_buffer_1_out = decoder_1_out0 ? demultiplexer_1_out1 : 32'bz;  // Controlled_Buffer controlled_buffer_1
  assign controlled_buffer_2_out = decoder_1_out0 ? demultiplexer_2_out1 : 32'bz;  // Controlled_Buffer controlled_buffer_2
  Rete_Pre_elaborazione rete_pre_elaborazione_1 (
    .in_1(in_3[2:0]), .in_2(demultiplexer_1_out0), .in_3(demultiplexer_2_out0),
    .out_4(rete_pre_elaborazione_1_out_4), .out_5(rete_pre_elaborazione_1_out_5));
  assign controlled_buffer_3_out = decoder_1_out0 ? multiplier_1_out : 32'bz;  // Controlled_Buffer controlled_buffer_3
  Multiplier #(.width(32)) multiplier_1 (
    .a(controlled_buffer_1_out), .b(controlled_buffer_2_out), .out(multiplier_1_out), .cin({32{1'b0}}));  // open: cout
  Divider divider_1 ();  // open: a, b, out, upper, rem
  Shifter shifter_1 ();  // open: in, dist, out
  Sommatore_32b sommatore_32b_1 (
    .in_2(in_3[3]), .in_3(rete_pre_elaborazione_1_out_4), .in_4(rete_pre_elaborazione_1_out_5),
    .out_5(sommatore_32b_1_out_5), .out_6(CF[1]), .in_1(in_3[4]));
  Multiplexer #(.width(32), .enable("false")) multiplexer_1 (
    .in0(sommatore_32b_1_out_5), .in1(controlled_buffer_3_out), .out(out_8), .sel(_0___disattiva));
  not not_1 (not_1_out, demultiplexer_2_out0[31]);
  or or_1 (or_1_out, out_8[31], out_8[30], out_8[29], out_8[28], out_8[27], out_8[26], out_8[25], out_8[24], out_8[23], out_8[22], out_8[21], out_8[20], out_8[19], out_8[18], out_8[17], out_8[16], out_8[15], out_8[14], out_8[13], out_8[12], out_8[11], out_8[10], out_8[9], out_8[8], out_8[7], out_8[6], out_8[5], out_8[4], out_8[3], out_8[2], out_8[1], out_8[0]);
  not not_2 (CF[0], or_1_out);
  Multiplexer #(.enable("false")) multiplexer_2 (
    .in0(demultiplexer_1_out0[31]), .in1(1'b0), .out(multiplexer_2_out), .sel(in_7));
  Multiplexer #(.enable("false")) multiplexer_3 (.in0(not_1_out), .in1(1'b1), .out(multiplexer_3_out), .sel(in_7));
  and and_1 (and_1_out, CF[0], ~full_adder_1_s);  // AND_Gate
  Full_adder full_adder_1 (.CI(CF[1]), .A(multiplexer_2_out), .B(multiplexer_3_out), .S(full_adder_1_s));  // open: CO
  or or_2 (or_2_out, ~full_adder_1_s, and_1_out);  // OR_Gate
  or or_3 (or_3_out, and_1_out, full_adder_1_s);
  not not_3 (not_3_out, full_adder_1_s);
  Multiplexer #(.select(3), .enable("false")) multiplexer_4 (
    .in0(full_adder_1_s), .in1(not_3_out), .in2(or_3_out), .in3(or_2_out), .in4(and_1_out), .in5(not_4_out),
    .out(out_10), .sel(in_6));  // open: in6, in7
  not not_4 (not_4_out, and_1_out);

  // Other names for the same wires on the sheet: altmod = _0___disattiva

  // Notes on the sheet:
  //   A
  //   B
  //   A
  //   B
  //   A
  //   B
  //   slt
  //   ZF
  //   sge
  //   seq
  //   sle
endmodule

module Rete_Pre_elaborazione (
  input  [2:0] in_1,
  input  [31:0] in_2,
  input  [31:0] in_3,
  output [31:0] out_4,
  output [31:0] out_5
);

  wire [31:0] multiplexer_1_out, not_1_out;

  Multiplexer #(.width(32), .enable("false")) multiplexer_1 (
    .in0(in_3), .in1({32{1'b0}}), .out(multiplexer_1_out), .sel(in_1[1]));
  Multiplexer #(.width(32), .enable("false")) multiplexer_2 (
    .in0(multiplexer_1_out), .in1(not_1_out), .out(out_5), .sel(in_1[0]));
  assign not_1_out = ~multiplexer_1_out;  // NOT_Gate not_1, 32 bits wide
  Multiplexer #(.width(32), .enable("false")) multiplexer_3 (.in0(in_2), .in1({32{1'b0}}), .out(out_4), .sel(in_1[2]));
endmodule

module Sommatore_32b (
  input  in_1,
  input  in_2,
  input  [31:0] in_3,
  input  [31:0] in_4,
  output [31:0] out_5,
  output out_6
);

  wire sommatore_4bit_1_co, sommatore_4bit_2_co, sommatore_4bit_3_co, sommatore_4bit_4_co,
       sommatore_4bit_5_co, sommatore_4bit_6_co, sommatore_4bit_7_co;

  Sommatore_4bit sommatore_4bit_1 (
    .CI(in_2), .CO(sommatore_4bit_1_co), .A(in_3[3:0]), .B(in_4[3:0]), .C(out_5[3:0]), .M(in_1));
  Sommatore_4bit sommatore_4bit_2 (
    .CI(sommatore_4bit_1_co), .CO(sommatore_4bit_2_co), .A(in_3[7:4]), .B(in_4[7:4]), .C(out_5[7:4]), .M(in_1));
  Sommatore_4bit sommatore_4bit_3 (
    .CI(sommatore_4bit_2_co), .CO(sommatore_4bit_3_co), .A(in_3[11:8]), .B(in_4[11:8]), .C(out_5[11:8]),
    .M(in_1));
  Sommatore_4bit sommatore_4bit_4 (
    .CI(sommatore_4bit_3_co), .CO(sommatore_4bit_4_co), .A(in_3[15:12]), .B(in_4[15:12]), .C(out_5[15:12]),
    .M(in_1));
  Sommatore_4bit sommatore_4bit_5 (
    .CI(sommatore_4bit_4_co), .CO(sommatore_4bit_5_co), .A(in_3[19:16]), .B(in_4[19:16]), .C(out_5[19:16]),
    .M(in_1));
  Sommatore_4bit sommatore_4bit_6 (
    .CI(sommatore_4bit_5_co), .CO(sommatore_4bit_6_co), .A(in_3[23:20]), .B(in_4[23:20]), .C(out_5[23:20]),
    .M(in_1));
  Sommatore_4bit sommatore_4bit_7 (
    .CI(sommatore_4bit_6_co), .CO(sommatore_4bit_7_co), .A(in_3[27:24]), .B(in_4[27:24]), .C(out_5[27:24]),
    .M(in_1));
  Sommatore_4bit sommatore_4bit_8 (
    .CI(sommatore_4bit_7_co), .CO(out_6), .A(in_3[31:28]), .B(in_4[31:28]), .C(out_5[31:28]), .M(in_1));
endmodule

module Sommatore_4bit (
  input  M,
  input  CI,
  input  [3:0] A,
  input  [3:0] B,
  output [3:0] C,
  output CO
);

  wire and_1_out, and_2_out, and_3_out, and_4_out, full_adder_1_co, full_adder_2_co, full_adder_3_co,
       full_adder_4_co;

  Full_adder full_adder_1 (.CI(and_1_out), .A(A[0]), .B(B[0]), .S(C[0]), .CO(full_adder_1_co));
  Full_adder full_adder_2 (.CI(and_2_out), .A(A[1]), .B(B[1]), .S(C[1]), .CO(full_adder_2_co));
  Full_adder full_adder_3 (.CI(and_3_out), .A(A[2]), .B(B[2]), .S(C[2]), .CO(full_adder_3_co));
  Full_adder full_adder_4 (.CI(and_4_out), .A(A[3]), .B(B[3]), .S(C[3]), .CO(full_adder_4_co));
  and and_1 (and_1_out, M, CI);
  and and_2 (and_2_out, full_adder_1_co, M);
  and and_3 (and_3_out, full_adder_2_co, M);
  and and_4 (and_4_out, full_adder_3_co, M);
  and and_5 (CO, full_adder_4_co, M);

  // Notes on the sheet:
  //   +
  //   A
  //   B
  //   =
endmodule

module Full_adder (
  input  CI,
  input  A,
  input  B,
  output S,
  output CO
);

  wire half_adder_1_riporto, half_adder_1_somma, half_adder_2_riporto;

  Half_Adder half_adder_1 (.A(A), .B(B), .Somma(half_adder_1_somma), .Riporto(half_adder_1_riporto));
  Half_Adder half_adder_2 (.A(CI), .B(half_adder_1_somma), .Somma(S), .Riporto(half_adder_2_riporto));
  or or_1 (CO, half_adder_2_riporto, half_adder_1_riporto);
endmodule

module Half_Adder (
  input  A,
  input  B,
  output Somma,
  output Riporto
);

  xor xor_1 (Somma, A, B);
  and and_1 (Riporto, A, B);
endmodule
