// Logisim project 32BitRegister.circ as structural Verilog: 1 circuit, main circuit mainReg
module mainReg (
  input  OE1,
  input  OE2,
  input  [31:0] D,
  input  WE,
  input  CK,
  output [31:0] mem,
  output [31:0] U1,
  output [31:0] U2
);

  Register #(.width(32)) register_1 (.D(D), .en(WE), .clk(CK), .Q(mem));  // open: clr
  assign U1 = OE1 ? mem : 32'bz;  // Controlled_Buffer controlled_buffer_1
  assign U2 = OE2 ? mem : 32'bz;  // Controlled_Buffer controlled_buffer_2
endmodule
