// Logisim project DataPath.circ as structural Verilog: 1 circuit, main circuit mainDataPath
module mainDataPath (
  input  CK,
  input  Cin4,
  input  [4:0] AluCtrl,
  input  rs1_en,
  input  rs2_en,
  input  rd_en,
  input  in_7,
  input  [2:0] in_8,
  input  [4:0] rs1,
  input  [4:0] rs2,
  input  [4:0] rd,
  input  [2:0] A,
  input  [2:0] B,
  input  [2:0] C,
  input  [2:0] PC,
  input  [2:0] TEMP,
  input  [2:0] IAR,
  input  [2:0] MAR,
  input  [2:0] MDR,
  input  [1:0] MUX,
  input  Const_en,
  input  [31:0] CONST,
  input  [31:0] DATI_IN,
  output ZF,
  output Co,
  output ris,
  output [31:0] INDIRIZZI,
  output [31:0] DATI_OUT
);

  wire [4:0] multiplexer_2_out, multiplexer_3_out;
  wire [31:0] alumain_1_p9, controlled_buffer_1_out, mainreg_1_mem, mainreg_2_mem, mainreg_3_mem,
       mainreg_4_mem, mainreg_5_mem, mainreg_6_mem, mainreg_7_mem, mainreg_8_mem, mainreg_8_u1,
       multiplexer_4_out, ram_1_dout, ram_2_dout;

  assign controlled_buffer_1_out = Const_en ? CONST : 32'bz;  // Controlled_Buffer controlled_buffer_1
  // Probe on mainreg_1_mem
  mainReg mainreg_1 (
    .D(ram_1_dout), .WE(A[0]), .CK(CK), .OE1(A[1]), .OE2(A[2]), .mem(mainreg_1_mem), .U1(DATI_OUT),
    .U2(controlled_buffer_1_out));
  // Probe on mainreg_2_mem
  mainReg mainreg_2 (
    .D(ram_2_dout), .WE(B[0]), .CK(CK), .OE1(B[1]), .OE2(B[2]), .mem(mainreg_2_mem), .U1(DATI_OUT),
    .U2(controlled_buffer_1_out));
  // Probe on DATI_OUT
  Multiplexer #(.width(32)) multiplexer_1 (
    .in0(controlled_buffer_1_out), .in1(controlled_buffer_1_out), .out(INDIRIZZI), .sel(MUX[1]));
  // Probe on controlled_buffer_1_out
  Multiplexer #(.width(5)) multiplexer_2 (.in0(rs1), .in1(rd), .out(multiplexer_2_out), .sel(rd_en));
  Multiplexer #(.width(5)) multiplexer_3 (.in0(rs2), .in1(rd), .out(multiplexer_3_out), .sel(rd_en));
  // aluMain alumain_1: pin names not known; wires that end beside it: DATI_OUT, controlled_buffer_1_out, AluCtrl, in_7, Cin4, in_8, ris, ZF, alumain_1_p9, Co
  RAM #(.addrWidth(5), .asyncread("true"), .dataWidth(32)) ram_1 (
    .addr(multiplexer_2_out), .we(rd_en), .oe(rs1_en), .clk(CK), .din(mainreg_8_u1), .dout(ram_1_dout));
  RAM #(.addrWidth(5), .asyncread("true"), .dataWidth(32)) ram_2 (
    .addr(multiplexer_3_out), .we(rd_en), .oe(rs2_en), .clk(CK), .din(mainreg_8_u1), .dout(ram_2_dout));
  // Probe on mainreg_3_mem
  mainReg mainreg_3 (
    .D(alumain_1_p9), .WE(PC[0]), .CK(CK), .OE1(PC[1]), .OE2(PC[2]), .mem(mainreg_3_mem), .U1(DATI_OUT),
    .U2(controlled_buffer_1_out));
  // Probe on mainreg_4_mem
  mainReg mainreg_4 (
    .D(alumain_1_p9), .WE(TEMP[0]), .CK(CK), .OE1(TEMP[1]), .OE2(TEMP[2]), .mem(mainreg_4_mem),
    .U1(DATI_OUT), .U2(controlled_buffer_1_out));
  // Probe on mainreg_5_mem
  mainReg mainreg_5 (
    .D(alumain_1_p9), .WE(IAR[0]), .CK(CK), .OE1(IAR[1]), .OE2(IAR[2]), .mem(mainreg_5_mem), .U1(DATI_OUT),
    .U2(controlled_buffer_1_out));
  // Probe on mainreg_6_mem
  mainReg mainreg_6 (
    .D(alumain_1_p9), .WE(MAR[0]), .CK(CK), .OE1(MAR[1]), .OE2(MAR[2]), .mem(mainreg_6_mem), .U1(DATI_OUT),
    .U2(controlled_buffer_1_out));
  // Probe on mainreg_7_mem
  mainReg mainreg_7 (
    .D(multiplexer_4_out), .WE(MDR[0]), .CK(CK), .OE1(MDR[1]), .OE2(MDR[2]), .mem(mainreg_7_mem),
    .U1(DATI_OUT), .U2(controlled_buffer_1_out));
  Multiplexer #(.width(32)) multiplexer_4 (.in0(alumain_1_p9), .in1(DATI_IN), .out(multiplexer_4_out), .sel(MUX[0]));
  // Probe on alumain_1_p9
  // Probe on mainreg_8_mem
  mainReg mainreg_8 (
    .D(alumain_1_p9), .WE(C[0]), .CK(CK), .OE1(C[1]), .OE2(C[2]), .mem(mainreg_8_mem), .U1(mainreg_8_u1));  // open: U2

  // Other names for the same wires on the sheet: mux_dati = MUX[0]; mux_ind = MUX[1]

  // Notes on the sheet:
  //   S1
  //   S2
endmodule
