// Logisim project ALEA_oscilloscopio.circ as structural Verilog: 1 circuit, main circuit main
module main (
  input  in_1
);

  wire and_1_out, not_1_out;

  not not_1 (not_1_out, in_1);
  and and_1 (and_1_out, not_1_out, in_1);
  // Digital_Oscilloscope digital_oscilloscope_1: pin names not known; wires that end beside it: and_1_out, not_1_out
  // Buffer buffer_1 has open pins: in=in_1, out=open
endmodule
