// Logisim project rete_combinatoria.circ as structural Verilog: 6 circuits, main circuit main
module main (
  input  I0,
  input  I1,
  input  I2,
  input  I3,
  input  I4,
  input  I5,
  output U0,
  output U1
);

  wire decoder_1_out0, decoder_1_out1, decoder_1_out2, decoder_1_out3, ha_1_c, ha_1_s, ha_2_c, ha_2_s,
       multiplexer_1_out, nand_1_out, not_1_out;

  Decoder #(.enable("false"), .select(2)) decoder_1 (
    .out0(decoder_1_out0), .out1(decoder_1_out1), .out2(decoder_1_out2), .out3(decoder_1_out3), .sel({I3, I2}));
  HA ha_1 (.A(I1), .B(decoder_1_out0), .S(ha_1_s), .C(ha_1_c));
  not not_1 (not_1_out, decoder_1_out2);
  HA ha_2 (.A(decoder_1_out3), .B(I4), .S(ha_2_s), .C(ha_2_c));
  nand nand_1 (nand_1_out, I0, ha_1_s);
  Multiplexer multiplexer_1 (.in0(ha_2_s), .in1(ha_2_c), .out(multiplexer_1_out), .sel(I5));
  Multiplexer multiplexer_2 (.in0(ha_1_c), .in1(decoder_1_out1), .out(U0), .sel(nand_1_out));
  or or_1 (U1, not_1_out, multiplexer_1_out);

  // Notes on the sheet:
  //   i0
  //   i1
  //   A
  //   A
  //   i0
  //   i1
endmodule

module due (
  input  I0,
  input  I1,
  input  I2,
  input  I3,
  input  I4,
  input  I5,
  output U0,
  output U1
);

  wire decoder_1_out0, decoder_1_out1, decoder_1_out2, decoder_1_out3, ha_2_c, ha_2_s, multiplexer_2_out,
       multiplexer_3_out, nand_1_out, not_1_out, or_2_out, undriven, undriven_2, undriven_3, undriven_4,
       undriven_5;

  Decoder #(.enable("false"), .select(2)) decoder_1 (
    .out0(decoder_1_out0), .out1(decoder_1_out1), .out2(decoder_1_out2), .out3(decoder_1_out3), .sel({I3, I2}));
  HA ha_1 (.A(undriven));  // open: B, S, C
  Multiplexer multiplexer_1 ();  // open: in0, in1, out, sel
  Multiplexer multiplexer_2 (.in0(decoder_1_out3), .in1(I4), .out(multiplexer_2_out), .sel(I5));
  Decoder #(.enable("false")) decoder_2 ();  // open: out0, out1, sel
  Multiplexer multiplexer_3 (.in0(undriven_2), .in1(undriven_3), .out(multiplexer_3_out), .sel(undriven_4));
  HA ha_2 (.A(I1), .B(decoder_1_out0), .S(ha_2_s), .C(ha_2_c));
  not not_1 (not_1_out, decoder_1_out2);
  or or_1 (U1, undriven_5, multiplexer_3_out);
  nand nand_1 (nand_1_out, I0, ha_2_s);
  or or_2 (or_2_out, decoder_1_out1, not_1_out, multiplexer_2_out);
  Multiplexer multiplexer_4 (.in0(ha_2_c), .in1(or_2_out), .out(U0), .sel(nand_1_out));

  // Notes on the sheet:
  //   A
  //   i0
  //   i1
  //   A
  //   i0
  //   i1
  //   A
  //   A
  //   i0
  //   i1
endmodule

module HA (
  input  A,
  input  B,
  output S,
  output C
);

  xor xor_1 (S, A, B);
  and and_1 (C, A, B);

  // Notes on the sheet:
  //   # HALF ADDER
endmodule

module tre (
);

  wire and_1_out, and_2_out, and_3_out, and_4_out, and_5_out, clock_1_out, clock_2_out, decoder_1_out0,
       decoder_1_out1, decoder_1_out2, decoder_1_out3, ha_1_c, ha_1_s, multiplexer_1_out, not_1_out,
       not_2_out, not_3_out, or_1_out, or_2_out, or_3_out, xor_1_out;
  wire [1:0] counter_1_q_2;
  wire [3:0] counter_1_q;

  Counter #(.max('h3f), .width(6)) counter_1 (
    .clk(clock_1_out), .Q({counter_1_q_2, counter_1_q}));  // open: clr, load, up, count, D, carry
  Clock clock_1 (.out(clock_1_out));
  _7_Segment_Display u_7_segment_display_1 ();  // open: g, f, a, b, e, d, c, dp
  // BCD_to_7_Segment_decoder bcd_to_7_segment_decoder_1: pin names not known
  // Binary_to_BCD_converter #(.binvalue(6)) binary_to_bcd_converter_1: pin names not known; wires that end beside it: {counter_1_q_2, counter_1_q}, counter_1_q[0], counter_1_q[1], counter_1_q[2]
  _7_Segment_Display u_7_segment_display_2 ();  // open: g, f, a, b, e, d, c, dp
  // BCD_to_7_Segment_decoder bcd_to_7_segment_decoder_2: pin names not known
  Hex_Digit_Display hex_digit_display_1 (.value({2'b00, counter_1_q_2}));  // open: dp
  Hex_Digit_Display hex_digit_display_2 (.value(counter_1_q));  // open: dp
  not not_1 (not_1_out, counter_1_q[0]);
  and and_1 (and_1_out, not_1_out, not_2_out);
  not not_2 (not_2_out, counter_1_q[3]);
  not not_3 (not_3_out, counter_1_q[0]);
  and and_2 (and_2_out, not_3_out, counter_1_q[1]);
  and and_3 (and_3_out, counter_1_q[0], counter_1_q[3]);
  and and_4 (and_4_out, counter_1_q[0], counter_1_q_2[0]);
  and and_5 (and_5_out, counter_1_q[0], counter_1_q_2[1]);
  Decoder #(.enable("false"), .select(2)) decoder_1 (
    .out0(decoder_1_out0), .out1(decoder_1_out1), .out2(decoder_1_out2), .out3(decoder_1_out3),
    .sel(counter_1_q[3:2]));
  or or_1 (or_1_out, and_1_out, and_2_out, and_3_out, and_4_out, and_5_out);
  or or_2 (or_2_out, counter_1_q[1], decoder_1_out0, decoder_1_out1);
  HA ha_1 (.A(decoder_1_out3), .B(counter_1_q_2[0]), .S(ha_1_s), .C(ha_1_c));
  or or_3 (or_3_out, decoder_1_out2, ha_1_s, ha_1_c, counter_1_q_2[1]);
  Multiplexer multiplexer_1 (.in0(or_2_out), .in1(or_3_out), .out(multiplexer_1_out), .sel(counter_1_q[0]));
  xor xor_1 (xor_1_out, multiplexer_1_out, or_1_out);
  Clock clock_2 (.out(clock_2_out));
  // Digital_Oscilloscope digital_oscilloscope_1: pin names not known; wires that end beside it: clock_2_out, xor_1_out

  // Notes on the sheet:
  //   A
  //   i0
  //   i1
endmodule

module quattro (
);

  wire decoder_1_out0, decoder_1_out1, decoder_1_out2, decoder_1_out3, ha_1_c, ha_1_s, or_1_out, or_2_out,
       undriven, undriven_2, undriven_4, undriven_5;
  wire [1:0] undriven_3;

  Multiplexer multiplexer_1 ();  // open: in0, in1, out, sel
  Decoder #(.enable("false"), .select(2)) decoder_1 (
    .out0(decoder_1_out0), .out1(decoder_1_out1), .out2(decoder_1_out2), .out3(decoder_1_out3),
    .sel(undriven_3));
  or or_1 (or_1_out, undriven_2, decoder_1_out0, decoder_1_out1);
  HA ha_1 (.A(decoder_1_out3), .B(undriven_4), .S(ha_1_s), .C(ha_1_c));
  or or_2 (or_2_out, decoder_1_out2, ha_1_s, ha_1_c, undriven_5);
  Multiplexer multiplexer_2 (.in0(or_1_out), .in1(or_2_out), .sel(undriven));  // open: out

  // Notes on the sheet:
  //   i0
  //   i1
  //   A
endmodule

module test (
  input  [5:0] in_1,
  output [3:0] out_2,
  output [3:0] out_3
);

  // Binary_to_BCD_converter binary_to_bcd_converter_1: pin names not known; wires that end beside it: {3'b000, in_1}, out_2, out_3
endmodule
