// Logisim project UDC.circ as structural Verilog: 4 circuits, main circuit main
module main (
  input  DEBUGGING,
  input  in_2,
  input  in_3,
  input  in_4,
  input  DEBUGGING_2,
  input  CLOCK,
  input  [31:0] in_7,
  input  [1:0] ZF,
  input  R,
  input  READY,
  output [3:0] out_11,
  output [2:0] cond,
  output U,
  output [31:0] out_14,
  output [4:0] RD,
  output [4:0] RS2,
  output [4:0] RS1,
  output rd_2,
  output rs2_2,
  output rs1_2,
  output [31:0] out_21
);

  wire and_1_out, and_2_out, clock_comparator_1_out_3, cop_handler_1_rs1, d_ff_2_q, MI, Mr30,
       multiplexer_1_out, multiplexer_2_out, multiplexer_3_out, multiplexer_4_out, not_1_out, not_2_out,
       not_3_out, or_1_out;
  wire [0:0] d_ff_1_q;
  wire [1:0] controlled_buffer_2_out;
  wire [2:0] master_controller_1_out_4;
  wire [3:0] counter_1_q, main_1_out_2, main_1_out_3, rom_2_data;
  wire [4:0] cop_handler_1_out_14;
  wire [5:0] multiplexer_5_out, n32b_register_1_out_6_2, rom_1_data;
  wire [9:0] multiplexer_6_out;
  wire [15:4] rom_2_data_2;
  wire [19:0] rom_3_data;
  wire [25:0] n32b_register_1_out_6;
  wire [31:0] controlled_buffer_1_out, main_2_out_8;

  and and_1 (and_1_out, d_ff_2_q, in_2);
  or or_1 (or_1_out, DEBUGGING_2, rom_1_data[1], multiplexer_4_out, clock_comparator_1_out_3);
  Multiplexer #(.enable("false")) multiplexer_1 (
    .in0(d_ff_1_q[0]), .in1(R), .out(multiplexer_1_out), .sel(rom_3_data[16]));
  Multiplexer #(.enable("false")) multiplexer_2 (
    .in0(d_ff_2_q), .in1(rom_3_data[1]), .out(multiplexer_2_out), .sel(rom_3_data[0]));
  Master_Controller master_controller_1 (
    .I0(or_1_out), .I1(and_1_out), .in_1(CLOCK), .out_4(master_controller_1_out_4[0]),
    .out_5(master_controller_1_out_4[1]), .out_6(master_controller_1_out_4[2]));
  not not_1 (not_1_out, ZF[0]);
  D_Flip_Flop d_ff_1 (.clk(CLOCK), .D(multiplexer_1_out), .Q(d_ff_1_q[0]));  // open: Qn, preset, en, reset
  D_Flip_Flop d_ff_2 (.clk(CLOCK), .D(multiplexer_2_out), .Q(d_ff_2_q));  // open: Qn, preset, en, reset
  ROM #(.addrWidth(3)) rom_1 (.addr(master_controller_1_out_4), .data({Mr30, MI, rom_1_data}), .sel(1'b1));
  Multiplexer #(.enable("false")) multiplexer_3 (
    .in0(not_1_out), .in1(ZF[0]), .out(multiplexer_3_out), .sel(rom_3_data[14]));
  BCD_ENCODER_main main_1 (.in_1({1'b0, master_controller_1_out_4}), .out_2(main_1_out_2), .out_3(main_1_out_3));
  Multiplexer #(.enable("false")) multiplexer_4 (
    .in0(1'b0), .in1(multiplexer_3_out), .out(multiplexer_4_out), .sel(rom_3_data[15]));
  _7_Segment_Display u_7_segment_display_1 (
    .g(main_1_out_2[3]), .f(main_1_out_2[2]), .a(main_1_out_2[1]), .b(main_1_out_2[0]), .e(main_1_out_3[3]),
    .d(main_1_out_3[2]), .c(main_1_out_3[1]), .dp(main_1_out_3[0]));
  assign controlled_buffer_1_out = out_14[31] ? {{31{1'b0}}, d_ff_1_q[0]} : 32'bz;  // Controlled_Buffer controlled_buffer_1
  // Probe on multiplexer_5_out
  Multiplexer #(.width(6), .enable("false")) multiplexer_5 (
    .in0(n32b_register_1_out_6_2), .in1({6{1'b1}}), .out(multiplexer_5_out), .sel(MI));
  _32b_register u_32b_register_1 (
    .OE1(1'b1), .WE(rom_1_data[1]), .CK(CLOCK), .in_5(in_7),
    .out_6({n32b_register_1_out_6_2, n32b_register_1_out_6}));  // open: OE2, out_7
  and and_2 (and_2_out, CLOCK, 1'b1);
  // Probe on rom_2_data
  ROM #(.addrWidth(6), .dataWidth(16)) rom_2 (
    .addr(multiplexer_5_out), .data({rom_2_data_2, rom_2_data}), .sel(rom_1_data[4]));
  not not_2 (not_2_out, rom_1_data[2]);
  Multiplexer #(.width(10), .enable("false")) multiplexer_6 (
    .in0({10{1'b0}}), .in1(rom_2_data_2[13:4]), .out(multiplexer_6_out), .sel(rom_1_data[4]));
  Counter #(.width(4), .max('hf)) counter_1 (
    .load(not_2_out), .count(rom_1_data[2]), .Q(counter_1_q), .clk(and_2_out), .clr(rom_1_data[1]));  // open: D, carry
  clock_comparator clock_comparator_1 (.in_1(rom_2_data), .in_2(counter_1_q), .out_3(clock_comparator_1_out_3));
  not not_3 (not_3_out, rom_1_data[5]);
  assign controlled_buffer_2_out = rom_1_data[5] ? 2'b10 : 2'bz;  // Controlled_Buffer controlled_buffer_2
  assign controlled_buffer_2_out = not_3_out ? rom_2_data_2[15:14] : 2'bz;  // Controlled_Buffer controlled_buffer_3
  COP_handler cop_handler_1 (
    .in_7(n32b_register_1_out_6), .out_12(controlled_buffer_1_out), .in_6(controlled_buffer_2_out),
    .RX(rom_3_data[9]), .RY(rom_3_data[8]), .RZ(rom_3_data[7]), .in_5(rom_3_data[6]), .out_8(RD), .RS2(RS2),
    .out_14(cop_handler_1_out_14), .RS1(cop_handler_1_rs1), .out_11(rs2_2), .RD(rd_2), .r17(rom_3_data[17]));
  SuperAlu_main main_2 (
    .in_3({1'b1, rom_1_data[0], 3'b000}), .in_4({{22{1'b0}}, multiplexer_6_out}),
    .in_5({{28{1'b0}}, counter_1_q}), .out_8(main_2_out_8), ._0___disattiva(1'b0), .in_1(2'b00));  // open: CF, in_7, in_6, out_10
  ROM #(.addrWidth(16), .dataWidth(20)) rom_3 (
    .addr(main_2_out_8[15:0]), .data({rom_3_data[19:14], U, cond, rom_3_data[9:6], out_11, rom_3_data[1:0]}),
    .sel(1'b1));
  ROM #(.addrWidth(16), .dataWidth(32)) rom_4 (.addr(main_2_out_8[15:0]), .data(out_14), .sel(1'b1));
  Multiplexer #(.width(5)) multiplexer_7 (
    .in0(cop_handler_1_out_14), .in1(5'b11101), .out(RS1), .sel(Mr30));  // open: en
  Multiplexer #(.width(32), .enable("false")) multiplexer_8 (
    .in0(controlled_buffer_1_out), .in1(32'h1), .out(out_21), .sel(rom_3_data[19]));
  or or_2 (rs1_2, cop_handler_1_rs1, Mr30);

  // Other names for the same wires on the sheet: ck = CLOCK; ris = out_14[31]

  // Notes on the sheet:
  //   CF
  //   IEN
  //   RIS
  //   Mastercontrolconfig.txt
  //   contents of rom_1 (hex, n*v repeats v):
  //   a 29 1c dc dc
  //   MUX BRANCH
  //   SET COND MODE
  //   BRANCH MODE
  //   IR
  //   COP MEMORY
  //   IR IN
  //   contents of rom_2 (hex, n*v repeats v):
  //   22 52 82 b2 e2 4112 4142 4172 41a2 41d2 4202 4233 270 c282 c2b2 c2e0 42f1 4311 333 11*0 4632 4663
  //   6a0 6b0 6c0 0 0 0 47a3 47e2 23*0 3f51
  //   RAM2
  //   RAM1
  //   contents of rom_3 (hex, n*v repeats v):
  //   4 300 0 0 80 0 0 80 9*0 40 0 80 40 0 80 9*0 40 0 8 40 4 0 80 7*0 40 1b000 40 c000 40 0 13000 0 80 0
  //   0 0 80 0 0 0 80 0 0 0 80 0 0 0 80 0 0 0 80 40 13000 0 80 40 0 0 80 40 0 0 80 40 0 0 80 40 0 0 80 40
  //   0 0 80 80000 20200 8 0 4 20200 0 3 1 3 13*0 40 10 0 20200 40 0 20 885*0 1 0 80000 0 8 0 0 4 1
  //   contents of rom_4 (hex, n*v repeats v):
  //   40010000 c12a 20404 80840 1000 20404 80849 1000 9*0 20004 80840 1000 20004 80849 1000 9*0 800040
  //   4000404 a000002 800040 26000000 8000802 1000 4042 6*0 c000 42 c000 42 c000 20404 80049 80000804 1000
  //   20404 80040 80000804 1000 20404 0 80000804 1000 20404 0 80000804 1000 20404 80040 80000804 1000
  //   20404 80040 80000804 1000 20004 80049 80000804 1000 20004 80040 80000804 1000 20004 0 80000804 1000
  //   20004 0 80000804 1000 20004 80040 80000804 1000 20004 80040 80000804 1000 800849 4001404 a000002
  //   800042 2600084a 8001802 1000 0 0 204002 13*0 800200 26000000 8000802 1000 800200 4000042 a000002
  //   884*0 108022 4042 20 800849 809002 a000002 4000000 8800002 26000000 8004002
  //   CONSTANT
  //   SEGNALI DI CONTROLLO
  //   RIS
  //   SEGNALI DI COMANDO
endmodule

module clock_comparator (
  input  [3:0] in_1,
  input  [3:0] in_2,
  output out_3
);

  wire xnor_1_out, xnor_2_out, xnor_3_out, xnor_4_out;

  xnor xnor_1 (xnor_1_out, in_1[3], in_2[3]);
  xnor xnor_2 (xnor_2_out, in_1[2], in_2[2]);
  xnor xnor_3 (xnor_3_out, in_1[0], in_2[0]);
  xnor xnor_4 (xnor_4_out, in_1[1], in_2[1]);
  and and_1 (out_3, xnor_1_out, xnor_2_out, xnor_4_out, xnor_3_out);
endmodule

module Master_Controller (
  input  in_1,
  input  I0,
  input  I1,
  output out_4,
  output out_5,
  output out_6
);

  wire and_1_out, and_2_out, and_3_out, and_4_out, and_5_out, and_6_out, and_7_out, not_1_out, or_1_out,
       or_2_out, or_3_out;

  not not_1 (not_1_out, I0);
  and and_1 (and_1_out, not_1_out, out_6);
  and and_2 (and_2_out, ~out_6, ~out_5, ~out_4, I0);  // AND_Gate
  or or_1 (or_1_out, and_2_out, and_3_out);
  and and_3 (and_3_out, ~out_6, ~out_5, ~out_4, I1);  // AND_Gate
  and and_4 (and_4_out, ~out_6, ~out_5, I1);  // AND_Gate
  and and_5 (and_5_out, ~out_6, ~out_5, out_4);  // AND_Gate
  and and_6 (and_6_out, ~out_6, out_5, ~out_4, ~I0);  // AND_Gate
  and and_7 (and_7_out, ~out_6, out_5, out_4);  // AND_Gate
  or or_2 (or_2_out, and_7_out, and_1_out);
  or or_3 (or_3_out, and_4_out, and_5_out, and_6_out);
  D_Flip_Flop d_ff_1 (.clk(in_1), .D(or_1_out), .Q(out_4));  // open: Qn, preset, en, reset
  D_Flip_Flop d_ff_2 (.clk(in_1), .D(or_3_out), .Q(out_5));  // open: Qn, preset, en, reset
  D_Flip_Flop d_ff_3 (.clk(in_1), .D(or_2_out), .Q(out_6));  // open: Qn, preset, en, reset

  // Notes on the sheet:
  //   I1
  //   I0
  //   q1
  //   q2
  //   q0
  //   Q0
  //   Q1
  //   Q2
endmodule

module COP_handler (
  input  r17,
  input  RX,
  input  RY,
  input  RZ,
  input  in_5,
  input  [1:0] in_6,
  input  [25:0] in_7,
  output [4:0] out_8,
  output RD,
  output [4:0] RS2,
  output out_11,
  output [31:0] out_12,
  output RS1,
  output [4:0] out_14
);

  wire and_1_out, and_2_out, and_3_out, and_4_out, and_5_out, and_6_out, and_7_out, and_8_out, and_9_out,
       and_10_out, and_11_out, decoder_1_out0, decoder_1_out1, decoder_1_out2, decoder_1_out3, not_1_out,
       or_1_out, or_2_out;
  wire [4:0] controlled_buffer_6_out, controlled_buffer_10_out;
  wire [6:0] multiplexer_1_out;
  wire [25:0] controlled_buffer_1_out, controlled_buffer_2_out, controlled_buffer_3_out,
       controlled_buffer_4_out;

  Decoder #(.select(2), .enable("false")) decoder_1 (
    .out0(decoder_1_out0), .out1(decoder_1_out1), .out2(decoder_1_out2), .out3(decoder_1_out3), .sel(in_6));
  assign controlled_buffer_1_out = decoder_1_out0 ? in_7 : 26'bz;  // Controlled_Buffer controlled_buffer_1
  assign controlled_buffer_2_out = decoder_1_out1 ? in_7 : 26'bz;  // Controlled_Buffer controlled_buffer_2
  assign controlled_buffer_3_out = decoder_1_out3 ? in_7 : 26'bz;  // Controlled_Buffer controlled_buffer_3
  assign controlled_buffer_4_out = decoder_1_out2 ? in_7 : 26'bz;  // Controlled_Buffer controlled_buffer_4
  and and_1 (and_1_out, decoder_1_out0, RY);
  and and_2 (and_2_out, decoder_1_out0, RX);
  assign RS2 = and_1_out ? controlled_buffer_1_out[20:16] : 5'bz;  // Controlled_Buffer controlled_buffer_5
  assign controlled_buffer_6_out = and_2_out ? controlled_buffer_1_out[25:21] : 5'bz;  // Controlled_Buffer controlled_buffer_6
  and and_3 (and_3_out, decoder_1_out1, RX);
  and and_4 (and_4_out, decoder_1_out1, RZ);
  assign controlled_buffer_6_out = and_3_out ? controlled_buffer_2_out[25:21] : 5'bz;  // Controlled_Buffer controlled_buffer_7
  Multiplexer #(.width(7)) multiplexer_1 (
    .in0({7{1'b0}}), .in1({7{1'b1}}), .out(multiplexer_1_out), .sel(controlled_buffer_3_out[25]));  // open: en
  and and_5 (and_5_out, decoder_1_out2, RX);
  and and_6 (and_6_out, decoder_1_out2, RY);
  assign RS2 = and_6_out ? controlled_buffer_4_out[20:16] : 5'bz;  // Controlled_Buffer controlled_buffer_8
  assign controlled_buffer_6_out = and_5_out ? controlled_buffer_4_out[25:21] : 5'bz;  // Controlled_Buffer controlled_buffer_9
  and and_7 (and_7_out, decoder_1_out0, RZ);
  assign controlled_buffer_10_out = and_7_out ? controlled_buffer_1_out[15:11] : 5'bz;  // Controlled_Buffer controlled_buffer_10
  assign controlled_buffer_10_out = and_4_out ? controlled_buffer_2_out[20:16] : 5'bz;  // Controlled_Buffer controlled_buffer_11
  and and_8 (and_8_out, decoder_1_out0, in_5);
  assign out_12 = and_8_out ? {{21{1'b0}}, controlled_buffer_1_out[10:0]} : 32'bz;  // Controlled_Buffer controlled_buffer_12
  and and_9 (and_9_out, decoder_1_out1, in_5);
  and and_10 (and_10_out, decoder_1_out3, in_5);
  assign out_12 = and_10_out ? {multiplexer_1_out, controlled_buffer_3_out[24:0]} : 32'bz;  // Controlled_Buffer controlled_buffer_13
  and and_11 (and_11_out, decoder_1_out2, in_5);
  assign out_12 = and_11_out ? {{16{1'b0}}, controlled_buffer_4_out[15:0]} : 32'bz;  // Controlled_Buffer controlled_buffer_14
  assign out_12 = and_9_out ? {{16{1'b0}}, controlled_buffer_2_out[15:0]} : 32'bz;  // Controlled_Buffer controlled_buffer_15
  or or_1 (or_1_out, and_2_out, and_3_out, and_5_out);
  or or_2 (or_2_out, and_7_out, and_4_out);
  or or_3 (out_11, and_1_out, and_6_out);
  Multiplexer #(.enable("false")) multiplexer_2 (.in0(or_2_out), .in1(or_1_out), .out(RD), .sel(r17));
  assign RS1 = not_1_out ? or_1_out : 1'bz;  // Controlled_Buffer controlled_buffer_16
  not not_1 (not_1_out, r17);
  assign out_14 = not_1_out ? controlled_buffer_6_out : 5'bz;  // Controlled_Buffer controlled_buffer_17
  Multiplexer #(.width(5), .enable("false")) multiplexer_3 (
    .in0(controlled_buffer_10_out), .in1(controlled_buffer_6_out), .out(out_8), .sel(r17));

  // Other names for the same wires on the sheet: rs1d = r17

  // Notes on the sheet:
  //   ECCEZIONI
  //   RD
  //   RS2
  //   RS1
  //   COST
  //   RD
  //   RS1
  //   COST
  //   RS2
  //   RS1
  //   Accedi a costante
  //   CONSTANT
endmodule
