// Logisim project SuperAlu.circ as structural Verilog: 6 circuits, main circuit alu
module alu (
  input  CI4,
  input  [4:0] in_2,
  input  [31:0] in_3,
  input  [31:0] in_4,
  input  [2:0] in_5,
  input  in_6,
  output [31:0] out_7,
  output [1:0] CF,
  output out_9
);

  wire and_1_out, full_adder_cf5d1299_1_s, multiplexer_1_out, multiplexer_2_out, not_1_out, not_3_out,
       not_4_out, or_1_out, or_2_out, or_3_out;
  wire [31:0] rete_pre_elaborazione_09b0a81e_1_out_4, rete_pre_elaborazione_09b0a81e_1_out_5;

  Rete_Pre_elaborazione_09b0a81e rete_pre_elaborazione_09b0a81e_1 (
    .in_2(in_3), .in_3(in_4), .in_1(in_2[2:0]), .out_4(rete_pre_elaborazione_09b0a81e_1_out_4),
    .out_5(rete_pre_elaborazione_09b0a81e_1_out_5));
  Sommatore_32b_3e0c3645 sommatore_32b_3e0c3645_1 (
    .B(rete_pre_elaborazione_09b0a81e_1_out_5), .CI(in_2[3]), .CI4(CI4), .M(in_2[4]),
    .A(rete_pre_elaborazione_09b0a81e_1_out_4), .out_6(out_7), .out_7(CF[1]));
  not not_1 (not_1_out, in_4[31]);
  or or_1 (or_1_out, out_7[31], out_7[30], out_7[29], out_7[28], out_7[27], out_7[26], out_7[25], out_7[24], out_7[23], out_7[22], out_7[21], out_7[20], out_7[19], out_7[18], out_7[17], out_7[16], out_7[15], out_7[14], out_7[13], out_7[12], out_7[11], out_7[10], out_7[9], out_7[8], out_7[7], out_7[6], out_7[5], out_7[4], out_7[3], out_7[2], out_7[1], out_7[0]);
  not not_2 (CF[0], or_1_out);
  Multiplexer multiplexer_1 (.in0(in_3[31]), .in1(1'b0), .out(multiplexer_1_out), .sel(in_6));
  Multiplexer multiplexer_2 (.in0(not_1_out), .in1(1'b1), .out(multiplexer_2_out), .sel(in_6));
  and and_1 (and_1_out, CF[0], ~full_adder_cf5d1299_1_s);  // AND_Gate
  Full_adder_cf5d1299 full_adder_cf5d1299_1 (
    .CI(CF[1]), .A(multiplexer_1_out), .in_3(multiplexer_2_out), .S(full_adder_cf5d1299_1_s));  // open: CO
  or or_2 (or_2_out, ~full_adder_cf5d1299_1_s, and_1_out);  // OR_Gate
  or or_3 (or_3_out, and_1_out, full_adder_cf5d1299_1_s);
  not not_3 (not_3_out, full_adder_cf5d1299_1_s);
  Multiplexer #(.select(3)) multiplexer_3 (
    .in0(full_adder_cf5d1299_1_s), .in1(not_3_out), .in2(or_3_out), .in3(or_2_out), .in4(and_1_out),
    .in5(not_4_out), .out(out_9), .sel(in_5));  // open: in6, in7
  not not_4 (not_4_out, and_1_out);

  // Notes on the sheet:
  //   A
  //   B
  //   A
  //   B
  //   slt
  //   ZF
  //   sge
  //   seq
  //   sle
endmodule

module Rete_Pre_elaborazione_09b0a81e (
  input  [2:0] in_1,
  input  [31:0] in_2,
  input  [31:0] in_3,
  output [31:0] out_4,
  output [31:0] out_5
);

  wire [31:0] multiplexer_1_out, not_1_out;

  Multiplexer #(.width(32)) multiplexer_1 (.in0(in_3), .in1({32{1'b0}}), .out(multiplexer_1_out), .sel(in_1[1]));
  Multiplexer #(.width(32)) multiplexer_2 (.in0(multiplexer_1_out), .in1(not_1_out), .out(out_5), .sel(in_1[0]));
  assign not_1_out = ~multiplexer_1_out;  // NOT_Gate not_1, 32 bits wide
  Multiplexer #(.width(32)) multiplexer_3 (.in0(in_2), .in1({32{1'b0}}), .out(out_4), .sel(in_1[2]));
endmodule

module Sommatore_32b_3e0c3645 (
  input  M,
  input  CI,
  input  CI4,
  input  [31:0] A,
  input  [31:0] B,
  output [31:0] out_6,
  output out_7
);

  wire sommatore_4bit_63afaf42_1_co, sommatore_4bit_63afaf42_2_co, sommatore_4bit_63afaf42_3_co,
       sommatore_4bit_63afaf42_4_co, sommatore_4bit_63afaf42_5_co, sommatore_4bit_63afaf42_6_co,
       sommatore_4bit_63afaf42_7_co;

  Sommatore_4bit_63afaf42 sommatore_4bit_63afaf42_1 (
    .A(A[3:0]), .B(B[3:0]), .CI(CI), .CI4(CI4), .M(M), .CO(sommatore_4bit_63afaf42_1_co), .C(out_6[3:0]));
  Sommatore_4bit_63afaf42 sommatore_4bit_63afaf42_2 (
    .A(A[7:4]), .B(B[7:4]), .CI(sommatore_4bit_63afaf42_1_co), .M(M), .CO(sommatore_4bit_63afaf42_2_co),
    .C(out_6[7:4]));  // open: CI4
  Sommatore_4bit_63afaf42 sommatore_4bit_63afaf42_3 (
    .A(A[11:8]), .B(B[11:8]), .CI(sommatore_4bit_63afaf42_2_co), .M(M), .CO(sommatore_4bit_63afaf42_3_co),
    .C(out_6[11:8]));  // open: CI4
  Sommatore_4bit_63afaf42 sommatore_4bit_63afaf42_4 (
    .A(A[15:12]), .B(B[15:12]), .CI(sommatore_4bit_63afaf42_3_co), .M(M), .CO(sommatore_4bit_63afaf42_4_co),
    .C(out_6[15:12]));  // open: CI4
  Sommatore_4bit_63afaf42 sommatore_4bit_63afaf42_5 (
    .A(A[19:16]), .B(B[19:16]), .CI(sommatore_4bit_63afaf42_4_co), .M(M), .CO(sommatore_4bit_63afaf42_5_co),
    .C(out_6[19:16]));  // open: CI4
  Sommatore_4bit_63afaf42 sommatore_4bit_63afaf42_6 (
    .A(A[23:20]), .B(B[23:20]), .CI(sommatore_4bit_63afaf42_5_co), .M(M), .CO(sommatore_4bit_63afaf42_6_co),
    .C(out_6[23:20]));  // open: CI4
  Sommatore_4bit_63afaf42 sommatore_4bit_63afaf42_7 (
    .A(A[27:24]), .B(B[27:24]), .CI(sommatore_4bit_63afaf42_6_co), .M(M), .CO(sommatore_4bit_63afaf42_7_co),
    .C(out_6[27:24]));  // open: CI4
  Sommatore_4bit_63afaf42 sommatore_4bit_63afaf42_8 (
    .A(A[31:28]), .B(B[31:28]), .CI(sommatore_4bit_63afaf42_7_co), .M(M), .CO(out_7), .C(out_6[31:28]));  // open: CI4
endmodule

module Sommatore_4bit_63afaf42 (
  input  M,
  input  CI,
  input  [3:0] A,
  input  [3:0] B,
  input  CI4,
  output [3:0] C,
  output CO
);

  wire and_1_out, and_2_out, and_3_out, and_4_out, full_adder_cf5d1299_1_co, full_adder_cf5d1299_2_co,
       full_adder_cf5d1299_3_co, full_adder_cf5d1299_4_co, or_1_out;

  Full_adder_cf5d1299 full_adder_cf5d1299_1 (
    .CI(and_1_out), .A(A[0]), .in_3(B[0]), .CO(full_adder_cf5d1299_1_co), .S(C[0]));
  Full_adder_cf5d1299 full_adder_cf5d1299_2 (
    .CI(and_2_out), .A(A[1]), .in_3(B[1]), .CO(full_adder_cf5d1299_2_co), .S(C[1]));
  or or_1 (or_1_out, and_3_out, CI4);
  Full_adder_cf5d1299 full_adder_cf5d1299_3 (
    .CI(or_1_out), .A(A[2]), .in_3(B[2]), .CO(full_adder_cf5d1299_3_co), .S(C[2]));
  Full_adder_cf5d1299 full_adder_cf5d1299_4 (
    .CI(and_4_out), .A(A[3]), .in_3(B[3]), .CO(full_adder_cf5d1299_4_co), .S(C[3]));
  and and_1 (and_1_out, M, CI);
  and and_2 (and_2_out, full_adder_cf5d1299_1_co, M);
  and and_3 (and_3_out, full_adder_cf5d1299_2_co, M);
  and and_4 (and_4_out, full_adder_cf5d1299_3_co, M);
  and and_5 (CO, full_adder_cf5d1299_4_co, M);

  // Notes on the sheet:
  //   +
  //   A
  //   B
  //   =
endmodule

module Full_adder_cf5d1299 (
  input  CI,
  input  A,
  input  in_3,
  output S,
  output CO
);

  wire half_adder_d61b399e_1_riporto, half_adder_d61b399e_1_somma, half_adder_d61b399e_2_riporto;

  Half_Adder_d61b399e half_adder_d61b399e_1 (
    .A(A), .B(in_3), .Somma(half_adder_d61b399e_1_somma), .Riporto(half_adder_d61b399e_1_riporto));
  Half_Adder_d61b399e half_adder_d61b399e_2 (
    .A(CI), .B(half_adder_d61b399e_1_somma), .Somma(S), .Riporto(half_adder_d61b399e_2_riporto));
  or or_1 (CO, half_adder_d61b399e_2_riporto, half_adder_d61b399e_1_riporto);

  // Notes on the sheet:
  //   B
endmodule

module Half_Adder_d61b399e (
  input  A,
  input  B,
  output Somma,
  output Riporto
);

  xor xor_1 (Somma, A, B);
  and and_1 (Riporto, A, B);
endmodule
