// Logisim project 1_NANOSPHERE.circ as structural Verilog
module main (
  input  in_1,
  input  INT,
  input  in_3
);

  wire a, and_1_out, and_2_out, and_3_out, and_4_out, and_5_out, b1, b2, b3, c, ci0, ci1, ci2, ci3, ck,
       d_ff_1_q, generic_interface_1_out_13, INT_t, intClock, or_1_out, or_2_out, or_3_out;
  wire [0:0] cpu_nano_1_mem_i_o, cpu_nano_1_mem_i_o_2;
  wire [1:0] cpu_nano_1_mem_i_o_3;
  wire [3:0] bin2dec_1__10, bin2dec_1__100, bin2dec_1__1000, bin2dec_1_out_2, bin2dec_1_out_3,
       bin2dec_1_out_4, bin2dec_1_out_6, bin2dec_1_out_8, bin2dec_1_out_10, bin2dec_1_out_11;
  wire [6:0] keyboard_1_data;
  wire [7:0] ledinterface_1_out_led;
  wire [13:0] cpu_nano_1_out_9;
  wire [15:0] clock_2_out_3;
  wire [17:0] cpu_nano_1_out_9_2;
  wire [31:0] clock_2_out_4, cpu_nano_1_out_8, generic_interface_1_out_11, generic_interface_1_out_12,
       generic_interface_1_out_14, generic_interface_2_out_14;

  Clock clock_1 (.out(ck));
  LED led_1 (.in(cpu_nano_1_mem_i_o[0]));
  LED led_2 (.in(cpu_nano_1_mem_i_o_2[0]));
  LED led_3 (.in(cpu_nano_1_mem_i_o_3[0]));
  LED led_4 (.in(cpu_nano_1_mem_i_o_3[1]));
  // Probe on generic_interface_1_out_11
  CPU_nano cpu_nano_1 (
    .in_4(in_1), .MEM_I_O({cpu_nano_1_mem_i_o_3, cpu_nano_1_mem_i_o_2[0], cpu_nano_1_mem_i_o[0]}),
    .in_2(generic_interface_1_out_11), .out_8(cpu_nano_1_out_8),
    .out_9({cpu_nano_1_out_9_2, cpu_nano_1_out_9}), .CK(ck), .in_5(or_1_out));  // open: READY, in_3
  or or_1 (or_1_out, INT, INT_t);
  LED led_5 (.in(ledinterface_1_out_led[6]));
  LED led_6 (.in(ledinterface_1_out_led[7]));
  io_chipsel io_chipsel_1 (
    .in_1({cpu_nano_1_out_9_2, cpu_nano_1_out_9}), .out_2(ci0), .out_3(ci1), .out_4(ci2), .out_5(ci3));  // open: out_6, out_7, out_8, out_9, out_10, out_11, out_12, out_13, out_14, out_15, out_16, out_17, out_18, out_19, out_20, out_21, out_22, out_23, out_24, out_25, out_26, out_27, out_28, out_29, out_30, out_31, out_32, out_33
  // Probe on cpu_nano_1_out_8
  LED led_7 (.in(ledinterface_1_out_led[5]));
  LED led_8 (.in(ledinterface_1_out_led[3]));
  LED led_9 (.in(ledinterface_1_out_led[2]));
  LED led_10 (.in(ledinterface_1_out_led[4]));
  ledinterface ledinterface_1 (
    .OUT_LED(ledinterface_1_out_led), .in_1(ck), .IN_DATA(cpu_nano_1_out_8),
    .Memrd({cpu_nano_1_mem_i_o_3, cpu_nano_1_mem_i_o_2[0], cpu_nano_1_mem_i_o[0]}), .nCS_I_O(c),
    .ADDRESS({cpu_nano_1_out_9_2, cpu_nano_1_out_9}));
  GENERIC_INTERFACE generic_interface_1 (
    .BUFOUT(1'b1), .out_12(generic_interface_1_out_12), .out_14(generic_interface_1_out_14),
    .out_11(generic_interface_1_out_11), .in_3(cpu_nano_1_out_8),
    .in_10({cpu_nano_1_out_9_2, cpu_nano_1_out_9}), .CS(ci0), .IO_WR(cpu_nano_1_mem_i_o_3[1]),
    .IO_RD(cpu_nano_1_mem_i_o_3[0]), .out_13(generic_interface_1_out_13));  // open: in_2, in_5, in_7, in_8
  and and_1 (and_1_out, ci1, cpu_nano_1_mem_i_o_3[0]);
  GENERIC_INTERFACE generic_interface_2 (
    .in_2({{25{1'b0}}, keyboard_1_data}), .in_5(ck), .out_14(generic_interface_2_out_14),
    .out_11(generic_interface_1_out_11), .in_3(cpu_nano_1_out_8),
    .in_10({cpu_nano_1_out_9_2, cpu_nano_1_out_9}), .CS(ci1), .IO_WR(cpu_nano_1_mem_i_o_3[1]),
    .IO_RD(cpu_nano_1_mem_i_o_3[0]));  // open: BUFOUT, out_12, in_7, in_8, out_13
  GENERIC_INTERFACE generic_interface_3 (
    .in_2(clock_2_out_4), .in_5(intClock), .out_11(generic_interface_1_out_11), .in_3(cpu_nano_1_out_8),
    .in_10({cpu_nano_1_out_9_2, cpu_nano_1_out_9}), .CS(ci2), .IO_WR(cpu_nano_1_mem_i_o_3[1]),
    .IO_RD(cpu_nano_1_mem_i_o_3[0]));  // open: BUFOUT, out_12, in_7, in_8, out_14, out_13
  LED led_11 (.in(ledinterface_1_out_led[1]));
  LED led_12 (.in(ledinterface_1_out_led[0]));
  // Probe on generic_interface_1_out_12[6:0]
  // Probe on {cpu_nano_1_out_9_2, cpu_nano_1_out_9}
  and and_2 (and_2_out, cpu_nano_1_mem_i_o[0], a);
  D_Flip_Flop d_ff_1 (.clk(ck), .D(generic_interface_1_out_13), .Q(d_ff_1_q));  // open: Qn, preset, en, reset
  TTY #(.rows(24), .cols(96)) tty_1 (
    .data(generic_interface_1_out_12[6:0]), .clk(d_ff_1_q), .we(1'b1), .clr(generic_interface_1_out_14[0]));
  clock clock_2 (.in_1(12'h40), .in_2(ck), .out_5(intClock), .out_3(clock_2_out_3), .out_4(clock_2_out_4));
  // Probe on clock_2_out_3
  // Probe on clock_2_out_4
  ROM #(.addrWidth(14), .dataWidth(32)) rom_1 (
    .addr(cpu_nano_1_out_9), .data(generic_interface_1_out_11), .sel(and_2_out));
  bin2dec bin2dec_1 (
    .in_1(clock_2_out_4), .out_2(bin2dec_1_out_2), .out_3(bin2dec_1_out_3), .out_4(bin2dec_1_out_4),
    ._1000(bin2dec_1__1000), .out_6(bin2dec_1_out_6), ._100(bin2dec_1__100), .out_10(bin2dec_1_out_10),
    .out_11(bin2dec_1_out_11), .out_8(bin2dec_1_out_8), ._10(bin2dec_1__10));
  or or_2 (or_2_out, cpu_nano_1_mem_i_o_2[0], cpu_nano_1_mem_i_o[0]);
  _7_Segment_Display u_7_segment_display_1 (
    .g(bin2dec_1_out_4[3]), .f(bin2dec_1_out_4[2]), .a(bin2dec_1_out_4[1]), .b(bin2dec_1_out_4[0]),
    .e(bin2dec_1__1000[3]), .d(bin2dec_1__1000[2]), .c(bin2dec_1__1000[1]), .dp(bin2dec_1__1000[0]));
  _7_Segment_Display u_7_segment_display_2 (
    .g(bin2dec_1_out_2[3]), .f(bin2dec_1_out_2[2]), .a(bin2dec_1_out_2[1]), .b(bin2dec_1_out_2[0]),
    .e(bin2dec_1_out_3[3]), .d(bin2dec_1_out_3[2]), .c(bin2dec_1_out_3[1]), .dp(bin2dec_1_out_3[0]));
  and and_3 (and_3_out, or_2_out, b1);
  Keyboard keyboard_1 (.clk(and_1_out), .clr(in_3), .avail(INT_t), .data(keyboard_1_data));  // open: re
  _7_Segment_Display u_7_segment_display_3 (
    .g(bin2dec_1_out_8[3]), .f(bin2dec_1_out_8[2]), .a(bin2dec_1_out_8[1]), .b(bin2dec_1_out_8[0]),
    .e(bin2dec_1__10[3]), .d(bin2dec_1__10[2]), .c(bin2dec_1__10[1]), .dp(bin2dec_1__10[0]));
  _7_Segment_Display u_7_segment_display_4 (
    .g(bin2dec_1_out_6[3]), .f(bin2dec_1_out_6[2]), .a(bin2dec_1_out_6[1]), .b(bin2dec_1_out_6[0]),
    .e(bin2dec_1__100[3]), .d(bin2dec_1__100[2]), .c(bin2dec_1__100[1]), .dp(bin2dec_1__100[0]));
  RAM #(.addrWidth(14), .dataWidth(32), .bus("separate")) ram_1 (
    .addr(cpu_nano_1_out_9), .din(cpu_nano_1_out_8), .data(generic_interface_1_out_11),
    .str(cpu_nano_1_mem_i_o_2[0]), .sel(and_3_out), .clk(ck), .ld(cpu_nano_1_mem_i_o[0]));  // open: clr
  _7_Segment_Display u_7_segment_display_5 (
    .g(bin2dec_1_out_10[3]), .f(bin2dec_1_out_10[2]), .a(bin2dec_1_out_10[1]), .b(bin2dec_1_out_10[0]),
    .e(bin2dec_1_out_11[3]), .d(bin2dec_1_out_11[2]), .c(bin2dec_1_out_11[1]), .dp(bin2dec_1_out_11[0]));
  // Probe on keyboard_1_data
  and and_4 (and_4_out, cpu_nano_1_mem_i_o[0], b2);
  ROM #(.addrWidth(14), .dataWidth(32)) rom_2 (
    .addr(cpu_nano_1_out_9), .data(generic_interface_1_out_11), .sel(and_4_out));
  or or_3 (or_3_out, cpu_nano_1_mem_i_o_2[0], cpu_nano_1_mem_i_o[0]);
  and and_5 (and_5_out, or_3_out, b3);
  RAM #(.addrWidth(14), .dataWidth(32), .bus("separate")) ram_2 (
    .addr(cpu_nano_1_out_9), .din(cpu_nano_1_out_8), .data(generic_interface_1_out_11),
    .str(cpu_nano_1_mem_i_o_2[0]), .sel(and_5_out), .clk(ck), .ld(cpu_nano_1_mem_i_o[0]));  // open: clr
  nano_chipselect nano_chipselect_1 (
    .in_1({cpu_nano_1_out_9_2, cpu_nano_1_out_9}), .out_2(c), .out_5(b1), .out_6(a), .out_4(b2), .out_3(b3));

  // Other names for the same wires on the sheet: nCS1 = c

  // Notes on the sheet:
  //   CMD
  //   memrd
  //   memwr
  //   IOrd
  //   IOwr
  //   CLOCK
  //   [NODO INTERFACCE]
  //   cmd
  //   dout
  //   add
  //   din
  //   DIN
  //   CPU Virtual Shock
  //   7
  //   5
  //   6
  //   DOUT
  //   [NODO CENTRALE]
  //   3
  //   2
  //   4
  //   ADD
  //   add
  //   Dout (from the cpu)
  //   cmd
  //   1
  //   0
  //   memrd
  //   Din (to the cpu) - unico bus che entra nella cpu
  //   DATA
  //   Clock
  //   MAIN ROM (64kB) - BOOTLOADER
  //   # 0000 0000h main first instruction
  //   # 0000 3fffh last address
  //   contents of rom_1 (hex, n*v repeats v):
  //   14010048 9c200001 14010065 9c200001 1401006c 9c200001 1401006c 9c200001 1401006f 9c200001 14010020
  //   9c200001 14010057 9c200001 1401006f 9c200001 14010072 9c200001 1401006c 9c200001 14010064 9c200001
  //   14010021 9c200001 30000000
  //   Clock
  //   # 0000 4000h DB table
  //   # 0000 7fffh last address
  //   RAM 1 (64kB) - BOOT OP MEMORY
  //   RAM 1
  //   BUFFER TASTIERA
  //   RAM 2 (64kB)-INTERRUPT ROUTINES
  //   #0000 8000h Interrupt Routine
  //   #0000 8fffh last address
  //   INTERFACCIA TTY Virtual Shock
  //   RAM 2
  //   contents of rom_2 (hex, n*v repeats v):
  //   7bc10000 7bc20000 98200004 9c200001 28014001 7fc20000 7fc10000 88000000
  //   SPECS:
  //   I/O:
  //   ------------------------------
  //   VIRTUAL SHOCK V1.0
  //   Last Update: 14/03/2022
  //   Bit-Width: 32b
  //   256kB of Address Space
  //   64kB Program Memory
  //   64kB Data Memory
  //   64kB Stack Memory
  //   64kB Routines Memory
  //   MEMORY:
  //   Stack Pointer: R30=ffffh
  //   IVT: R29=8000h
  //   TTY: 0001h bufout, 0003h control
  //   DEVLOG:
  //   -invertiti registri nell' IN
  //   RAM 3 (64kB) - STACK
  //   # 0000 c000h last stack address
  //   # 0000 ffffh stack begin
  //   Leds: 8000h control, 8001h data (La ROM IVT è protetta)
  //   Tastiera: 0004h bufin, 0005h status, 0006h control
  //   -Risolto Bug Buffer Periferiche di I/O, controlla mappatura indirizzi
  //   -Individuato Bug interrupt durante stampa carattere su tty
  //   RAM 3
  //   -La Jump è signed. L'ultimo bit viene usato per riconoscere il segno, l'operando va scritto in complemento a due
  //   #CS I/O
  //   #CS RAM 3
  //   #CS RAM 2
  //   #CS RAM 1
  //   #CS ROM
endmodule

module nano_chipselect (
  input  [31:0] in_1,
  output out_2,
  output out_3,
  output out_4,
  output out_5,
  output out_6
);

  wire and_1_out, and_2_out, and_3_out, and_4_out, not_1_out, not_2_out, not_3_out, not_4_out, not_5_out,
       or_1_out, or_2_out, or_3_out, or_4_out;

  or or_1 (or_1_out, in_1[25], in_1[24], in_1[23], in_1[22], in_1[21]);
  or or_2 (or_2_out, in_1[30], in_1[29], in_1[28], in_1[27], in_1[26]);
  or or_3 (or_3_out, in_1[31], or_2_out, or_1_out, or_4_out);
  not not_1 (not_1_out, or_3_out);
  or or_4 (or_4_out, in_1[20], in_1[19], in_1[18], in_1[17], in_1[16]);
  not not_2 (not_2_out, in_1[14]);
  not not_3 (not_3_out, in_1[15]);
  not not_4 (not_4_out, in_1[15]);
  not not_5 (not_5_out, in_1[14]);
  and and_1 (and_1_out, in_1[15], in_1[14]);
  and and_2 (and_2_out, in_1[15], not_2_out);
  and and_3 (and_3_out, not_3_out, in_1[14]);
  and and_4 (and_4_out, not_4_out, not_5_out);
  and and_5 (out_3, and_1_out, not_1_out);
  and and_6 (out_4, and_2_out, not_1_out);
  and and_7 (out_5, and_3_out, not_1_out);
  and and_8 (out_6, and_4_out, not_1_out);

  assign out_2 = 1'b1;

  // Notes on the sheet:
  //   #CS I/O
  //   #CS RAM 3
  //   #CS RAM 2
  //   #CS RAM 1
  //   #CS ROM
endmodule

module io_chipsel (
  input  [31:0] in_1,
  output out_2,
  output out_3,
  output out_4,
  output out_5,
  output out_6,
  output out_7,
  output out_8,
  output out_9,
  output out_10,
  output out_11,
  output out_12,
  output out_13,
  output out_14,
  output out_15,
  output out_16,
  output out_17,
  output out_18,
  output out_19,
  output out_20,
  output out_21,
  output out_22,
  output out_23,
  output out_24,
  output out_25,
  output out_26,
  output out_27,
  output out_28,
  output out_29,
  output out_30,
  output out_31,
  output out_32,
  output out_33
);

  wire or_1_out, or_2_out, or_3_out, or_4_out, or_5_out, or_6_out;

  or or_1 (or_1_out, in_1[31], in_1[30], in_1[29], in_1[28], in_1[27]);
  or or_2 (or_2_out, in_1[26], in_1[25], in_1[24], in_1[23], in_1[22]);
  or or_3 (or_3_out, in_1[21], in_1[20], in_1[19], in_1[18], in_1[17]);
  or or_4 (or_4_out, or_1_out, or_2_out, or_3_out, or_6_out, or_5_out);
  // NOT_Gate not_1 has open pins: in=or_4_out, out=open
  or or_5 (or_5_out, in_1[11], in_1[10], in_1[9], in_1[8], in_1[7]);
  or or_6 (or_6_out, in_1[16], in_1[15], in_1[14], in_1[13], in_1[12]);
  Decoder #(.select(5)) decoder_1 (
    .out0(out_2), .out1(out_3), .out2(out_4), .out3(out_5), .out4(out_6), .out5(out_7), .out6(out_8),
    .out7(out_9), .out8(out_10), .out9(out_11), .out10(out_12), .out11(out_13), .out12(out_14),
    .out13(out_15), .out14(out_16), .out15(out_17), .out16(out_18), .out17(out_19), .out18(out_20),
    .out19(out_21), .out20(out_22), .out21(out_23), .out22(out_24), .out23(out_25), .out24(out_26),
    .out25(out_27), .out26(out_28), .out27(out_29), .out28(out_30), .out29(out_31), .out30(out_32),
    .out31(out_33), .sel(in_1[6:2]));  // open: en

  // Notes on the sheet:
  //   PROBLEMA CON PERIFERICA I/O! SE IL FILO VA IN ERR IL BUFFER NON CAMPIONA E SI MANGIA LE LETTERE
  //   a
  //   i
endmodule

module CPU_nano (
  input  READY,
  input  [31:0] in_2,
  input  in_3,
  input  in_4,
  input  in_5,
  input  CK,
  output [3:0] MEM_I_O,
  output [31:0] out_8,
  output [31:0] out_9
);

  wire datapath_nano_1_out_38, main_1_rd_2, main_1_rs1_2, main_1_rs2_2, main_1_u;
  wire [1:0] datapath_nano_1_flag;
  wire [2:0] main_1_cond;
  wire [4:0] main_1_rd, main_1_rs1, main_1_rs2;
  wire [4:4] not_1_out;
  wire [31:0] main_1_out_14, main_1_out_21;

  UDC_main main_1 (
    .in_2(in_5), .CLOCK(CK), .out_11(MEM_I_O), .out_14(main_1_out_14), .RD(main_1_rd), .RS2(main_1_rs2),
    .RS1(main_1_rs1), .out_21(main_1_out_21), .in_7(in_2), .in_3(in_4), .in_4(in_3),
    .R(datapath_nano_1_out_38), .cond(main_1_cond), .U(main_1_u), .ZF(datapath_nano_1_flag), .READY(READY),
    .rd_2(main_1_rd_2), .rs1_2(main_1_rs1_2), .rs2_2(main_1_rs2_2));  // open: DEBUGGING, DEBUGGING_2
  not not_1 (not_1_out[4], main_1_out_14[4]);
  DATAPATH_nano datapath_nano_1 (
    .RS1(main_1_rs1), .in_6(main_1_rs2), .in_8(main_1_rd), .we(main_1_out_14[5]), .oe1(main_1_out_14[6]),
    .oe2(main_1_out_14[7]), .we_2(main_1_out_14[8]), .oe1_2(main_1_out_14[9]), .oe2_2(main_1_out_14[10]),
    .we_3(main_1_out_14[11]), .oe1_3(main_1_out_14[12]), .we_4(main_1_out_14[14]), .oe1_4(main_1_out_14[15]),
    .oe2_3(main_1_out_14[16]), .we_5(main_1_out_14[17]), .oe1_5(main_1_out_14[18]),
    .oe2_4(main_1_out_14[19]), .we_6(main_1_out_14[20]), .oe1_6(main_1_out_14[21]),
    .oe2_5(main_1_out_14[22]), .we_7(main_1_out_14[23]), .oe1_7(main_1_out_14[24]),
    .oe2_6(main_1_out_14[25]), .we_8(main_1_out_14[26]), .oe1_8(main_1_out_14[27]),
    .oe2_7(main_1_out_14[28]), .Mux_INDIRIZZI(main_1_out_14[30]), .in_33(in_2), .out_41(out_8),
    .RS2(main_1_rs1_2), .RD(main_1_rs2_2), .in_9(main_1_rd_2), .cond(main_1_cond),
    .M_CI_C2_C1_C0({not_1_out[4], main_1_out_14[3:0]}), .U___1_unsigned(main_1_u), .Clock__TUNNEL(CK),
    .in_36(main_1_out_21), .out_40(out_9), .FLAG(datapath_nano_1_flag), .out_38(datapath_nano_1_out_38),
    .MUX_DATI(main_1_out_14[29]));

  // Notes on the sheet:
  //   UDC
  //   DATI IN
  //   INDIRIZZI
  //   DATI OUT
endmodule

module DATAPATH_nano (
  input  [2:0] cond,
  input  [4:0] M_CI_C2_C1_C0,
  input  U___1_unsigned,
  input  [4:0] RS1,
  input  RS2,
  input  [4:0] in_6,
  input  RD,
  input  [4:0] in_8,
  input  in_9,
  input  we,
  input  oe1,
  input  oe2,
  input  we_2,
  input  oe1_2,
  input  oe2_2,
  input  we_3,
  input  oe1_3,
  input  we_4,
  input  oe1_4,
  input  oe2_3,
  input  we_5,
  input  oe1_5,
  input  oe2_4,
  input  we_6,
  input  oe1_6,
  input  oe2_5,
  input  we_7,
  input  oe1_7,
  input  oe2_6,
  input  we_8,
  input  oe1_8,
  input  oe2_7,
  input  [31:0] in_33,
  input  Mux_INDIRIZZI,
  input  MUX_DATI,
  input  [31:0] in_36,
  input  Clock__TUNNEL,
  output out_38,
  output [1:0] FLAG,
  output [31:0] out_40,
  output [31:0] out_41
);

  wire [4:0] multiplexer_2_out, multiplexer_4_out;
  wire [31:0] controlled_buffer_1_out, controlled_buffer_2_out, main_1_out_8, multiplexer_3_out,
       multiplexer_5_out, ram_1_data, ram_2_data, register32b_1_out_6, register32b_2_out_6,
       register32b_3_out_6, register32b_4_out_6, register32b_5_out_6, register32b_6_out_6,
       register32b_7_out_6, register32b_8_out_6, register32b_8_out_7, undriven;

  register32b register32b_1 (
    .in_2(controlled_buffer_1_out), .out_7(out_41), .out_8(in_36), .WE(we), .CK(Clock__TUNNEL), .OE1(oe1),
    .OE2(oe2), .out_6(register32b_1_out_6));
  // Probe on register32b_2_out_6
  register32b register32b_2 (
    .in_2(controlled_buffer_2_out), .out_7(out_41), .out_8(in_36), .WE(we_2), .CK(Clock__TUNNEL),
    .OE1(oe1_2), .OE2(oe2_2), .out_6(register32b_2_out_6));
  // Probe on register32b_1_out_6
  Multiplexer #(.width(32), .enable("false")) multiplexer_1 (
    .in0(in_36), .in1(in_36), .out(out_40), .sel(Mux_INDIRIZZI));
  // Probe on out_41
  Multiplexer #(.width(5), .enable("false")) multiplexer_2 (.in0(RS1), .in1(in_8), .out(multiplexer_2_out), .sel(in_9));
  Multiplexer #(.width(32), .enable("false")) multiplexer_3 (
    .in0(undriven), .in1(register32b_8_out_7), .out(multiplexer_3_out), .sel(in_9));
  Multiplexer #(.width(5), .enable("false")) multiplexer_4 (
    .in0(in_6), .in1(in_8), .out(multiplexer_4_out), .sel(in_9));
  // Probe on in_36
  RAM #(.addrWidth(5), .dataWidth(32), .bus("separate")) ram_1 (
    .addr(multiplexer_2_out), .din(multiplexer_3_out), .data(ram_1_data), .str(in_9), .sel(1'b1),
    .clk(Clock__TUNNEL), .ld(1'b1));  // open: clr
  RAM #(.addrWidth(5), .dataWidth(32), .bus("separate")) ram_2 (
    .addr(multiplexer_4_out), .din(multiplexer_3_out), .data(ram_2_data), .str(in_9), .sel(1'b1),
    .clk(Clock__TUNNEL), .ld(1'b1));  // open: clr
  register32b register32b_3 (
    .in_2(main_1_out_8), .out_7(out_41), .out_8(in_36), .WE(we_4), .CK(Clock__TUNNEL), .OE1(oe1_4),
    .OE2(oe2_3), .out_6(register32b_3_out_6));
  // Probe on register32b_3_out_6
  register32b register32b_4 (
    .in_2(main_1_out_8), .out_7(out_41), .out_8(in_36), .WE(we_5), .CK(Clock__TUNNEL), .OE1(oe1_5),
    .OE2(oe2_4), .out_6(register32b_4_out_6));
  // Probe on register32b_4_out_6
  register32b register32b_5 (
    .in_2(main_1_out_8), .out_7(out_41), .out_8(in_36), .WE(we_6), .CK(Clock__TUNNEL), .OE1(oe1_6),
    .OE2(oe2_5), .out_6(register32b_5_out_6));
  // Probe on register32b_5_out_6
  register32b register32b_6 (
    .in_2(main_1_out_8), .out_7(out_41), .out_8(in_36), .WE(we_7), .CK(Clock__TUNNEL), .OE1(oe1_7),
    .OE2(oe2_6), .out_6(register32b_6_out_6));
  // Probe on register32b_6_out_6
  register32b register32b_7 (
    .in_2(multiplexer_5_out), .out_7(out_41), .out_8(in_36), .WE(we_8), .CK(Clock__TUNNEL), .OE1(oe1_8),
    .OE2(oe2_7), .out_6(register32b_7_out_6));
  // Probe on register32b_7_out_6
  SuperAlu_main main_1 (
    .in_3(M_CI_C2_C1_C0), .in_4(out_41), .in_5(in_36), .out_8(main_1_out_8), .CF(FLAG),
    .in_7(U___1_unsigned), .in_6(cond), .out_10(out_38), ._0___disattiva(1'b0), .in_1(2'b00));
  assign controlled_buffer_1_out = RS2 ? ram_1_data : 32'bz;  // Controlled_Buffer controlled_buffer_1
  assign controlled_buffer_2_out = RD ? ram_2_data : 32'bz;  // Controlled_Buffer controlled_buffer_2
  Multiplexer #(.width(32), .enable("false")) multiplexer_5 (
    .in0(main_1_out_8), .in1(in_33), .out(multiplexer_5_out), .sel(MUX_DATI));
  // Probe on register32b_8_out_6
  register32b register32b_8 (
    .in_2(main_1_out_8), .out_7(register32b_8_out_7), .WE(we_3), .CK(Clock__TUNNEL), .OE1(oe1_3),
    .out_6(register32b_8_out_6));  // open: out_8, OE2
  // Probe on main_1_out_8

  // Other names for the same wires on the sheet: ck = Clock__TUNNEL

  // Notes on the sheet:
  //   PC
  //   TEMP
  //   IAR
  //   MAR
  //   MDR
  //   A
  //   B
  //   C
  //   CONSTANT
  //   BUS1
  //   BUS2
  //   A
  //   B
  //   INDIRIZZI
  //   BUS1
  //   BUS2
  //   REGISTER FILE
  //   [ALUCTRL]
  //   PC
  //   TEMP
  //   IAR
  //   MAR
  //   MDR
  //   C
  //   DATI IN
  //   DATI OUT
endmodule

module RF (
  input  [4:0] RD,
  input  [4:0] RS1,
  input  in_3,
  input  in_4,
  input  [31:0] in_5,
  input  [4:0] RS2,
  input  in_7,
  input  in_8,
  output [31:0] out_9,
  output [31:0] out_10
);

  wire [4:0] multiplexer_1_out, multiplexer_3_out;
  wire [31:0] controlled_buffer_1_out, controlled_buffer_2_out, multiplexer_2_out, ram_1_data, ram_2_data,
       undriven;

  Multiplexer #(.width(5), .enable("false")) multiplexer_1 (.in0(RS1), .in1(RD), .out(multiplexer_1_out), .sel(in_3));
  Multiplexer #(.width(32), .enable("false")) multiplexer_2 (
    .in0(multiplexer_2_out), .in1(undriven), .out(multiplexer_2_out), .sel(in_3));
  Multiplexer #(.width(5), .enable("false")) multiplexer_3 (.in0(RS2), .in1(RD), .out(multiplexer_3_out), .sel(in_3));
  RAM #(.addrWidth(5), .dataWidth(32), .bus("separate")) ram_1 (
    .addr(multiplexer_1_out), .din(multiplexer_2_out), .data(ram_1_data), .str(1'b1), .sel(1'b1), .clk(in_8),
    .ld(1'b1));  // open: clr
  RAM #(.addrWidth(5), .dataWidth(32), .bus("separate")) ram_2 (
    .addr(multiplexer_3_out), .din(multiplexer_2_out), .data(ram_2_data), .str(1'b1), .sel(1'b1), .clk(in_8),
    .ld(1'b1));  // open: clr
  assign controlled_buffer_1_out = in_4 ? ram_1_data : 32'bz;  // Controlled_Buffer controlled_buffer_1
  assign controlled_buffer_2_out = in_7 ? ram_2_data : 32'bz;  // Controlled_Buffer controlled_buffer_2

  // Other names for the same wires on the sheet: ck = in_8
endmodule

module register32b (
  input  OE1,
  input  [31:0] in_2,
  input  WE,
  input  CK,
  input  OE2,
  output [31:0] out_6,
  output [31:0] out_7,
  output [31:0] out_8
);

  wire [31:0] multiplexer_1_out;

  Multiplexer #(.width(32), .enable("false")) multiplexer_1 (
    .in0(out_6), .in1(in_2), .out(multiplexer_1_out), .sel(WE));
  Register #(.width(32)) register_1 (.D(multiplexer_1_out), .Q(out_6), .clk(CK));  // open: en, clr
  assign out_7 = OE1 ? out_6 : 32'bz;  // Controlled_Buffer controlled_buffer_1
  assign out_8 = OE2 ? out_6 : 32'bz;  // Controlled_Buffer controlled_buffer_2

  // Notes on the sheet:
  //   IN
  //   (attivo alto)
  //   32b register
  //   OUT UNSHADOWED
  //   O1
  //   O2
endmodule

module ttyinterface (
  input  [31:0] in_1,
  input  rd,
  input  [31:0] in_3,
  input  ck,
  output [6:0] out_5,
  output clock_int,
  output clear,
  output oe1
);

  wire d_ff_1_q, not_1_out;

  not not_1 (not_1_out, ck);
  D_Flip_Flop d_ff_1 (.clk(not_1_out), .D(rd), .Q(d_ff_1_q));  // open: Qn, preset, en, reset
  D_Flip_Flop d_ff_2 (.clk(not_1_out), .D(d_ff_1_q), .Q(clock_int));  // open: Qn, preset, en, reset
  or or_1 (oe1, clock_int, d_ff_1_q);

  assign clear = in_3[0];
  assign out_5 = in_1[6:0];

  // Notes on the sheet:
  //   ascii
  //   bufout
  //   CONTROl
endmodule

module ledinterface (
  input  in_1,
  input  [3:0] Memrd,
  input  [31:0] IN_DATA,
  input  nCS_I_O,
  input  [31:0] ADDRESS,
  output [7:0] OUT_LED
);

  wire and_1_out, and_2_out, and_3_out, decoder_1_out0, decoder_1_out1, not_1_out, not_2_out, not_3_out,
       or_1_out, or_2_out, or_3_out, or_4_out, or_5_out, or_6_out, or_7_out, or_8_out, or_9_out;
  wire [31:0] register32b_2_out_7;
  wire [31:8] register32b_1_out_7;

  not not_1 (not_1_out, register32b_2_out_7[0]);
  register32b register32b_1 (
    .in_2(IN_DATA), .out_7({register32b_1_out_7, OUT_LED}), .WE(and_1_out), .CK(in_1), .OE1(not_1_out));  // open: out_8, OE2, out_6
  register32b register32b_2 (
    .in_2(IN_DATA), .out_7(register32b_2_out_7), .WE(and_2_out), .CK(in_1), .OE1(1'b1));  // open: out_8, OE2, out_6
  and and_1 (and_1_out, decoder_1_out0, Memrd[1]);
  and and_2 (and_2_out, decoder_1_out1, Memrd[1]);
  Decoder decoder_1 (.out0(decoder_1_out0), .out1(decoder_1_out1), .sel(not_3_out), .en(and_3_out));
  and and_3 (and_3_out, nCS_I_O, not_2_out);
  not not_2 (not_2_out, or_4_out);
  or or_1 (or_1_out, or_3_out, or_2_out, or_6_out);
  or or_2 (or_2_out, ADDRESS[26], ADDRESS[25], ADDRESS[24], ADDRESS[23], ADDRESS[22]);
  or or_3 (or_3_out, ADDRESS[31], ADDRESS[30], ADDRESS[29], ADDRESS[28], ADDRESS[27]);
  or or_4 (or_4_out, or_1_out, or_7_out, ADDRESS[1]);
  or or_5 (or_5_out, ADDRESS[16], ADDRESS[14], ADDRESS[13], ADDRESS[12]);
  or or_6 (or_6_out, ADDRESS[21], ADDRESS[20], ADDRESS[19], ADDRESS[18], ADDRESS[17]);
  or or_7 (or_7_out, or_5_out, or_8_out, or_9_out);
  or or_8 (or_8_out, ADDRESS[11], ADDRESS[10], ADDRESS[9], ADDRESS[8], ADDRESS[7]);
  not not_3 (not_3_out, ADDRESS[0]);
  or or_9 (or_9_out, ADDRESS[6], ADDRESS[5], ADDRESS[4], ADDRESS[3], ADDRESS[2]);

  // Notes on the sheet:
  //   BUFIN
  //   CONTROL
endmodule

module PIC (
  input  CLOCK,
  input  [7:0] in_2,
  input  IR0,
  input  in_4,
  input  in_5,
  input  in_6,
  input  in_7,
  input  in_8,
  input  IR7,
  input  in_10,
  input  in_11,
  input  INTA,
  output INT,
  output [7:0] out_14
);

  wire and_1_out, and_2_out, and_3_out, and_4_out, and_5_out, and_6_out, and_7_out, and_8_out, and_17_out,
       or_2_out, or_3_out, undriven, undriven_2;
  wire [2:0] priority_encoder_1_out;
  wire [7:0] and_9_out, decoder_1_out7, isr, multiplexer_1_out, multiplexer_2_out, multiplexer_3_out,
       not_1_out, not_2_out, register_1_q, register_2_q, subtractor_1_out;

  and and_1 (and_1_out, IR0, not_1_out[0]);
  and and_2 (and_2_out, in_4, not_1_out[1]);
  and and_3 (and_3_out, in_5, not_1_out[2]);
  and and_4 (and_4_out, in_6, not_1_out[3]);
  and and_5 (and_5_out, in_7, not_1_out[4]);
  and and_6 (and_6_out, in_8, not_1_out[5]);
  and and_7 (and_7_out, IR7, not_1_out[6]);
  and and_8 (and_8_out, in_10, not_1_out[7]);
  assign not_1_out = ~isr;  // NOT_Gate not_1, 8 bits wide
  Register register_1 (.D(in_2), .Q(register_1_q), .clk(CLOCK));  // open: en, clr
  assign not_2_out = ~register_1_q;  // NOT_Gate not_2, 8 bits wide
  and and_9 (and_9_out[0], and_1_out, not_2_out[0]);
  and and_10 (and_9_out[1], and_2_out, not_2_out[1]);
  and and_11 (and_9_out[2], and_3_out, not_2_out[2]);
  and and_12 (and_9_out[3], and_4_out, not_2_out[3]);
  and and_13 (and_9_out[4], and_5_out, not_2_out[4]);
  and and_14 (and_9_out[5], and_6_out, not_2_out[5]);
  and and_15 (and_9_out[6], and_7_out, not_2_out[6]);
  and and_16 (and_9_out[7], and_8_out, not_2_out[7]);
  Multiplexer #(.width(8), .enable("false")) multiplexer_1 (
    .in0(register_2_q), .in1(and_9_out), .out(multiplexer_1_out), .sel(in_11));
  Register register_2 (.D(multiplexer_2_out), .Q(register_2_q), .clk(CLOCK));  // open: en, clr
  Multiplexer #(.width(8), .enable("false")) multiplexer_2 (
    .in0(multiplexer_1_out), .in1(subtractor_1_out), .out(multiplexer_2_out), .sel(and_17_out));
  or or_1 (INT, or_2_out, or_3_out);
  or or_2 (or_2_out, register_2_q[7], register_2_q[6], register_2_q[5], register_2_q[4], register_2_q[3]);
  or or_3 (or_3_out, register_2_q[2], register_2_q[1], register_2_q[0]);
  // Probe on register_2_q
  Subtractor subtractor_1 (.a(register_2_q), .b(decoder_1_out7), .out(subtractor_1_out));  // open: bin, bout
  and and_17 (and_17_out, INT, INTA);
  Priority_Encoder priority_encoder_1 (
    .in0(register_2_q[7]), .in1(register_2_q[6]), .in2(register_2_q[5]), .in3(register_2_q[4]),
    .in4(register_2_q[3]), .in5(register_2_q[2]), .in6(register_2_q[1]), .in7(register_2_q[0]),
    .out(priority_encoder_1_out));  // open: en_in, gs, en_out
  Decoder #(.select(3), .enable("false")) decoder_1 (
    .out0(decoder_1_out7[7]), .out1(decoder_1_out7[6]), .out2(decoder_1_out7[5]), .out3(decoder_1_out7[4]),
    .out4(decoder_1_out7[3]), .out5(decoder_1_out7[2]), .out6(decoder_1_out7[1]), .out7(decoder_1_out7[0]),
    .sel(priority_encoder_1_out));
  Multiplexer #(.width(8), .enable("false")) multiplexer_3 (
    .in0(isr), .in1(decoder_1_out7), .out(multiplexer_3_out), .sel(and_17_out));
  Register register_3 (.D(multiplexer_3_out), .Q(isr), .clk(CLOCK), .clr(undriven));  // open: en
  // Probe on isr
  assign out_14 = undriven_2 ? isr : 8'bz;  // Controlled_Buffer controlled_buffer_1

  // Other names for the same wires on the sheet: ck = CLOCK

  // Notes on the sheet:
  //   isrnot
  //   IMR
  //   mask
  //   IRR
  //   WE ISR + IRR
  //   ISR
endmodule

module GENERIC_INTERFACE (
  input  IO_WR,
  input  [31:0] in_2,
  input  [31:0] in_3,
  input  IO_RD,
  input  in_5,
  input  BUFOUT,
  input  [31:0] in_7,
  input  in_8,
  input  CS,
  input  [31:0] in_10,
  output [31:0] out_11,
  output [31:0] out_12,
  output out_13,
  output [31:0] out_14
);

  wire and_1_out, and_5_out, and_6_out, decoder_1_out0, decoder_1_out1, decoder_1_out2, decoder_1_out3, oei,
       oes;
  wire [1:0] multiplexer_1_out;
  wire [31:0] register32b_2_out_6;

  register32b register32b_1 (.in_2(in_2), .out_7(out_11), .WE(1'b1), .CK(in_5), .OE1(oei));  // open: out_8, OE2, out_6
  register32b register32b_2 (
    .in_2(in_3), .out_7(out_12), .WE(1'b1), .CK(out_13), .OE1(BUFOUT), .out_6(register32b_2_out_6));  // open: out_8, OE2
  register32b register32b_3 (.in_2(in_7), .out_7(out_11), .WE(1'b1), .CK(in_8), .OE1(oes));  // open: out_8, OE2, out_6
  register32b register32b_4 (
    .in_2(in_3), .out_7(out_14), .WE(1'b1), .CK(and_5_out), .OE1(1'b1));  // open: out_8, OE2, out_6
  // Probe on register32b_2_out_6
  and and_1 (and_1_out, IO_WR, CS);
  and and_2 (oei, decoder_1_out0, and_6_out);
  and and_3 (out_13, decoder_1_out1, and_1_out);
  and and_4 (oes, decoder_1_out2, and_6_out);
  and and_5 (and_5_out, decoder_1_out3, and_1_out);
  and and_6 (and_6_out, IO_RD, CS);
  Decoder #(.select(2)) decoder_1 (
    .out0(decoder_1_out0), .out1(decoder_1_out1), .out2(decoder_1_out2), .out3(decoder_1_out3),
    .sel(multiplexer_1_out));  // open: en
  Multiplexer #(.width(2)) multiplexer_1 (
    .in0(2'b00), .in1(in_10[1:0]), .out(multiplexer_1_out), .sel(CS));  // open: en

  // Other names for the same wires on the sheet: bufi[31:0] = out_11; stat[31:0] = out_11

  // Notes on the sheet:
  //   BUFIN
  //   STATUS
  //   CONTROL
  //   DOUT
  //   DATI IN
  //   DATI OUT
  //   b0
  //   b1
  //   ADDRESS
  //   (INTERFACCE ALLINEATE)
endmodule

module clock (
  input  [11:0] in_1,
  input  in_2,
  output [15:0] out_3,
  output [31:0] out_4,
  output out_5
);

  wire and_1_out, and_2_out, and_4_out, xnor_1_out, xnor_2_out, xnor_3_out, xnor_4_out, xnor_5_out,
       xnor_6_out, xnor_7_out, xnor_8_out, xnor_9_out, xnor_10_out, xnor_11_out, xnor_12_out;
  wire [11:0] counter_1_q;

  Counter #(.width(12), .max('hfff)) counter_1 (
    .count(1'b1), .Q(counter_1_q), .clk(in_2), .clr(out_5));  // open: load, D, carry
  xnor xnor_1 (xnor_1_out, counter_1_q[11], in_1[11]);
  xnor xnor_2 (xnor_2_out, counter_1_q[9], in_1[9]);
  xnor xnor_3 (xnor_3_out, counter_1_q[8], in_1[8]);
  xnor xnor_4 (xnor_4_out, counter_1_q[10], in_1[10]);
  and and_1 (and_1_out, xnor_1_out, xnor_4_out, xnor_2_out, xnor_3_out);
  xnor xnor_5 (xnor_5_out, counter_1_q[6], in_1[6]);
  xnor xnor_6 (xnor_6_out, counter_1_q[7], in_1[7]);
  and and_2 (and_2_out, xnor_6_out, xnor_5_out, xnor_7_out);
  xnor xnor_7 (xnor_7_out, counter_1_q[5], in_1[5]);
  xnor xnor_8 (xnor_8_out, counter_1_q[4], in_1[4]);
  and and_3 (out_5, and_1_out, and_2_out, and_4_out);
  xnor xnor_9 (xnor_9_out, counter_1_q[3], in_1[3]);
  xnor xnor_10 (xnor_10_out, counter_1_q[2], in_1[2]);
  and and_4 (and_4_out, xnor_8_out, xnor_9_out, xnor_10_out, xnor_12_out, xnor_11_out);
  xnor xnor_11 (xnor_11_out, counter_1_q[0], in_1[0]);
  xnor xnor_12 (xnor_12_out, counter_1_q[1], in_1[1]);
  Counter #(.width(32), .max('hffffffff)) counter_2 (
    .count(1'b1), .Q({out_4[31:16], out_3}), .clk(out_5));  // open: load, D, carry, clr

  assign out_4[15:0] = out_3;
endmodule

module bin2dec (
  input  [31:0] in_1,
  output [3:0] out_2,
  output [3:0] out_3,
  output [3:0] out_4,
  output [3:0] _1000,
  output [3:0] out_6,
  output [3:0] _100,
  output [3:0] out_8,
  output [3:0] _10,
  output [3:0] out_10,
  output [3:0] out_11
);

  wire [3:0] subtractor_5_out;
  wire [15:0] divider_1_out, divider_2_out, divider_3_out, divider_4_out, multiplier_1_out, multiplier_2_out,
       multiplier_3_out, multiplier_4_out, multiplier_5_out, multiplier_6_out, multiplier_7_out,
       multiplier_8_out, multiplier_9_out, multiplier_10_out, subtractor_1_out, subtractor_2_out,
       subtractor_3_out, subtractor_4_out, subtractor_6_out, subtractor_7_out, subtractor_8_out,
       subtractor_9_out, subtractor_10_out;
  wire [15:4] subtractor_5_out_2;

  Divider #(.width(16)) divider_1 (.a(in_1[15:0]), .b(16'h2710), .out(divider_1_out));  // open: upper, rem
  Divider #(.width(16)) divider_2 (.a(in_1[15:0]), .b(16'h3e8), .out(divider_2_out));  // open: upper, rem
  Divider #(.width(16)) divider_3 (.a(in_1[15:0]), .b(16'h64), .out(divider_3_out));  // open: upper, rem
  Divider #(.width(16)) divider_4 (.a(in_1[15:0]), .b(16'ha), .out(divider_4_out));  // open: upper, rem
  Multiplier #(.width(16)) multiplier_1 (.a(divider_1_out), .b(16'ha), .out(multiplier_1_out));  // open: cin, cout
  Subtractor #(.width(16)) subtractor_1 (
    .a(divider_2_out), .b(multiplier_1_out), .out(subtractor_1_out));  // open: bin, bout
  Multiplier #(.width(16)) multiplier_2 (.a(multiplier_1_out), .b(16'ha), .out(multiplier_2_out));  // open: cin, cout
  Multiplier #(.width(16)) multiplier_3 (.a(subtractor_1_out), .b(16'ha), .out(multiplier_3_out));  // open: cin, cout
  Multiplier #(.width(16)) multiplier_4 (.a(multiplier_2_out), .b(16'ha), .out(multiplier_4_out));  // open: cin, cout
  Multiplier #(.width(16)) multiplier_5 (.a(multiplier_4_out), .b(16'ha), .out(multiplier_5_out));  // open: cin, cout
  Subtractor #(.width(16)) subtractor_2 (
    .a(divider_4_out), .b(multiplier_4_out), .out(subtractor_2_out));  // open: bin, bout
  Subtractor #(.width(16)) subtractor_3 (
    .a(in_1[15:0]), .b(multiplier_5_out), .out(subtractor_3_out));  // open: bin, bout
  Subtractor #(.width(16)) subtractor_4 (
    .a(divider_3_out), .b(multiplier_2_out), .out(subtractor_4_out));  // open: bin, bout
  Multiplier #(.width(16)) multiplier_6 (.a(multiplier_3_out), .b(16'ha), .out(multiplier_6_out));  // open: cin, cout
  Subtractor #(.width(16)) subtractor_5 (
    .a(subtractor_4_out), .b(multiplier_3_out), .out({subtractor_5_out_2, subtractor_5_out}));  // open: bin, bout
  Subtractor #(.width(16)) subtractor_6 (
    .a(subtractor_2_out), .b(multiplier_6_out), .out(subtractor_6_out));  // open: bin, bout
  Multiplier #(.width(16)) multiplier_7 (.a(multiplier_6_out), .b(16'ha), .out(multiplier_7_out));  // open: cin, cout
  Subtractor #(.width(16)) subtractor_7 (
    .a(subtractor_3_out), .b(multiplier_7_out), .out(subtractor_7_out));  // open: bin, bout
  Multiplier #(.width(16)) multiplier_8 (
    .a({subtractor_5_out_2, subtractor_5_out}), .b(16'ha), .out(multiplier_8_out));  // open: cin, cout
  Subtractor #(.width(16)) subtractor_8 (
    .a(subtractor_6_out), .b(multiplier_8_out), .out(subtractor_8_out));  // open: bin, bout
  Multiplier #(.width(16)) multiplier_9 (.a(multiplier_8_out), .b(16'ha), .out(multiplier_9_out));  // open: cin, cout
  BCD_ENCODER_main main_1 (.in_1(divider_1_out[3:0]), .out_2(out_2), .out_3(out_3));
  Multiplier #(.width(16)) multiplier_10 (.a(subtractor_8_out), .b(16'ha), .out(multiplier_10_out));  // open: cin, cout
  Subtractor #(.width(16)) subtractor_9 (
    .a(subtractor_7_out), .b(multiplier_9_out), .out(subtractor_9_out));  // open: bin, bout
  BCD_ENCODER_main main_2 (.in_1(subtractor_1_out[3:0]), .out_2(out_4), .out_3(_1000));
  BCD_ENCODER_main main_3 (.in_1(subtractor_5_out), .out_2(out_6), .out_3(_100));
  Subtractor #(.width(16)) subtractor_10 (
    .a(subtractor_9_out), .b(multiplier_10_out), .out(subtractor_10_out));  // open: bin, bout
  BCD_ENCODER_main main_4 (.in_1(subtractor_8_out[3:0]), .out_2(out_8), .out_3(_10));
  BCD_ENCODER_main main_5 (.in_1(subtractor_10_out[3:0]), .out_2(out_10), .out_3(out_11));

  // Notes on the sheet:
  //   BINARY
  //   3
  //   32
  //   327
  //   3276
  //   32768
  //   3
  //   30
  //   32
  //   30
  //   300
  //   2
  //   3000
  //   3000
  //   30000
  //   32768
  //   30000
  //   20
  //   327
  //   300
  //   3276
  //   276
  //   27
  //   20
  //   200
  //   2768
  //   7
  //   76
  //   2000
  //   768
  //   70
  //   6
  //   700
  //   10000
  //   65
  //   60
endmodule

module TTY_SCHEMA (
  input  [31:0] in_1,
  input  in_2,
  input  in_3,
  input  in_4,
  input  [31:0] in_5
);

  wire d_ff_1_q, generic_interface_1_out_13;
  wire [31:0] generic_interface_1_out_12;

  GENERIC_INTERFACE generic_interface_1 (
    .BUFOUT(1'b1), .out_12(generic_interface_1_out_12), .in_3(in_1), .in_10(in_5), .CS(in_2), .IO_WR(in_2),
    .out_13(generic_interface_1_out_13));  // open: in_2, in_5, in_7, in_8, out_14, out_11, IO_RD
  // Probe on generic_interface_1_out_12
  TTY tty_1 (.data(generic_interface_1_out_12[6:0]), .clk(d_ff_1_q), .clr(in_3));  // open: we
  D_Flip_Flop d_ff_1 (.clk(in_4), .D(generic_interface_1_out_13), .Q(d_ff_1_q), .en(1'b1));  // open: Qn, preset, reset
endmodule

module tastiera_schema (
  input  in_1,
  input  in_2,
  input  in_3,
  input  in_4,
  input  in_5,
  input  [31:0] in_6,
  output [31:0] out_7,
  output INTERRUPT
);

  wire or_1_out;
  wire [6:0] keyboard_1_data;

  GENERIC_INTERFACE generic_interface_1 (
    .in_2({{25{1'b0}}, keyboard_1_data}), .in_5(or_1_out), .out_11(out_7), .in_10(in_6), .CS(in_4));  // open: BUFOUT, out_12, in_7, in_8, out_14, in_3, IO_WR, IO_RD, out_13
  or or_1 (or_1_out, in_2, in_5);
  Keyboard keyboard_1 (.clk(in_3), .clr(in_1), .avail(INTERRUPT), .data(keyboard_1_data));  // open: re
  // Probe on keyboard_1_data
endmodule

module Compl2 (
  input  [25:0] in_1,
  output [31:0] out_2
);

  wire adder_1_cout;
  wire [25:0] not_1_out;
  wire [25:25] adder_1_out;

  assign not_1_out = ~in_1;  // NOT_Gate not_1, 26 bits wide
  // Probe on not_1_out
  Adder #(.width(26)) adder_1 (
    .a(not_1_out), .b({26{1'b0}}), .out({adder_1_out[25], out_2[24:0]}), .cin(1'b1), .cout(adder_1_cout));
  // Probe on adder_1_cout
  // Probe on {adder_1_out[25], out_2[24:0]}
  Multiplexer #(.width(7)) multiplexer_1 (
    .in0({7{1'b0}}), .in1({7{1'b1}}), .out(out_2[31:25]), .sel(adder_1_out[25]));  // open: en
endmodule
