// Logisim project CPU.circ as structural Verilog: 9 circuits, main circuit cpu_main
module system (
  input  in_1,
  input  in_2
);

  wire ck, cpu_main_1_p4, cpu_main_1_p5, cpu_main_1_p6, cpu_main_1_p7, cs1, cs2, cs_io_1, cs_io_2, cs_io_3,
       cs_io_4, cs_io_5, cs_io_6, IR1, keyboard_1_avail, keyboard_interface_1_kb_ck,
       keyboard_interface_1_kb_en, n7_segment_display_1_p1, n7_segment_display_3_p1,
       output_interface_1_out_6, output_interface_1_out_7, output_interface_1_out_8, output_interface_1_u0,
       output_interface_2_out_6, output_interface_2_out_7, output_interface_2_out_8,
       output_interface_2_out_9, output_interface_2_out_10, output_interface_2_out_11, output_interface_2_u0,
       output_interface_2_u7, ram_adapter_1_ram_ck, ram_adapter_1_ram_oe, ram_adapter_1_ram_we, rgbled_1_p7,
       tty_interface_1_tty_ck, tty_interface_1_tty_res, tty_interface_1_tty_wen;
  wire [3:0] cpu_main_1_p11;
  wire [6:0] keyboard_1_data, tty_interface_1_tty_data_in;
  wire [9:0] ram_adapter_1_ram_addr, rom_adapter_1_rom_add;
  wire [31:0] cpu_main_1_p8, cpu_main_1_p9, cpu_main_1_p10, pc, ram_1_dout, ram_adapter_1_ram_datatowr,
       rom_1_data;

  Clock clock_1 (.out(ck));
  ROM #(.addrWidth(10), .dataWidth(32)) rom_1 (.addr(rom_adapter_1_rom_add), .data(rom_1_data));
  RAM #(.addrWidth(10), .asyncread("true"), .dataWidth(32)) ram_1 (
    .addr(ram_adapter_1_ram_addr), .we(ram_adapter_1_ram_we), .oe(ram_adapter_1_ram_oe),
    .clk(ram_adapter_1_ram_ck), .din(ram_adapter_1_ram_datatowr), .dout(ram_1_dout));
  // _7_Segment_Display 7_segment_display_1: pin names not known; wires that end beside it: n7_segment_display_1_p1, n7_segment_display_1_p1
  // BCD_to_7_Segment_decoder bcd_to_7_segment_decoder_1: pin names not known
  // Binary_to_BCD_converter binary_to_bcd_converter_1: pin names not known; wires that end beside it: pc[8:0]
  // cpu_main cpu_main_1: pin names not known; wires that end beside it: in_1, ck, pc, cpu_main_1_p4, cpu_main_1_p5, cpu_main_1_p6, cpu_main_1_p7, cpu_main_1_p8, cpu_main_1_p9, cpu_main_1_p10, cpu_main_1_p11
  LED led_1 (.in(cpu_main_1_p4));
  LED led_2 (.in(cpu_main_1_p6));
  _7_Segment_Display u_7_segment_display_2 ();  // open: g, f, a, b, e, d, c, dp
  // _7_Segment_Display 7_segment_display_3: pin names not known; wires that end beside it: n7_segment_display_3_p1, n7_segment_display_3_p1
  // BCD_to_7_Segment_decoder bcd_to_7_segment_decoder_2: pin names not known
  // BCD_to_7_Segment_decoder bcd_to_7_segment_decoder_3: pin names not known; wires that end beside it: cpu_main_1_p5, cpu_main_1_p7, cpu_main_1_p8
  rom_adapter rom_adapter_1 (
    .address(cpu_main_1_p8), .cmd(cpu_main_1_p11), .rom_data(rom_1_data), .cs(cs1),
    .rom_add(rom_adapter_1_rom_add), .data(cpu_main_1_p10));
  ram_adapter ram_adapter_1 (
    .address(cpu_main_1_p8), .cmd(cpu_main_1_p11), .cs(cs2), .data_to_write(cpu_main_1_p9),
    .ram_ck({ck, ram_adapter_1_ram_ck}), .ram_datatord(ram_1_dout), .ram_addr(ram_adapter_1_ram_addr),
    .ram_we(ram_adapter_1_ram_we), .ram_oe(ram_adapter_1_ram_oe), .ram_datatowr(ram_adapter_1_ram_datatowr),
    .data_to_read(cpu_main_1_p10));
  // cs_memory cs_mem: pin names not known; wires that end beside it: cpu_main_1_p9, cpu_main_1_p10, cpu_main_1_p11, cpu_main_1_p8, cs1, cs2
  cs_io cs_inout (
    .address(cpu_main_1_p8), .cs_peripheral_1(cs_io_1), .out_3(cs_io_2), .out_4(cs_io_3), .out_5(cs_io_4),
    .out_6(cs_io_5), .out_7(cs_io_6));  // open: out_8, out_9, out_10, out_11, out_12, out_13, out_14, out_15, out_16, cs_peripheral_16
  TTY #(.cols(64), .rows(16)) tty_1 (
    .data(tty_interface_1_tty_data_in), .clk(tty_interface_1_tty_ck), .we(tty_interface_1_tty_wen),
    .clr(tty_interface_1_tty_res));
  // RGBLED rgbled_1: pin names not known; wires that end beside it: cpu_main_1_p5, cpu_main_1_p7, cpu_main_1_p8, cpu_main_1_p9, cpu_main_1_p10, cpu_main_1_p11, rgbled_1_p7
  tty_interface tty_interface_1 (
    .cmd(cpu_main_1_p11), .CS(cs_io_5), .wdata(cpu_main_1_p9), .CK(ck), .tty_wen(tty_interface_1_tty_wen),
    .tty_data_in(tty_interface_1_tty_data_in), .tty_ck(tty_interface_1_tty_ck),
    .tty_res(tty_interface_1_tty_res));
  pic_main pic_main_1 (
    .IR0(IR1), .in_8(in_2), .in_9(1'b0), .in_10(1'b0), .in_11(1'b0), .in_12(1'b0), .in_13(1'b0), .IR7(1'b0),
    .not_INTA(cpu_main_1_p7), .cmd(cpu_main_1_p11), .addr(cpu_main_1_p8), .wdata(cpu_main_1_p9),
    .cs(cs_io_2), .CK(ck), .rdata(cpu_main_1_p10), .ready(rgbled_1_p7), .INT(cpu_main_1_p5));
  Keyboard keyboard_1 (
    .clk(keyboard_interface_1_kb_ck), .re(keyboard_interface_1_kb_en), .avail(keyboard_1_avail),
    .data(keyboard_1_data));  // open: clr
  keyboard_interface keyboard_interface_1 (
    .cmd(cpu_main_1_p11), .ck(ck), .CS(cs_io_6), .kb_int(keyboard_1_avail), .kb_data(keyboard_1_data),
    .kb_ck(keyboard_interface_1_kb_ck), .kb_en(keyboard_interface_1_kb_en), .\int (IR1),
    .out_8(cpu_main_1_p10));
  output_interface output_interface_1 (
    .cmd(cpu_main_1_p11), .wdata(cpu_main_1_p9), .cs(cs_io_3), .ck(ck), .U0(output_interface_1_u0),
    .out_6(output_interface_1_out_6), .out_7(output_interface_1_out_7), .out_8(output_interface_1_out_8),
    .out_9(output_interface_1_out_8), .out_10(output_interface_1_out_8), .out_11(output_interface_1_out_8),
    .U7(output_interface_1_out_8));
  // RGBLED rgbled_2: pin names not known; wires that end beside it: output_interface_1_out_7, output_interface_1_out_6, output_interface_1_u0
  LedBar ledbar_1 (
    .led0(output_interface_2_u7), .led1(output_interface_2_out_11), .led2(output_interface_2_out_10),
    .led3(output_interface_2_out_9), .led4(output_interface_2_out_8), .led5(output_interface_2_out_7),
    .led6(output_interface_2_out_6), .led7(output_interface_2_u0));
  output_interface output_interface_2 (
    .cmd(cpu_main_1_p11), .wdata(cpu_main_1_p9), .cs(cs_io_4), .ck(ck), .U0(output_interface_2_u0),
    .out_6(output_interface_2_out_6), .out_7(output_interface_2_out_7), .out_8(output_interface_2_out_8),
    .out_9(output_interface_2_out_9), .out_10(output_interface_2_out_10), .out_11(output_interface_2_out_11),
    .U7(output_interface_2_u7));
  // also tied to GND on the sheet: output_interface_1_out_8

  // Notes on the sheet:
  //   Program
  //   Counter
  //   Value
  //   contents of rom_1 (hex, n*v repeats v):
  //   c0000000 281e0800 28010013 b4010100 28010000 b4010101 28010001 b4010101 bc000000 54010400 6820fffe
  //   50000400 54010401 b4010400 5ffffffa a03e0000 b8010500 50010401 28010001 50010400 28010020 b4010100
  //   a43e0000 c7c00000 744*0 f
  //   rd
  //   wr
  //   Rom-program (add: 0000 0000h)
  //   Ram-variables/stack (add: 0000 0400h)
  //   pic ready
  //   status led
  //   led_7
  //   led_0
endmodule

module cpu_main (
  input  CK,
  input  \int ,
  input  ready,
  input  [31:0] din,
  output [31:0] pc_value,
  output not_INTA,
  output [31:0] address,
  output [31:0] dout,
  output [3:0] cmd,
  output led_rd,
  output led_wr
);

  wire end_inta, udc_main_1_cost_enable, udc_main_1_rd1, udc_main_1_rd2, udc_main_1_u, udc_main_1_wr;
  wire [2:0] dp_main_1_flags, udc_main_1_cond;
  wire [4:0] udc_main_1_out_13, udc_main_1_out_15, udc_main_1_out_17;
  wire [31:0] multiplexer_1_out, udc_main_1_cost, udc_main_1_reg_ctrl;

  udc_main udc_main_1 (
    .ZF(dp_main_1_flags[0]), .INT(\int ), .ir_in(din), .CK(CK), .ready(ready), .U(udc_main_1_u),
    .cond(udc_main_1_cond), .cost_enable(udc_main_1_cost_enable), .cmd_signals(cmd),
    .reg_ctrl(udc_main_1_reg_ctrl), .RD1(udc_main_1_rd1), .out_13(udc_main_1_out_13), .RD2(udc_main_1_rd2),
    .out_15(udc_main_1_out_15), .WR(udc_main_1_wr), .end_inta(end_inta), .out_17(udc_main_1_out_17),
    .COST(udc_main_1_cost), .not_INTA(not_INTA));
  or or_1 (led_rd, cmd[0], cmd[2]);
  or or_2 (led_wr, cmd[1], cmd[3]);
  dp_main dp_main_1 (
    .WR(udc_main_1_wr), .c_en(udc_main_1_reg_ctrl[13:11]), .Waddr(udc_main_1_out_17),
    .addrMux(udc_main_1_reg_ctrl[30]), .cost_en(udc_main_1_cost_enable), .RD1(udc_main_1_rd1),
    .Raddr1(udc_main_1_out_13), .a_en(udc_main_1_reg_ctrl[7:5]), .b_en(udc_main_1_reg_ctrl[10:8]),
    .Raddr2(udc_main_1_out_15), .RD2(udc_main_1_rd2), .pc_en(udc_main_1_reg_ctrl[16:14]),
    .temp_en(udc_main_1_reg_ctrl[19:17]), .iar_en(udc_main_1_reg_ctrl[22:20]),
    .mar_en(udc_main_1_reg_ctrl[25:23]), .mdr_en(udc_main_1_reg_ctrl[28:26]), .cost_in(udc_main_1_cost),
    .U(udc_main_1_u), .cond(udc_main_1_cond), .alu_ctrl(udc_main_1_reg_ctrl[4:0]),
    .dataMux(udc_main_1_reg_ctrl[29]), .CK(CK), .data_in(multiplexer_1_out), .address_out(address),
    .data_out(dout), .pc_state(pc_value), .flags(dp_main_1_flags));
  Multiplexer #(.width(32)) multiplexer_1 (.in0(din), .in1({24'h3, din[7:0]}), .out(multiplexer_1_out), .sel(end_inta));

  // Notes on the sheet:
  //   #Led on when a mem operation is performed
  //   ivt_address
endmodule

module cs_memory (
  input  [31:0] address,
  output cs_mem_1,
  output out_3,
  output out_4,
  output out_5,
  output out_6,
  output out_7,
  output out_8,
  output out_9,
  output out_10,
  output out_11,
  output out_12,
  output out_13,
  output out_14,
  output out_15,
  output out_16,
  output cs_mem_16
);

  Decoder #(.enable("false"), .select(4)) decoder_1 (
    .out0(cs_mem_1), .out1(out_3), .out2(out_4), .out3(out_5), .out4(out_6), .out5(out_7), .out6(out_8),
    .out7(out_9), .out8(out_10), .out9(out_11), .out10(out_12), .out11(out_13), .out12(out_14),
    .out13(out_15), .out14(out_16), .out15(cs_mem_16), .sel(address[13:10]));

  // Notes on the sheet:
  //   i=10
endmodule

module cs_io (
  input  [31:0] address,
  output cs_peripheral_1,
  output out_3,
  output out_4,
  output out_5,
  output out_6,
  output out_7,
  output out_8,
  output out_9,
  output out_10,
  output out_11,
  output out_12,
  output out_13,
  output out_14,
  output out_15,
  output out_16,
  output cs_peripheral_16
);

  Decoder #(.enable("false"), .select(4)) decoder_1 (
    .out0(cs_peripheral_1), .out1(out_3), .out2(out_4), .out3(out_5), .out4(out_6), .out5(out_7),
    .out6(out_8), .out7(out_9), .out8(out_10), .out9(out_11), .out10(out_12), .out11(out_13), .out12(out_14),
    .out13(out_15), .out14(out_16), .out15(cs_peripheral_16), .sel(address[11:8]));

  // Notes on the sheet:
  //   i=8
endmodule

module rom_adapter (
  input  cs,
  input  [3:0] cmd,
  input  [31:0] rom_data,
  input  [31:0] address,
  output [9:0] rom_add,
  output [31:0] data
);

  wire add_en;

  Multiplexer #(.width(10)) multiplexer_1 (.in0({10{1'b0}}), .in1(address[9:0]), .out(rom_add), .sel(add_en));
  and and_1 (add_en, cs, cmd[0]);
  assign data = add_en ? rom_data : 32'bz;  // Controlled_Buffer controlled_buffer_1

  // Notes on the sheet:
  //   memrd
endmodule

module ram_adapter (
  input  cs,
  input  [3:0] cmd,
  input  ck,
  input  [31:0] data_to_write,
  input  [31:0] ram_datatord,
  input  [31:0] address,
  output [9:0] ram_addr,
  output ram_we,
  output ram_oe,
  output ram_ck,
  output [31:0] ram_datatowr,
  output [31:0] data_to_read
);

  wire add_en;

  Multiplexer #(.width(10)) multiplexer_1 (.in0({10{1'b0}}), .in1(address[9:0]), .out(ram_addr), .sel(add_en));
  and and_1 (ram_oe, cs, cmd[0]);
  and and_2 (ram_we, cs, cmd[1]);
  or or_1 (add_en, ram_oe, ram_we);
  assign ram_datatowr = ram_we ? data_to_write : 32'bz;  // Controlled_Buffer controlled_buffer_1
  RAM #(.addrWidth(10), .asyncread("true"), .dataWidth(32)) ram_1 ();  // open: addr, we, oe, clk, din, dout
  assign data_to_read = ram_oe ? ram_datatord : 32'bz;  // Controlled_Buffer controlled_buffer_2

  assign ram_ck = ck;

  // Notes on the sheet:
  //   memrd
endmodule

module output_interface (
  input  cs,
  input  [3:0] cmd,
  input  ck,
  input  [31:0] wdata,
  output U0,
  output out_6,
  output out_7,
  output out_8,
  output out_9,
  output out_10,
  output out_11,
  output U7
);

  wire and_1_out;

  and and_1 (and_1_out, cs, cmd[3]);
  Register register_1 (
    .D(wdata[7:0]), .en(and_1_out), .Q({U7, out_11, out_10, out_9, out_8, out_7, out_6, U0}), .clk(ck));  // open: clr

  // Notes on the sheet:
  //   IO-WR
endmodule

module tty_interface (
  input  CK,
  input  [31:0] wdata,
  input  [3:0] cmd,
  input  CS,
  output [6:0] tty_data_in,
  output tty_ck,
  output tty_wen,
  output tty_res
);

  and and_1 (tty_wen, cmd[3], CS);

  assign tty_ck = CK;
  assign tty_data_in = wdata[6:0];
  assign tty_res = 1'b0;
endmodule

module keyboard_interface (
  input  [6:0] kb_data,
  input  ck,
  input  kb_int,
  input  [3:0] cmd,
  input  CS,
  output kb_ck,
  output kb_en,
  output [31:0] out_8,
  output \int 
);

  wire not_1_out;

  and and_1 (kb_en, cmd[2], CS);
  not not_1 (not_1_out, kb_en);
  and and_2 (\int , not_1_out, kb_int);
  assign out_8 = kb_en ? {{25{1'b0}}, kb_data} : 32'bz;  // Controlled_Buffer controlled_buffer_1

  assign kb_ck = ck;
endmodule
