// Logisim project Udc.circ as structural Verilog: 9 circuits, main circuit udc_main
module udc_main (
  input  CK,
  input  INT,
  input  ZF,
  input  ready,
  input  [31:0] ir_in,
  output [31:0] reg_ctrl,
  output not_INTA,
  output end_inta,
  output [3:0] cmd_signals,
  output U,
  output [2:0] cond,
  output RD1,
  output [4:0] out_13,
  output RD2,
  output [4:0] out_15,
  output WR,
  output [4:0] out_17,
  output [31:0] COST,
  output cost_enable
);

  wire and_1_out, ask_ready, branch_control_1_force_stop, counter_control_1_ck_counter,
       counter_control_1_count, counter_control_1_cycles_finished, counter_control_1_reset_counter, d_ff_1_q,
       ien, ir_wr, multiplexer_1_out, not_1_out, not_2_out, or_1_out, or_2_out, we_ien;
  wire [1:0] master_control_1_q0;
  wire [2:0] branch, r30_en;
  wire [3:0] counter_1_q, multiplexer_4_out, val;
  wire [15:0] multiplexer_2_out, multiplexer_3_out, rom_1_data;
  wire [25:0] register_main_1_u1;
  wire [31:0] alu_main_1_u, register_main_1_state, register_main_1_u2;
  wire [31:26] register_main_1_u1_2;
  wire [63:39] rom_2_data;

  Multiplexer multiplexer_1 (.in0(d_ff_1_q), .in1(ien), .out(multiplexer_1_out), .sel(we_ien));
  ROM #(.addrWidth(6), .dataWidth(16)) rom_1 (.addr(register_main_1_u1_2), .data(rom_1_data));
  D_Flip_Flop d_ff_1 (.clk(CK), .D(multiplexer_1_out), .Q(d_ff_1_q));  // open: Qn, preset, reset
  or or_1 (or_1_out, val[0], val[1], val[2], val[3], master_control_1_q0[0], master_control_1_q0[1]);
  not not_1 (not_1_out, or_1_out);
  and and_1 (and_1_out, INT, d_ff_1_q, not_1_out);
  register_main register_main_1 (
    .D(ir_in), .CK(CK), .reg_ctrl({2'b01, ir_wr}), .state(register_main_1_state),
    .U1({register_main_1_u1_2, register_main_1_u1}), .U2(register_main_1_u2));
  // Probe on register_main_1_state
  Multiplexer #(.width(16)) multiplexer_2 (.in0(16'h1), .in1({16{1'b0}}), .out(multiplexer_2_out), .sel(and_1_out));
  master_control master_control_1 (
    .CK(CK), .I2(1'b0), .I1(and_1_out), .I0(counter_control_1_cycles_finished), .q1(master_control_1_q0[1]),
    .q0(master_control_1_q0[0]));
  Multiplexer #(.select(2), .width(16)) multiplexer_3 (
    .in0(multiplexer_2_out), .in1(rom_1_data), .in2(16'h27), .out(multiplexer_3_out),
    .sel(master_control_1_q0));  // open: in3
  not not_2 (not_2_out, branch_control_1_force_stop);
  Multiplexer #(.width(4)) multiplexer_4 (
    .in0(4'b0000), .in1(multiplexer_3_out[3:0]), .out(multiplexer_4_out), .sel(not_2_out));
  counter_control counter_control_1 (
    .in_1(CK), .n_cycles(multiplexer_4_out), .ready(or_2_out), .ask_ready(ask_ready),
    .Q_counter(counter_1_q), .count(counter_control_1_count), .ck_counter(counter_control_1_ck_counter),
    .reset_counter(counter_control_1_reset_counter), .current_cycle(val),
    .cycles_finished(counter_control_1_cycles_finished));
  Counter #(.max('hf), .width(4)) counter_1 (
    .count(counter_control_1_count), .Q(counter_1_q), .clk(counter_control_1_ck_counter),
    .clr(counter_control_1_reset_counter));  // open: load, D, carry, up
  or or_2 (or_2_out, ready, end_inta);
  not_inta_wave_gen not_inta_wave_gen_1 (
    .end_inta(end_inta), .CK(CK), .start_inta(rom_2_data[53]), .not_INTA(not_INTA));
  instruction_registers_manager instruction_registers_manager_1 (
    .RD1(rom_2_data[41]), .RD2(rom_2_data[40]), .WR(rom_2_data[39]),
    .instruction_type(multiplexer_3_out[15:14]), .ir_fields(register_main_1_u1), .unsigned_cost(U),
    .r30_en(r30_en), .rs2_as_dest(rom_2_data[50]), .rs1_as_dest(rom_2_data[51]), .cost(COST), .rd(out_17),
    .rs2(out_15), .rs1(out_13), .out_10(RD1), .out_11(RD2), .out_12(WR));
  branch_control branch_control_1 (
    .beqz_enable(branch[0]), .bneqz(branch[1]), .ZF(ZF), .force_stop(branch_control_1_force_stop));
  alu_main alu_main_1 (
    .alu_ctrl(3'b000), .A({{22{1'b0}}, multiplexer_3_out[13:4]}), .B({{28{1'b0}}, val}), .M(1'b1), .CI(1'b0),
    .U(alu_main_1_u));  // open: out_flags
  ROM #(.addrWidth(10), .dataWidth(64)) rom_2 (
    .addr(alu_main_1_u[9:0]),
    .data({rom_2_data[63:57], r30_en, rom_2_data[53], ask_ready, rom_2_data[51:50], ir_wr, branch, U, cond, rom_2_data[41:39], cost_enable, cmd_signals, ien, we_ien, reg_ctrl}));
  // also tied to GND on the sheet: {register_main_1_u2[0], register_main_1_u2[1], register_main_1_u2[2], register_main_1_u2[3], register_main_1_u2[4], register_main_1_u2[5], register_main_1_u2[6], register_main_1_u2[7], register_main_1_u2[8], register_main_1_u2[9], register_main_1_u2[10], register_main_1_u2[11], register_main_1_u2[12], register_main_1_u2[13], register_main_1_u2[14], register_main_1_u2[15], register_main_1_u2[16], register_main_1_u2[17], register_main_1_u2[18], register_main_1_u2[19], register_main_1_u2[20], register_main_1_u2[21], register_main_1_u2[22], register_main_1_u2[23], register_main_1_u2[24], register_main_1_u2[25], register_main_1_u2[26], register_main_1_u2[27], register_main_1_u2[28], register_main_1_u2[29], register_main_1_u2[30], register_main_1_u2[31], alu_main_1_u[10], alu_main_1_u[11], alu_main_1_u[12], alu_main_1_u[13], alu_main_1_u[14], alu_main_1_u[15], alu_main_1_u[16], alu_main_1_u[17], alu_main_1_u[18], alu_main_1_u[19], alu_main_1_u[20], alu_main_1_u[21], alu_main_1_u[22], alu_main_1_u[23], alu_main_1_u[24], alu_main_1_u[25], alu_main_1_u[26], alu_main_1_u[27], alu_main_1_u[28], alu_main_1_u[29], alu_main_1_u[30], alu_main_1_u[31]}

  // Notes on the sheet:
  //   contents of rom_1 (hex, n*v repeats v):
  //   a1 c1 8*0 40e1 4101 8*0 4122 4153 190 c1a0 0 0 41b1 41d1 1f1 11*0 4212 4244 4293 42d3 4313 4392 4353
  //   3c0 3d0 3e3
  //   COP
  //   #evaluate interrupt only in state 0
  //   ir[25...0]
  //   istr_type
  //   start_addr
  //   end inta
  //   inta wavegen
  //   start inta
  //   contents of rom_2 (hex, n*v repeats v):
  //   2000440010000 3000000c13a 80000000000020 800853 40000004009000 811000000 30000024000000 8800000
  //   425000000 108004000 c50 8000001000 c59 8000001000 4000000850 4008000001000 4000000859 4008000001000
  //   4000800050 4000200 811000000 4000800050 425000000 8000800 4008000001000 4040 400000c010 400000000052
  //   400000c010 c00000000052 400000c010 100000000c59 8000001000 800a13 4008004001040 811000000 800200
  //   425000000 a1a 4008008001800 8008000001000 4008000 400000c010 800a13 4008811001000 4008000 4040
  //   800a13 4008811001000 800200 425000000 a1a 4008008005000 4000800050 1025000000 8000800 4008000001000
  //   4000800050 4000200 2011000000 300000000 100000000 800040 425000000 85a 8008308005000
  //   memrd
  //   memwr
  //   iord
  //   iowr
endmodule

module master_control (
  input  I2,
  input  I1,
  input  I0,
  input  CK,
  output q1,
  output q0
);

  wire and_1_out, and_2_out, and_3_out, and_4_out, not_1_out, not_2_out, not_3_out, not_4_out, not_5_out,
       not_6_out, not_7_out, not_8_out, not_9_out, not_10_out, not_11_out, or_1_out, or_2_out;

  not not_1 (not_1_out, I2);
  not not_2 (not_2_out, I1);
  not not_3 (not_3_out, q1);
  not not_4 (not_4_out, q0);
  not not_5 (not_5_out, I2);
  not not_6 (not_6_out, I0);
  not not_7 (not_7_out, I2);
  not not_8 (not_8_out, q1);
  not not_9 (not_9_out, q0);
  not not_10 (not_10_out, I2);
  not not_11 (not_11_out, I0);
  and and_1 (and_1_out, not_1_out, not_2_out, not_3_out, not_4_out, I0);
  and and_2 (and_2_out, not_5_out, q0, not_6_out);
  and and_3 (and_3_out, not_7_out, not_8_out, not_9_out, I1);
  and and_4 (and_4_out, not_10_out, q1, not_11_out);
  or or_1 (or_1_out, and_1_out, and_2_out);
  or or_2 (or_2_out, and_3_out, and_4_out);
  D_Flip_Flop d_ff_1 (.clk(CK), .D(or_1_out), .Q(q0));  // open: Qn, preset, reset
  D_Flip_Flop d_ff_2 (.clk(CK), .D(or_2_out), .Q(q1));  // open: Qn, preset, reset

  // Notes on the sheet:
  //   q0
  //   q1
  //   Q0
  //   Q1
endmodule

module compare_counter (
  input  [3:0] in_1,
  input  [3:0] in_2,
  output out_3
);

  wire or_1_out;
  wire [3:0] xor_1_out;

  assign xor_1_out = in_1 ^ in_2;  // XOR_Gate xor_1, 4 bits wide
  or or_1 (or_1_out, xor_1_out[0], xor_1_out[1], xor_1_out[2], xor_1_out[3]);
  not not_1 (out_3, or_1_out);
endmodule

module counter_control (
  input  in_1,
  input  ask_ready,
  input  [3:0] Q_counter,
  input  ready,
  input  [3:0] n_cycles,
  output [3:0] current_cycle,
  output count,
  output ck_counter,
  output reset_counter,
  output cycles_finished
);

  wire [3:0] adder_1_out;

  Multiplexer multiplexer_1 (.in0(1'b1), .in1(ready), .out(count), .sel(ask_ready));
  Adder #(.width(4)) adder_1 (.a(n_cycles), .b(4'b0000), .out(adder_1_out), .cin(1'b1));  // open: cout
  Counter #(.max('hf), .width(4)) counter_1 ();  // open: load, D, count, Q, carry, up, clk, clr
  compare_counter compare_counter_1 (.in_1(Q_counter), .in_2(adder_1_out), .out_3(reset_counter));
  compare_counter compare_counter_2 (.in_1(Q_counter), .in_2(n_cycles), .out_3(cycles_finished));

  assign ck_counter = in_1;
  assign current_cycle = Q_counter;

  // Other names for the same wires on the sheet: ck = in_1
endmodule

module instruction_registers_manager (
  input  RD1,
  input  RD2,
  input  WR,
  input  [25:0] ir_fields,
  input  [1:0] instruction_type,
  input  unsigned_cost,
  input  rs2_as_dest,
  input  rs1_as_dest,
  input  [2:0] r30_en,
  output out_10,
  output out_11,
  output out_12,
  output [31:0] cost,
  output [4:0] rd,
  output [4:0] rs2,
  output [4:0] rs1
);

  wire and_1_out, and_2_out, and_3_out, and_4_out, and_5_out, i, j, r;
  wire [31:0] immediate_bit_extender_1_out_3, jump_bit_extender_1_out_2;

  Decoder #(.enable("false"), .select(2)) decoder_1 (
    .out0(r), .out1(i), .out3(j), .sel(instruction_type));  // open: out2
  and and_1 (and_1_out, r, WR);
  and and_2 (and_2_out, r, RD2);
  assign rd = and_1_out ? ir_fields[15:11] : 5'bz;  // Controlled_Buffer controlled_buffer_1
  assign rs2 = and_2_out ? ir_fields[20:16] : 5'bz;  // Controlled_Buffer controlled_buffer_2
  assign rs1 = and_3_out ? ir_fields[25:21] : 5'bz;  // Controlled_Buffer controlled_buffer_3
  jump_bit_extender jump_bit_extender_1 (.in_1(ir_fields), .out_2(jump_bit_extender_1_out_2));
  and and_3 (and_3_out, r, RD1);
  assign cost = j ? jump_bit_extender_1_out_2 : 32'bz;  // Controlled_Buffer controlled_buffer_4
  immediate_bit_extender immediate_bit_extender_1 (
    .in_2(ir_fields[15:0]), .U(unsigned_cost), .out_3(immediate_bit_extender_1_out_3));
  assign cost = i ? immediate_bit_extender_1_out_3 : 32'bz;  // Controlled_Buffer controlled_buffer_5
  assign rs2 = and_4_out ? ir_fields[20:16] : 5'bz;  // Controlled_Buffer controlled_buffer_6
  assign rs1 = and_5_out ? ir_fields[25:21] : 5'bz;  // Controlled_Buffer controlled_buffer_7
  and and_4 (and_4_out, i, RD2);
  and and_5 (and_5_out, i, RD1);
  assign rd = rs2_as_dest ? ir_fields[20:16] : 5'bz;  // Controlled_Buffer controlled_buffer_8
  assign rd = rs1_as_dest ? ir_fields[25:21] : 5'bz;  // Controlled_Buffer controlled_buffer_9
  assign rd = r30_en[0] ? 5'b11110 : 5'bz;  // Controlled_Buffer controlled_buffer_10
  assign rs2 = r30_en[2] ? 5'b11110 : 5'bz;  // Controlled_Buffer controlled_buffer_11
  assign rs1 = r30_en[1] ? 5'b11110 : 5'bz;  // Controlled_Buffer controlled_buffer_12
  or or_1 (out_10, r30_en[1], RD1);
  or or_2 (out_11, RD2, r30_en[2]);
  or or_3 (out_12, WR, r30_en[0]);

  // Notes on the sheet:
  //   IR[25...0]
  //   rd
  //   rs2
  //   rs1
  //   jump cost signed
  //   cost
  //   rs2
  //   rs1
  //   bit extender
  //   R30
  //   wr
  //   oe1
  //   oe2
endmodule

module immediate_bit_extender (
  input  U,
  input  [15:0] in_2,
  output [31:0] out_3
);

  Multiplexer #(.width(32)) multiplexer_1 (
    .in0({{17{in_2[15]}}, in_2[14:0]}), .in1({{16{1'b0}}, in_2}), .out(out_3), .sel(U));
endmodule

module jump_bit_extender (
  input  [25:0] in_1,
  output [31:0] out_2
);


  assign out_2 = {{7{in_1[25]}}, in_1[24:0]};
endmodule

module branch_control (
  input  beqz_enable,
  input  bneqz,
  input  ZF,
  output force_stop
);

  wire multiplexer_1_out, not_1_out;

  not not_1 (not_1_out, ZF);
  Multiplexer multiplexer_1 (.in0(not_1_out), .in1(ZF), .out(multiplexer_1_out), .sel(bneqz));
  Multiplexer multiplexer_2 (.in0(1'b0), .in1(multiplexer_1_out), .out(force_stop), .sel(beqz_enable));
endmodule

module not_inta_wave_gen (
  input  CK,
  input  start_inta,
  output not_INTA,
  output end_inta
);

  wire not_1_out;
  wire [1:0] counter_1_q;

  not not_1 (not_1_out, start_inta);
  Counter #(.max('h3), .width(2)) counter_1 (
    .Q(counter_1_q), .clk(CK), .clr(not_1_out));  // open: load, D, count, carry, up
  Multiplexer #(.select(2)) multiplexer_1 (
    .in0(1'b1), .in1(1'b0), .in2(1'b1), .in3(1'b0), .out(not_INTA), .sel(counter_1_q));
  and and_1 (end_inta, counter_1_q[0], counter_1_q[1]);
endmodule
