// Logisim project 32BitRegister.circ as structural Verilog: 1 circuit, main circuit register_main
module register_main (
  input  [31:0] D,
  input  CK,
  input  [2:0] reg_ctrl,
  output [31:0] state,
  output [31:0] U1,
  output [31:0] U2
);

  wire not_1_out;
  wire [31:0] multiplexer_1_out;

  Multiplexer #(.width(32)) multiplexer_1 (.in0(D), .in1(state), .out(multiplexer_1_out), .sel(not_1_out));
  not not_1 (not_1_out, reg_ctrl[0]);
  Register #(.width(32)) register_1 (.D(multiplexer_1_out), .Q(state), .clk(CK));  // open: en, clr
  assign U1 = reg_ctrl[1] ? state : 32'bz;  // Controlled_Buffer controlled_buffer_1
  assign U2 = reg_ctrl[2] ? state : 32'bz;  // Controlled_Buffer controlled_buffer_2

  // Notes on the sheet:
  //   we
  //   oe2
  //   oe1
endmodule
