// Logisim project 8BitRegister.circ as structural Verilog: 1 circuit, main circuit eightbit_register_main
module eightbit_register_main (
  input  [7:0] D,
  input  CK,
  input  [2:0] reg_ctrl,
  output [7:0] state,
  output [7:0] U1,
  output [7:0] U2
);

  wire not_1_out;
  wire [7:0] multiplexer_1_out;

  Multiplexer #(.width(8)) multiplexer_1 (.in0(D), .in1(state), .out(multiplexer_1_out), .sel(not_1_out));
  Register register_1 (.D(multiplexer_1_out), .Q(state), .clk(CK));  // open: en, clr
  not not_1 (not_1_out, reg_ctrl[0]);
  assign U1 = reg_ctrl[1] ? state : 8'bz;  // Controlled_Buffer controlled_buffer_1
  assign U2 = reg_ctrl[2] ? state : 8'bz;  // Controlled_Buffer controlled_buffer_2
endmodule
