// Logisim project PIC.circ as structural Verilog: 8 circuits, main circuit pic_main
module pic_main (
  input  cs,
  input  CK,
  input  [3:0] cmd,
  input  [31:0] addr,
  input  [31:0] wdata,
  input  not_INTA,
  input  IR0,
  input  in_8,
  input  in_9,
  input  in_10,
  input  in_11,
  input  in_12,
  input  in_13,
  input  IR7,
  output [31:0] rdata,
  output ready,
  output INT
);

  wire aeoi, and_1_out, and_2_out, and_3_out, and_4_out, and_5_out, and_6_out, ck_t, decoder_1_out0,
       decoder_1_out1, decoder_1_out2, EOI, iri_rst, ltim, not_1_out, not_2_out, pri_flag, pri_rst,
       priority_resolution_1_pri_flag, priority_resolution_3_pri_flag;
  wire [0:0] or_1_out;
  wire [1:0] icw_controller_1_q0, irr_mux, isr_mux;
  wire [2:0] adder_1_out, inta_controller_mealy_1_u, IRR_en, ISR_en, priority_encoder_1_out, register_2_q;
  wire [4:0] addr_msb;
  wire [7:0] controlled_buffer_2_out, eightbit_register_main_1_u1, eightbit_register_main_1_u2,
       eightbit_register_main_2_state, iri_preelab_1_iri, irrst, masked_bits, multiplexer_1_out,
       multiplexer_2_out, priority_resolution_1_u, priority_resolution_2_u, priority_resolution_3_u,
       register_3_q;
  wire [7:1] register_1_q;
  wire [15:12] rom_1_data;

  Clock clock_1 (.out(ck_t));
  and and_1 (and_1_out, cs, cmd[2]);
  and and_2 (and_2_out, cs, cmd[3]);
  not not_1 (not_1_out, ltim);
  assign rdata = and_1_out ? {{24{1'b0}}, controlled_buffer_2_out} : 32'bz;  // Controlled_Buffer controlled_buffer_1
  icw_controller icw_controller_1 (
    .a0(addr[0]), .wr(and_2_out), .in_3(ck_t), .q0(icw_controller_1_q0[0]), .q1(icw_controller_1_q0[1]));
  Decoder #(.enable("false"), .select(2)) decoder_1 (
    .out0(decoder_1_out0), .out1(decoder_1_out1), .out2(decoder_1_out2), .out3(ready),
    .sel(icw_controller_1_q0));
  inta_controller_mealy inta_controller_mealy_1 (
    .I1(not_INTA), .I0(pri_flag), .CK(ck_t), .U(inta_controller_mealy_1_u));
  iri_preelab iri_preelab_1 (
    .IR0(IR0), .in_6(in_8), .in_7(in_9), .in_8(in_10), .in_10(in_11), .in_11(in_12), .in_12(in_13),
    .IR7(IR7), .masked_bits(masked_bits), .irr(irrst), .reset(iri_rst), .ck(ck_t), .fronte(not_1_out),
    .pic_ready(ready), .IRi(iri_preelab_1_iri));
  ROM #(.addrWidth(3), .dataWidth(16)) rom_1 (
    .addr(adder_1_out),
    .data({rom_1_data[15], INT, rom_1_data[13:12], iri_rst, pri_rst, isr_mux, ISR_en, IRR_en, irr_mux}));
  Adder #(.width(3)) adder_1 (.a(inta_controller_mealy_1_u), .b(3'b000), .out(adder_1_out), .cin(1'b0));  // open: cout
  // Probe on eightbit_register_main_1_u1
  and and_3 (and_3_out, and_2_out, decoder_1_out0);
  and and_4 (and_4_out, and_2_out, decoder_1_out1);
  and and_5 (and_5_out, and_2_out, decoder_1_out2);
  // Probe on eightbit_register_main_1_u2
  or or_1 (or_1_out[0], EOI, ISR_en[0]);
  Register register_1 (.D({{7{1'b0}}, wdata[0]}), .en(and_3_out), .Q({register_1_q, ltim}), .clk(ck_t));  // open: clr
  Register register_2 (
    .D({wdata[7:3], 3'b000}), .en(and_4_out), .Q({addr_msb, register_2_q}), .clk(ck_t));  // open: clr
  Register register_3 (
    .D({{6{1'b0}}, wdata[1:0]}), .en(and_5_out), .Q({register_3_q[7:2], aeoi, register_3_q[0]}), .clk(ck_t));  // open: clr
  priority_resolution priority_resolution_1 (
    .A(eightbit_register_main_1_u1), .B(eightbit_register_main_1_u1), .Reset(1'b1),
    .U(priority_resolution_1_u), .pri_flag(priority_resolution_1_pri_flag));
  priority_resolution priority_resolution_2 (
    .A(eightbit_register_main_1_u1), .B(eightbit_register_main_1_u2), .Reset(pri_rst),
    .U(priority_resolution_2_u), .pri_flag(pri_flag));
  eightbit_register_main eightbit_register_main_1 (
    .D(multiplexer_1_out), .CK(ck_t), .reg_ctrl(IRR_en), .state(irrst), .U1(eightbit_register_main_1_u1),
    .U2(eightbit_register_main_1_u2));
  Multiplexer #(.select(2), .width(8)) multiplexer_1 (
    .in0(iri_preelab_1_iri), .in1(priority_resolution_2_u), .in2(priority_resolution_1_u),
    .out(multiplexer_1_out), .sel(irr_mux));  // open: in3
  // Probe on irrst
  eightbit_register_main eightbit_register_main_2 (
    .D(multiplexer_2_out), .CK(ck_t), .reg_ctrl({ISR_en[2:1], or_1_out[0]}),
    .state(eightbit_register_main_2_state), .U1(eightbit_register_main_1_u1), .U2(eightbit_register_main_1_u2));
  Multiplexer #(.select(2), .width(8)) multiplexer_2 (
    .in0(priority_resolution_3_u), .in1(priority_resolution_2_u), .out(multiplexer_2_out), .sel(isr_mux));  // open: in2, in3
  // Probe on eightbit_register_main_2_state
  priority_resolution priority_resolution_3 (
    .A(eightbit_register_main_1_u2), .B(eightbit_register_main_1_u2), .Reset(1'b1),
    .U(priority_resolution_3_u), .pri_flag(priority_resolution_3_pri_flag));
  // Probe on priority_resolution_2_u
  // Probe on priority_resolution_1_u
  // Probe on iri_preelab_1_iri
  Priority_Encoder priority_encoder_1 (
    .in0(eightbit_register_main_1_u2[0]), .in1(eightbit_register_main_1_u2[1]),
    .in2(eightbit_register_main_1_u2[2]), .in3(eightbit_register_main_1_u2[3]),
    .in4(eightbit_register_main_1_u2[4]), .in5(eightbit_register_main_1_u2[5]),
    .in6(eightbit_register_main_1_u2[6]), .in7(eightbit_register_main_1_u2[7]), .out(priority_encoder_1_out));  // open: en_in, gs, en_out
  and and_6 (and_6_out, and_2_out, addr[0], ready);
  not not_2 (not_2_out, addr[0]);
  and and_7 (EOI, and_2_out, not_2_out, ready);
  assign controlled_buffer_2_out = rom_1_data[15] ? {addr_msb, priority_encoder_1_out} : 8'bz;  // Controlled_Buffer controlled_buffer_2
  Register IMR (.D(wdata[7:0]), .en(and_6_out), .Q(masked_bits), .clk(ck_t));  // open: clr
  // also tied to GND on the sheet: {priority_resolution_3_pri_flag, priority_resolution_1_pri_flag}

  // Notes on the sheet:
  //   bd[7...0]
  //   iord
  //   iowr
  //   ba[0]
  //   bd[7...0]
  //   contents of rom_1 (hex, n*v repeats v):
  //   8c 408c 49ae 4000 c480
  //   eoi_reset_isr
  //   reset_pri(irr)
  //   A0=1
  //   A1=1
  //   n
  //   rdata
endmodule

module icw_controller (
  input  a0,
  input  wr,
  input  in_3,
  output q0,
  output q1
);

  wire and_1_out, and_2_out, and_3_out, and_4_out, and_5_out, not_1_out, not_2_out, not_3_out, or_1_out,
       or_2_out;

  not not_1 (not_1_out, q1);
  not not_2 (not_2_out, a0);
  and and_1 (and_1_out, not_1_out, not_2_out, wr);
  and and_2 (and_2_out, q1, a0, wr);
  and and_3 (and_3_out, q0, not_3_out);
  not not_3 (not_3_out, wr);
  and and_4 (and_4_out, q1, q0);
  and and_5 (and_5_out, q0, a0, wr);
  or or_1 (or_1_out, and_5_out, q1);
  or or_2 (or_2_out, and_1_out, and_2_out, and_3_out, and_4_out);
  D_Flip_Flop d_ff_1 (.clk(in_3), .D(or_2_out), .Q(q0));  // open: Qn, preset, reset
  D_Flip_Flop d_ff_2 (.clk(in_3), .D(or_1_out), .Q(q1));  // open: Qn, preset, reset

  // Notes on the sheet:
  //   i1
  //   i0
  //   q1
  //   q0
  //   Q0
  //   Q1
endmodule

module priority_resolution (
  input  Reset,
  input  [7:0] A,
  input  [7:0] B,
  output [7:0] U,
  output pri_flag
);

  wire not_1_out, not_3_out, not_4_out, priority_encoder_1_en_out, priority_encoder_2_en_out,
       priority_encoder_3_en_out;
  wire [2:0] priority_encoder_1_out, priority_encoder_2_out, priority_encoder_3_out;
  wire [7:0] and_1_out, decoder_1_out0, decoder_2_out0, decoder_3_out0, not_2_out, or_1_out;

  Priority_Encoder priority_encoder_1 (
    .in0(A[0]), .in1(A[1]), .in2(A[2]), .in3(A[3]), .in4(A[4]), .in5(A[5]), .in6(A[6]), .in7(A[7]),
    .out(priority_encoder_1_out), .en_out(priority_encoder_1_en_out));  // open: en_in, gs
  not not_1 (not_1_out, priority_encoder_1_en_out);
  Decoder #(.select(3)) decoder_1 (
    .out0(decoder_1_out0[0]), .out1(decoder_1_out0[1]), .out2(decoder_1_out0[2]), .out3(decoder_1_out0[3]),
    .out4(decoder_1_out0[4]), .out5(decoder_1_out0[5]), .out6(decoder_1_out0[6]), .out7(decoder_1_out0[7]),
    .sel(priority_encoder_1_out), .en(not_1_out));
  Priority_Encoder priority_encoder_2 (
    .in0(A[0]), .in1(A[1]), .in2(A[2]), .in3(A[3]), .in4(A[4]), .in5(A[5]), .in6(A[6]), .in7(A[7]),
    .out(priority_encoder_2_out), .en_out(priority_encoder_2_en_out));  // open: en_in, gs
  Priority_Encoder priority_encoder_3 (
    .in0(B[0]), .in1(B[1]), .in2(B[2]), .in3(B[3]), .in4(B[4]), .in5(B[5]), .in6(B[6]), .in7(B[7]),
    .out(priority_encoder_3_out), .en_out(priority_encoder_3_en_out));  // open: en_in, gs
  assign not_2_out = ~decoder_1_out0;  // NOT_Gate not_2, 8 bits wide
  not not_3 (not_3_out, priority_encoder_2_en_out);
  Decoder #(.select(3)) decoder_2 (
    .out0(decoder_2_out0[0]), .out1(decoder_2_out0[1]), .out2(decoder_2_out0[2]), .out3(decoder_2_out0[3]),
    .out4(decoder_2_out0[4]), .out5(decoder_2_out0[5]), .out6(decoder_2_out0[6]), .out7(decoder_2_out0[7]),
    .sel(priority_encoder_2_out), .en(not_3_out));
  not not_4 (not_4_out, priority_encoder_3_en_out);
  Decoder #(.select(3)) decoder_3 (
    .out0(decoder_3_out0[0]), .out1(decoder_3_out0[1]), .out2(decoder_3_out0[2]), .out3(decoder_3_out0[3]),
    .out4(decoder_3_out0[4]), .out5(decoder_3_out0[5]), .out6(decoder_3_out0[6]), .out7(decoder_3_out0[7]),
    .sel(priority_encoder_3_out), .en(not_4_out));
  assign or_1_out = decoder_1_out0 | B;  // OR_Gate or_1, 8 bits wide
  assign and_1_out = not_2_out & B;  // AND_Gate and_1, 8 bits wide
  Multiplexer #(.width(8)) multiplexer_1 (.in0(or_1_out), .in1(and_1_out), .out(U), .sel(Reset));
  Comparator #(.mode("unsigned")) comparator_1 (.a(decoder_2_out0), .b(decoder_3_out0), .gt(pri_flag));  // open: eq, lt

  // Notes on the sheet:
  //   A>B?
endmodule

module inta_controller_mealy (
  input  I1,
  input  I0,
  input  CK,
  output [2:0] U
);

  wire inta_ctrl_mealy_g_1_q0, inta_ctrl_mealy_g_1_q1;

  inta_ctrl_mealy_F inta_ctrl_mealy_f_1 (
    .I1(I1), .I0(I0), .q1(inta_ctrl_mealy_g_1_q1), .q0(inta_ctrl_mealy_g_1_q0), .U0(U[0]), .U1(U[1]),
    .U2(U[2]));
  inta_ctrl_mealy_G inta_ctrl_mealy_g_1 (
    .I1(I1), .I0(I0), .CK(CK), .q0(inta_ctrl_mealy_g_1_q0), .q1(inta_ctrl_mealy_g_1_q1));
endmodule

module inta_ctrl_mealy_G (
  input  I1,
  input  I0,
  input  CK,
  output q0,
  output q1
);

  wire and_1_out, and_2_out, and_3_out, and_4_out, and_5_out, and_6_out, not_1_out, not_2_out, not_3_out,
       not_4_out, not_5_out, or_1_out, or_2_out;

  not not_1 (not_1_out, q1);
  not not_2 (not_2_out, q0);
  not not_3 (not_3_out, q1);
  not not_4 (not_4_out, I1);
  not not_5 (not_5_out, q0);
  and and_1 (and_1_out, not_1_out, not_2_out, I0);
  and and_2 (and_2_out, q0, I1);
  and and_3 (and_3_out, q1, I1);
  and and_4 (and_4_out, not_3_out, q0, not_4_out);
  and and_5 (and_5_out, q1, I1);
  and and_6 (and_6_out, q1, not_5_out);
  or or_1 (or_1_out, and_1_out, and_2_out, and_3_out);
  or or_2 (or_2_out, and_4_out, and_5_out, and_6_out);
  D_Flip_Flop d_ff_1 (.clk(CK), .D(or_1_out), .Q(q0));  // open: Qn, preset, reset
  D_Flip_Flop d_ff_2 (.clk(CK), .D(or_2_out), .Q(q1));  // open: Qn, preset, reset

  // Notes on the sheet:
  //   q1
  //   q0
  //   Q0
  //   Q1
endmodule

module inta_ctrl_mealy_F (
  input  I1,
  input  I0,
  input  q1,
  input  q0,
  output U0,
  output U1,
  output U2
);

  wire and_1_out, and_2_out, and_3_out, and_4_out, and_5_out, and_6_out, and_7_out, not_1_out, not_2_out,
       not_3_out, not_4_out, not_5_out, not_6_out, not_7_out;

  not not_1 (not_1_out, q1);
  not not_2 (not_2_out, q0);
  not not_3 (not_3_out, q0);
  not not_4 (not_4_out, q1);
  not not_5 (not_5_out, I1);
  not not_6 (not_6_out, q0);
  not not_7 (not_7_out, I1);
  and and_1 (and_1_out, not_1_out, not_2_out, I0);
  and and_2 (and_2_out, q0, I1);
  and and_3 (and_3_out, q1, I1);
  and and_4 (and_4_out, q1, not_3_out);
  and and_5 (and_5_out, not_4_out, q0, not_5_out);
  and and_6 (and_6_out, q1, I1);
  and and_7 (and_7_out, q1, not_6_out);
  and and_8 (U2, q1, q0, not_7_out);
  or or_1 (U0, and_1_out, and_2_out, and_3_out, and_4_out);
  or or_2 (U1, and_5_out, and_6_out, and_7_out);
endmodule

module inta_controller (
  input  IRi,
  input  not_INTA,
  input  CK,
  output q0,
  output q1,
  output q2
);

  wire and_1_out, and_2_out, and_3_out, and_4_out, and_5_out, and_6_out, and_7_out, not_1_out, not_2_out,
       not_3_out, not_4_out, not_5_out, not_6_out, not_7_out, or_1_out, or_2_out;

  not not_1 (not_1_out, q2);
  not not_2 (not_2_out, q1);
  and and_1 (and_1_out, not_1_out, not_2_out, not_3_out, IRi);
  not not_3 (not_3_out, q0);
  and and_2 (and_2_out, q0, not_INTA);
  and and_3 (and_3_out, q1, not_INTA);
  not not_4 (not_4_out, q1);
  and and_4 (and_4_out, not_4_out, q0, not_5_out);
  not not_5 (not_5_out, not_INTA);
  and and_5 (and_5_out, q1, not_INTA);
  and and_6 (and_6_out, q1, not_6_out);
  not not_6 (not_6_out, q0);
  and and_7 (and_7_out, q1, q0, not_7_out);
  not not_7 (not_7_out, not_INTA);
  or or_1 (or_1_out, and_1_out, and_2_out, and_3_out);
  or or_2 (or_2_out, and_4_out, and_5_out, and_6_out);
  D_Flip_Flop d_ff_1 (.clk(CK), .D(or_1_out), .Q(q0));  // open: Qn, preset, reset
  D_Flip_Flop d_ff_2 (.clk(CK), .D(or_2_out), .Q(q1));  // open: Qn, preset, reset
  D_Flip_Flop d_ff_3 (.clk(CK), .D(and_7_out), .Q(q2));  // open: Qn, preset, reset

  // Notes on the sheet:
  //   I0
  //   I1
  //   q2
  //   q1
  //   q0
  //   Q0
  //   Q1
  //   Q2
endmodule

module iri_preelab (
  input  [7:0] masked_bits,
  input  reset,
  input  pic_ready,
  input  fronte,
  input  IR0,
  input  in_6,
  input  in_7,
  input  in_8,
  input  ck,
  input  in_10,
  input  in_11,
  input  in_12,
  input  IR7,
  input  [7:0] irr,
  output [7:0] IRi
);

  wire and_2_out, and_3_out, and_4_out, and_5_out, and_6_out, and_7_out, and_8_out, and_9_out;
  wire [7:0] and_1_out, d_ff_1_q, multiplexer_1_out, multiplexer_2_out, not_1_out, register_1_q;

  assign not_1_out = ~masked_bits;  // NOT_Gate not_1, 8 bits wide
  assign and_1_out = not_1_out & {IR7, in_12, in_11, in_10, in_8, in_7, in_6, IR0};  // AND_Gate and_1, 8 bits wide
  Multiplexer #(.width(8)) multiplexer_1 (.in0({8{1'b0}}), .in1(and_1_out), .out(multiplexer_1_out), .sel(fronte));
  and and_2 (and_2_out, reset, irr[0]);
  and and_3 (and_3_out, reset, irr[1]);
  and and_4 (and_4_out, reset, irr[2]);
  and and_5 (and_5_out, reset, irr[3]);
  and and_6 (and_6_out, reset, irr[4]);
  and and_7 (and_7_out, reset, irr[5]);
  and and_8 (and_8_out, reset, irr[6]);
  and and_9 (and_9_out, reset, irr[7]);
  D_Flip_Flop d_ff_1 (.clk(multiplexer_1_out[0]), .D(1'b1), .Q(d_ff_1_q[0]), .reset(and_2_out));  // open: Qn, preset
  D_Flip_Flop d_ff_2 (.clk(multiplexer_1_out[1]), .D(1'b1), .Q(d_ff_1_q[1]), .reset(and_3_out));  // open: Qn, preset
  D_Flip_Flop d_ff_3 (.clk(multiplexer_1_out[2]), .D(1'b1), .Q(d_ff_1_q[2]), .reset(and_4_out));  // open: Qn, preset
  D_Flip_Flop d_ff_4 (.clk(multiplexer_1_out[3]), .D(1'b1), .Q(d_ff_1_q[3]), .reset(and_5_out));  // open: Qn, preset
  D_Flip_Flop d_ff_5 (.clk(multiplexer_1_out[4]), .D(1'b1), .Q(d_ff_1_q[4]), .reset(and_6_out));  // open: Qn, preset
  D_Flip_Flop d_ff_6 (.clk(multiplexer_1_out[5]), .D(1'b1), .Q(d_ff_1_q[5]), .reset(and_7_out));  // open: Qn, preset
  D_Flip_Flop d_ff_7 (.clk(multiplexer_1_out[6]), .D(1'b1), .Q(d_ff_1_q[6]), .reset(and_8_out));  // open: Qn, preset
  D_Flip_Flop d_ff_8 (.clk(multiplexer_1_out[7]), .D(1'b1), .Q(d_ff_1_q[7]), .reset(and_9_out));  // open: Qn, preset
  Multiplexer #(.width(8)) multiplexer_2 (.in0(and_1_out), .in1(register_1_q), .out(multiplexer_2_out), .sel(fronte));
  Register register_1 (.D(d_ff_1_q), .Q(register_1_q), .clk(ck));  // open: en, clr
  Multiplexer #(.width(8)) multiplexer_3 (.in0({8{1'b0}}), .in1(multiplexer_2_out), .out(IRi), .sel(pic_ready));
endmodule
