// Logisim project alu.circ as structural Verilog: 8 circuits, main circuit alu_main
module alu_main (
  input  [2:0] cond,
  input  M,
  input  CI,
  input  [2:0] alu_ctrl,
  input  [31:0] A,
  input  [31:0] B,
  input  in_7,
  output [2:0] out_flags,
  output [31:0] U
);

  wire or_1_out, thirtytwobitadder_1_co;
  wire [0:0] compare_1_res;
  wire [31:0] retedipreelaborazione_1_u_a, retedipreelaborazione_1_u_b, thirtytwobitadder_1_s;

  ReteDiPreelaborazione retedipreelaborazione_1 (
    .C2(alu_ctrl[2]), .C1(alu_ctrl[1]), .C0(alu_ctrl[0]), .A(A), .B(B), .U_A(retedipreelaborazione_1_u_a),
    .U_B(retedipreelaborazione_1_u_b));
  ThirtyTwoBitAdder thirtytwobitadder_1 (
    .M(M), .CI(CI), .A(retedipreelaborazione_1_u_a), .B(retedipreelaborazione_1_u_b),
    .S(thirtytwobitadder_1_s), .CO(thirtytwobitadder_1_co));
  // Probe on thirtytwobitadder_1_s
  flags flags_1 (
    .U(thirtytwobitadder_1_s), .CO(thirtytwobitadder_1_co), .ZF(out_flags[0]), .SF(out_flags[1]),
    .CF(out_flags[2]));
  or or_1 (or_1_out, cond[0], cond[1], cond[2]);
  compare compare_1 (
    .flags(out_flags), .A(retedipreelaborazione_1_u_a), .B(retedipreelaborazione_1_u_b), .cond(cond),
    .U(in_7), .res(compare_1_res[0]));
  Multiplexer #(.width(32)) multiplexer_1 (
    .in0(thirtytwobitadder_1_s), .in1({{31{1'b0}}, compare_1_res[0]}), .out(U), .sel(or_1_out));

  // Notes on the sheet:
  //   c2
  //   c1
  //   c0
  //   Diverso da slide: 000 normale, !=000 fa la set condition
endmodule

module HalfAdder (
  input  in_1,
  input  in_2,
  output out_3,
  output out_4
);

  xor xor_1 (out_3, in_1, in_2);
  and and_1 (out_4, in_1, in_2);
endmodule

module FullAdder (
  input  in_1,
  input  in_2,
  input  in_3,
  output out_4,
  output out_5
);

  wire halfadder_1_out_3, halfadder_1_out_4, halfadder_2_out_4;

  HalfAdder halfadder_1 (.in_1(in_2), .in_2(in_3), .out_3(halfadder_1_out_3), .out_4(halfadder_1_out_4));
  HalfAdder halfadder_2 (.in_1(in_1), .in_2(halfadder_1_out_3), .out_3(out_4), .out_4(halfadder_2_out_4));
  or or_1 (out_5, halfadder_2_out_4, halfadder_1_out_4);
endmodule

module FourBitAdder (
  input  M,
  input  CI,
  input  [3:0] A,
  input  [3:0] B,
  output [3:0] S,
  output CO
);

  wire and_1_out, and_2_out, and_3_out, fulladder_1_out_5, fulladder_2_out_5, fulladder_3_out_5,
       fulladder_4_out_5;

  FullAdder fulladder_1 (.in_1(CI), .in_2(A[0]), .in_3(B[0]), .out_4(S[0]), .out_5(fulladder_1_out_5));
  FullAdder fulladder_2 (.in_1(and_1_out), .in_2(A[1]), .in_3(B[1]), .out_4(S[1]), .out_5(fulladder_2_out_5));
  FullAdder fulladder_3 (.in_1(and_2_out), .in_2(A[2]), .in_3(B[2]), .out_4(S[2]), .out_5(fulladder_3_out_5));
  FullAdder fulladder_4 (.in_1(and_3_out), .in_2(A[3]), .in_3(B[3]), .out_4(S[3]), .out_5(fulladder_4_out_5));
  and and_1 (and_1_out, fulladder_1_out_5, M);
  and and_2 (and_2_out, fulladder_2_out_5, M);
  and and_3 (and_3_out, fulladder_3_out_5, M);
  and and_4 (CO, fulladder_4_out_5, M);
endmodule

module ThirtyTwoBitAdder (
  input  M,
  input  CI,
  input  [31:0] A,
  input  [31:0] B,
  output [31:0] S,
  output CO
);

  wire fourbitadder_1_co, fourbitadder_2_co, fourbitadder_3_co, fourbitadder_4_co, fourbitadder_5_co,
       fourbitadder_6_co, fourbitadder_7_co;

  FourBitAdder fourbitadder_1 (.M(M), .CI(CI), .A(A[3:0]), .B(B[3:0]), .S(S[3:0]), .CO(fourbitadder_1_co));
  FourBitAdder fourbitadder_2 (
    .M(M), .CI(fourbitadder_1_co), .A(A[7:4]), .B(B[7:4]), .S(S[7:4]), .CO(fourbitadder_2_co));
  FourBitAdder fourbitadder_3 (
    .M(M), .CI(fourbitadder_2_co), .A(A[11:8]), .B(B[11:8]), .S(S[11:8]), .CO(fourbitadder_3_co));
  FourBitAdder fourbitadder_4 (
    .M(M), .CI(fourbitadder_3_co), .A(A[15:12]), .B(B[15:12]), .S(S[15:12]), .CO(fourbitadder_4_co));
  FourBitAdder fourbitadder_5 (
    .M(M), .CI(fourbitadder_4_co), .A(A[19:16]), .B(B[19:16]), .S(S[19:16]), .CO(fourbitadder_5_co));
  FourBitAdder fourbitadder_6 (
    .M(M), .CI(fourbitadder_5_co), .A(A[23:20]), .B(B[23:20]), .S(S[23:20]), .CO(fourbitadder_6_co));
  FourBitAdder fourbitadder_7 (
    .M(M), .CI(fourbitadder_6_co), .A(A[27:24]), .B(B[27:24]), .S(S[27:24]), .CO(fourbitadder_7_co));
  FourBitAdder fourbitadder_8 (.M(M), .CI(fourbitadder_7_co), .A(A[31:28]), .B(B[31:28]), .S(S[31:28]), .CO(CO));
endmodule

module ReteDiPreelaborazione (
  input  C2,
  input  C1,
  input  C0,
  input  [31:0] A,
  input  [31:0] B,
  output [31:0] U_A,
  output [31:0] U_B
);

  wire [31:0] multiplexer_1_out, not_1_out;

  Multiplexer #(.width(32)) multiplexer_1 (.in0(B), .in1({32{1'b0}}), .out(multiplexer_1_out), .sel(C1));
  Multiplexer #(.width(32)) multiplexer_2 (.in0(A), .in1({32{1'b0}}), .out(U_A), .sel(C2));
  assign not_1_out = ~multiplexer_1_out;  // NOT_Gate not_1, 32 bits wide
  Multiplexer #(.width(32)) multiplexer_3 (.in0(multiplexer_1_out), .in1(not_1_out), .out(U_B), .sel(C0));
endmodule

module flags (
  input  [31:0] U,
  input  CO,
  output ZF,
  output SF,
  output CF
);

  wire or_1_out;

  or or_1 (or_1_out, U[0], U[1], U[2], U[3], U[4], U[5], U[6], U[7], U[8], U[9], U[10], U[11], U[12], U[13], U[14], U[15], U[16], U[17], U[18], U[19], U[20], U[21], U[22], U[23], U[24], U[25], U[26], U[27], U[28], U[29], U[30], U[31]);
  not not_1 (ZF, or_1_out);

  assign CF = CO;
  assign SF = U[31];
endmodule

module compare (
  input  [2:0] flags,
  input  [31:0] A,
  input  [31:0] B,
  input  [2:0] cond,
  input  U,
  output res
);

  wire fulladder_1_out_4, multiplexer_1_out, multiplexer_2_out, not_1_out, not_2_out, not_3_out, or_1_out;

  Multiplexer multiplexer_1 (.in0(A[31]), .in1(1'b0), .out(multiplexer_1_out), .sel(U));
  Multiplexer multiplexer_2 (.in0(B[31]), .in1(1'b1), .out(multiplexer_2_out), .sel(U));
  FullAdder fulladder_1 (
    .in_1(flags[2]), .in_2(multiplexer_1_out), .in_3(multiplexer_2_out), .out_4(fulladder_1_out_4));  // open: out_5
  or or_1 (or_1_out, flags[0], fulladder_1_out_4);
  not not_1 (not_1_out, or_1_out);
  not not_2 (not_2_out, fulladder_1_out_4);
  not not_3 (not_3_out, flags[0]);
  Multiplexer #(.select(3)) multiplexer_3 (
    .in1(not_1_out), .in2(or_1_out), .in3(not_2_out), .in4(flags[0]), .in5(not_3_out),
    .in6(fulladder_1_out_4), .out(res), .sel(cond));  // open: in0, in7

  // Notes on the sheet:
  //   cf
  //   zf
  //   LT
  //   EQ
  //   LE
  //   Modificato LT: invece che entrare all'ingresso zero del mux va al 7
endmodule
