// Logisim project Encoder.circ as structural Verilog: 3 circuits, main circuit eightBitEncoder
module eightBitEncoder (
  input  [7:0] I,
  output [2:0] U,
  output en
);

  wire priority_encoder_1_en_out;

  not not_1 (en, priority_encoder_1_en_out);
  Priority_Encoder priority_encoder_1 (
    .in0(I[0]), .in1(I[1]), .in2(I[2]), .in3(I[3]), .in4(I[4]), .in5(I[5]), .in6(I[6]), .in7(I[7]), .out(U),
    .en_in(1'b1), .en_out(priority_encoder_1_en_out));  // open: gs
endmodule

module thirtytwoBitEncoder (
  input  [31:0] in_1,
  output [4:0] out_2,
  output out_3
);

  wire eightbitencoder_1_en, eightbitencoder_2_en, eightbitencoder_3_en, eightbitencoder_4_en;
  wire [2:0] eightbitencoder_1_u, eightbitencoder_2_u, eightbitencoder_3_u, eightbitencoder_4_u;
  wire [4:0] adder_1_out, adder_2_out, adder_3_out;

  eightBitEncoder eightbitencoder_1 (.I(in_1[7:0]), .U(eightbitencoder_1_u), .en(eightbitencoder_1_en));
  eightBitEncoder eightbitencoder_2 (.I(in_1[15:8]), .U(eightbitencoder_2_u), .en(eightbitencoder_2_en));
  eightBitEncoder eightbitencoder_3 (.I(in_1[23:16]), .U(eightbitencoder_3_u), .en(eightbitencoder_3_en));
  eightBitEncoder eightbitencoder_4 (.I(in_1[31:24]), .U(eightbitencoder_4_u), .en(eightbitencoder_4_en));
  or or_1 (out_3, eightbitencoder_1_en, eightbitencoder_2_en, eightbitencoder_3_en, eightbitencoder_4_en);
  Adder #(.width(5)) adder_1 (
    .a({2'b00, eightbitencoder_2_u}), .b(5'b01000), .out(adder_1_out), .cin(1'b0));  // open: cout
  Adder #(.width(5)) adder_2 (
    .a({2'b00, eightbitencoder_3_u}), .b(5'b10000), .out(adder_2_out), .cin(1'b0));  // open: cout
  Adder #(.width(5)) adder_3 (
    .a({2'b00, eightbitencoder_4_u}), .b(5'b11000), .out(adder_3_out), .cin(1'b0));  // open: cout
  assign out_2 = eightbitencoder_1_en ? {2'b00, eightbitencoder_1_u} : 5'bz;  // Controlled_Buffer controlled_buffer_1
  assign out_2 = eightbitencoder_2_en ? adder_1_out : 5'bz;  // Controlled_Buffer controlled_buffer_2
  assign out_2 = eightbitencoder_3_en ? adder_2_out : 5'bz;  // Controlled_Buffer controlled_buffer_3
  assign out_2 = eightbitencoder_4_en ? adder_3_out : 5'bz;  // Controlled_Buffer controlled_buffer_4
endmodule

module rfEncoderBlock (
  input  [31:0] WERF,
  input  [31:0] OE1RF,
  input  [31:0] OE2RF,
  output [4:0] A1,
  output [4:0] A2,
  output WE,
  output OE1,
  output OE2
);

  wire [4:0] thirtytwobitencoder_1_out_2, thirtytwobitencoder_2_out_2, thirtytwobitencoder_3_out_2;

  thirtytwoBitEncoder thirtytwobitencoder_1 (.in_1(WERF), .out_2(thirtytwobitencoder_1_out_2), .out_3(WE));
  thirtytwoBitEncoder thirtytwobitencoder_2 (.in_1(OE1RF), .out_2(thirtytwobitencoder_2_out_2), .out_3(OE1));
  thirtytwoBitEncoder thirtytwobitencoder_3 (.in_1(OE2RF), .out_2(thirtytwobitencoder_3_out_2), .out_3(OE2));
  Multiplexer #(.width(5)) multiplexer_1 (
    .in0(thirtytwobitencoder_2_out_2), .in1(thirtytwobitencoder_1_out_2), .out(A1), .sel(WE));
  Multiplexer #(.width(5)) multiplexer_2 (
    .in0(thirtytwobitencoder_3_out_2), .in1(thirtytwobitencoder_1_out_2), .out(A2), .sel(WE));
endmodule
