// Logisim project Mapping.circ as structural Verilog: 1 circuit, main circuit main
module main (
  input  in_1,
  input  [31:0] in_2,
  input  [31:0] in_3
);

  wire clock_1_out, clock_2_out, clock_3_out, cs1, cs2, cs3, not_1_out, not_2_out, not_3_out, not_4_out,
       not_5_out, not_6_out, or_1_out, or_2_out, or_3_out;

  // Probe on in_2
  // Probe on in_3
  LED BA29 (.in(in_2[29]));
  RAM #(.addrWidth(16), .asyncread("true"), .dataWidth(32)) ram_1 (
    .addr(in_2[15:0]), .we(not_1_out), .oe(1'b1), .clk(clock_1_out), .din(in_3));  // open: dout
  or or_1 (or_1_out, cs1, in_1);
  not not_1 (not_1_out, or_1_out);
  Clock clock_1 (.out(clock_1_out));
  RAM #(.addrWidth(16), .asyncread("true"), .dataWidth(32)) ram_2 (
    .addr(in_2[15:0]), .we(not_2_out), .oe(1'b1), .clk(clock_2_out), .din(in_3));  // open: dout
  or or_2 (or_2_out, cs2, in_1);
  not not_2 (not_2_out, or_2_out);
  Clock clock_2 (.out(clock_2_out));
  RAM #(.addrWidth(16), .asyncread("true"), .dataWidth(32)) ram_3 (
    .addr(in_2[15:0]), .we(not_3_out), .oe(1'b1), .clk(clock_3_out), .din(in_3));  // open: dout
  or or_3 (or_3_out, cs3, in_1);
  not not_3 (not_3_out, or_3_out);
  Clock clock_3 (.out(clock_3_out));
  LED BA28 (.in(in_2[28]));
  LED BA27 (.in(in_2[27]));
  LED BA26 (.in(in_2[26]));
  or or_4 (cs1, in_2[28], in_2[27]);
  or or_5 (cs2, in_2[28], not_4_out, in_2[26]);
  not not_4 (not_4_out, in_2[27]);
  or or_6 (cs3, in_2[29], not_5_out, not_6_out);
  not not_5 (not_5_out, in_2[27]);
  not not_6 (not_6_out, in_2[26]);

  // Notes on the sheet:
  //   MemWR#
  //   Indirizzi
  //   Dati
  //   Bus Cmd
  //   Bus Indirizzi
  //   Bus Dati
  //   EPROM1
  //   EPROM2
  //   EPROM3
  //   # CIRCUITO PER LA DECODIFICA SEMPLIFICATA DELL'INDIRIZZO
  //   CSEPROM1#
  //   CSEPROM2#
  //   CSEPROM3#
endmodule
