// Logisim project CPU.circ as structural Verilog: 1 circuit, main circuit main
module main (
  input  READY,
  input  [31:0] in_2,
  input  Clear_master,
  input  Clrear,
  input  in_5,
  input  in_6,
  output [3:0] Mem_IO,
  output [31:0] out_8,
  output [31:0] out_9
);

  wire main_1_p4, main_1_p5, main_1_p6, main_1_p7, main_1_p10, main_1_p11, main_1_p12, main_1_p13;
  wire [3:0] main_3_out_2, main_3_out_3;
  wire [4:4] not_1_out;
  wire [31:0] main_1_p9, main_2_p17;

  // UDC_main main_1: pin names not known; wires that end beside it: READY, Clear_master, Clrear, main_1_p4, main_1_p5, main_1_p6, main_1_p7, Mem_IO, main_1_p9, main_1_p10, main_1_p11, main_1_p12, main_1_p13, in_2, in_6, in_5
  not not_1 (not_1_out[4], main_1_p9[4]);
  // DATAPATH_main main_2: pin names not known; wires that end beside it: {not_1_out[4], main_1_p9[3:0]}, main_1_p10, main_1_p11, main_1_p12, main_1_p9[7:5], main_1_p9[10:8], main_1_p9[13:11], main_1_p9[16:14], main_1_p9[19:17], main_1_p9[22:20], main_1_p9[25:23], main_1_p9[28:26], main_1_p9[30:29], main_1_p6, main_1_p7, main_1_p13, main_2_p17, main_1_p4, main_1_p5, in_2, out_8, out_9, in_5
  _7_Segment_Display u_7_segment_display_1 (
    .g(main_3_out_2[3]), .f(main_3_out_2[2]), .a(main_3_out_2[1]), .b(main_3_out_2[0]), .e(main_3_out_3[0]),
    .d(main_3_out_3[1]), .c(main_3_out_3[2]), .dp(main_3_out_3[3]));
  BCD_ENCODER_main main_3 (.in_1(main_2_p17[3:0]), .out_2(main_3_out_2), .out_3(main_3_out_3));
endmodule
