// Logisim project 32bREGISTER.circ as structural Verilog: 2 circuits, main circuit main
module _32b_register (
  input  OE1,
  input  OE2,
  input  WE,
  input  CK,
  input  [31:0] in_5,
  output [31:0] out_6,
  output [31:0] out_7
);

  main main_1 (.OE1(OE1), .OE2(OE2), .WE(WE), .CK(CK), .in_5(in_5[3:0]), .out_6(out_6[3:0]), .out_7(out_7[3:0]));
  main main_2 (.OE1(OE1), .OE2(OE2), .WE(WE), .CK(CK), .in_5(in_5[7:4]), .out_6(out_6[7:4]), .out_7(out_7[7:4]));
  main main_3 (.OE1(OE1), .OE2(OE2), .WE(WE), .CK(CK), .in_5(in_5[11:8]), .out_6(out_6[11:8]), .out_7(out_7[11:8]));
  main main_4 (.OE1(OE1), .OE2(OE2), .WE(WE), .CK(CK), .in_5(in_5[15:12]), .out_6(out_6[15:12]), .out_7(out_7[15:12]));
  main main_5 (.OE1(OE1), .OE2(OE2), .WE(WE), .CK(CK), .in_5(in_5[19:16]), .out_6(out_6[19:16]), .out_7(out_7[19:16]));
  main main_6 (.OE1(OE1), .OE2(OE2), .WE(WE), .CK(CK), .in_5(in_5[23:20]), .out_6(out_6[23:20]), .out_7(out_7[23:20]));
  main main_7 (.OE1(OE1), .OE2(OE2), .WE(WE), .CK(CK), .in_5(in_5[27:24]), .out_6(out_6[27:24]), .out_7(out_7[27:24]));
  main main_8 (.OE1(OE1), .OE2(OE2), .WE(WE), .CK(CK), .in_5(in_5[31:28]), .out_6(out_6[31:28]), .out_7(out_7[31:28]));
endmodule

module main (
  input  OE1,
  input  OE2,
  input  WE,
  input  CK,
  input  [3:0] in_5,
  output [3:0] out_6,
  output [3:0] out_7
);

  wire d_ff_1_q, d_ff_2_q, d_ff_3_q, d_ff_4_q, multiplexer_1_out, multiplexer_2_out, multiplexer_3_out,
       multiplexer_4_out;

  Multiplexer #(.enable("false")) multiplexer_1 (.in0(d_ff_1_q), .in1(in_5[0]), .out(multiplexer_1_out), .sel(WE));
  Multiplexer #(.enable("false")) multiplexer_2 (.in0(d_ff_2_q), .in1(in_5[1]), .out(multiplexer_2_out), .sel(WE));
  Multiplexer #(.enable("false")) multiplexer_3 (.in0(d_ff_3_q), .in1(in_5[2]), .out(multiplexer_3_out), .sel(WE));
  Multiplexer #(.enable("false")) multiplexer_4 (.in0(d_ff_4_q), .in1(in_5[3]), .out(multiplexer_4_out), .sel(WE));
  D_Flip_Flop d_ff_1 (.clk(CK), .D(multiplexer_1_out), .Q(d_ff_1_q));  // open: Qn, preset, en, reset
  D_Flip_Flop d_ff_2 (.clk(CK), .D(multiplexer_2_out), .Q(d_ff_2_q));  // open: Qn, preset, en, reset
  D_Flip_Flop d_ff_3 (.clk(CK), .D(multiplexer_3_out), .Q(d_ff_3_q));  // open: Qn, preset, en, reset
  D_Flip_Flop d_ff_4 (.clk(CK), .D(multiplexer_4_out), .Q(d_ff_4_q));  // open: Qn, preset, en, reset
  assign out_6[0] = OE1 ? d_ff_1_q : 1'bz;  // Controlled_Buffer controlled_buffer_1
  assign out_7[0] = OE2 ? d_ff_1_q : 1'bz;  // Controlled_Buffer controlled_buffer_2
  assign out_6[1] = OE1 ? d_ff_2_q : 1'bz;  // Controlled_Buffer controlled_buffer_3
  assign out_7[1] = OE2 ? d_ff_2_q : 1'bz;  // Controlled_Buffer controlled_buffer_4
  assign out_6[2] = OE1 ? d_ff_3_q : 1'bz;  // Controlled_Buffer controlled_buffer_5
  assign out_7[2] = OE2 ? d_ff_3_q : 1'bz;  // Controlled_Buffer controlled_buffer_6
  assign out_6[3] = OE1 ? d_ff_4_q : 1'bz;  // Controlled_Buffer controlled_buffer_7
  assign out_7[3] = OE2 ? d_ff_4_q : 1'bz;  // Controlled_Buffer controlled_buffer_8
endmodule
