// Logisim project CPU.circ as structural Verilog: 1 circuit, main circuit cpu_main
module cpu_main (
);

  wire ck;
  wire [31:0] dp_main_1_address_out, dp_main_1_data_out, undriven;

  dp_main dp_main_1 (
    .CK(ck), .data_in(undriven), .address_out(dp_main_1_address_out), .data_out(dp_main_1_data_out));  // open: WR, c_en, Waddr, addrMux, cost_en, RD1, Raddr1, a_en, b_en, Raddr2, RD2, pc_en, temp_en, iar_en, mar_en, mdr_en, cost_in, alu_ctrl, dataMux, flags
endmodule
