// Logisim project DataPath.circ as structural Verilog: 3 circuits, main circuit dp_main
module dp_main (
  input  [4:0] alu_ctrl,
  input  CK,
  input  RD1,
  input  [4:0] Raddr1,
  input  WR,
  input  [2:0] a_en,
  input  [2:0] c_en,
  input  [2:0] b_en,
  input  [4:0] Waddr,
  input  [4:0] Raddr2,
  input  RD2,
  input  [2:0] pc_en,
  input  [2:0] temp_en,
  input  [2:0] iar_en,
  input  [2:0] mar_en,
  input  [2:0] mdr_en,
  input  dataMux,
  input  addrMux,
  input  cost_en,
  input  [31:0] data_in,
  input  [31:0] cost_in,
  output [2:0] flags,
  output [31:0] address_out,
  output [31:0] data_out
);

  wire rf_read_write_logic_1_ck_r1, rf_read_write_logic_1_ck_r2, rf_read_write_logic_1_oe1,
       rf_read_write_logic_1_oe2, rf_read_write_logic_1_we1, rf_read_write_logic_1_we2;
  wire [4:0] rf_read_write_logic_1_a_r1, rf_read_write_logic_1_a_r2;
  wire [31:0] alu_main_1_u, controlled_buffer_1_out, multiplexer_2_out, ram_1_dout, ram_2_dout,
       register_main_1_state, register_main_2_state, register_main_3_state, register_main_4_state,
       register_main_5_state, register_main_6_state, register_main_7_state, register_main_8_state,
       register_main_8_u1, register_main_8_u2, rf_read_write_logic_1_d_r1, rf_read_write_logic_1_d_r2,
       rf_read_write_logic_1_out_16, rf_read_write_logic_1_out_22;

  assign controlled_buffer_1_out = cost_en ? cost_in : 32'bz;  // Controlled_Buffer controlled_buffer_1
  register_main register_main_1 (
    .D(rf_read_write_logic_1_out_16), .CK(CK), .reg_ctrl(a_en), .state(register_main_1_state),
    .U1(controlled_buffer_1_out), .U2(data_out));
  // Probe on register_main_1_state
  register_main register_main_2 (
    .D(rf_read_write_logic_1_out_22), .CK(CK), .reg_ctrl(b_en), .state(register_main_2_state),
    .U1(controlled_buffer_1_out), .U2(data_out));
  // Probe on register_main_2_state
  Multiplexer #(.width(32)) multiplexer_1 (.in0(data_out), .in1(data_out), .out(address_out), .sel(addrMux));
  // Probe on data_out
  // Probe on controlled_buffer_1_out
  RAM #(.addrWidth(5), .asyncread("true"), .dataWidth(32)) ram_1 (
    .addr(rf_read_write_logic_1_a_r1), .we(rf_read_write_logic_1_we1), .oe(rf_read_write_logic_1_oe1),
    .clk(rf_read_write_logic_1_ck_r1), .din(rf_read_write_logic_1_d_r1), .dout(ram_1_dout));
  RAM #(.addrWidth(5), .asyncread("true"), .dataWidth(32)) ram_2 (
    .addr(rf_read_write_logic_1_a_r2), .we(rf_read_write_logic_1_we2), .oe(rf_read_write_logic_1_oe2),
    .clk(rf_read_write_logic_1_ck_r2), .din(rf_read_write_logic_1_d_r2), .dout(ram_2_dout));
  alu_main alu_main_1 (
    .alu_ctrl(alu_ctrl[2:0]), .A(data_out), .B(controlled_buffer_1_out), .M(alu_ctrl[4]), .CI(alu_ctrl[3]),
    .U(alu_main_1_u), .out_flags(flags));
  register_main register_main_3 (
    .D(alu_main_1_u), .CK(CK), .reg_ctrl(pc_en), .state(register_main_3_state), .U1(controlled_buffer_1_out),
    .U2(data_out));
  // Probe on register_main_3_state
  register_main register_main_4 (
    .D(alu_main_1_u), .CK(CK), .reg_ctrl(temp_en), .state(register_main_4_state),
    .U1(controlled_buffer_1_out), .U2(data_out));
  // Probe on register_main_4_state
  register_main register_main_5 (
    .D(alu_main_1_u), .CK(CK), .reg_ctrl(iar_en), .state(register_main_5_state),
    .U1(controlled_buffer_1_out), .U2(data_out));
  // Probe on register_main_5_state
  register_main register_main_6 (
    .D(alu_main_1_u), .CK(CK), .reg_ctrl(mar_en), .state(register_main_6_state),
    .U1(controlled_buffer_1_out), .U2(data_out));
  // Probe on register_main_6_state
  register_main register_main_7 (
    .D(multiplexer_2_out), .CK(CK), .reg_ctrl(mdr_en), .state(register_main_7_state),
    .U1(controlled_buffer_1_out), .U2(data_out));
  // Probe on register_main_7_state
  // Probe on alu_main_1_u
  rf_read_write_logic rf_read_write_logic_1 (
    .in_1(CK), .in_3(RD1), .in_6(RD2), .in_10(WR), .in_5(Raddr2), .in_9(Waddr), .in_2(Raddr1),
    .in_8(register_main_8_u1), .do_1(ram_1_dout), .do_2(ram_2_dout), .out_16(rf_read_write_logic_1_out_16),
    .out_22(rf_read_write_logic_1_out_22), .a_r1(rf_read_write_logic_1_a_r1),
    .we1(rf_read_write_logic_1_we1), .oe1(rf_read_write_logic_1_oe1), .ck_r1(rf_read_write_logic_1_ck_r1),
    .d_r1(rf_read_write_logic_1_d_r1), .a_r2(rf_read_write_logic_1_a_r2), .we2(rf_read_write_logic_1_we2),
    .oe2(rf_read_write_logic_1_oe2), .ck_r2(rf_read_write_logic_1_ck_r2), .d_r2(rf_read_write_logic_1_d_r2));
  Multiplexer #(.width(32)) multiplexer_2 (.in0(alu_main_1_u), .in1(data_in), .out(multiplexer_2_out), .sel(dataMux));
  register_main register_main_8 (
    .D(alu_main_1_u), .CK(CK), .reg_ctrl(c_en), .state(register_main_8_state), .U1(register_main_8_u1),
    .U2(register_main_8_u2));
  // Probe on register_main_8_state
  // also tied to GND on the sheet: {register_main_8_u2[0], register_main_8_u2[1], register_main_8_u2[2], register_main_8_u2[3], register_main_8_u2[4], register_main_8_u2[5], register_main_8_u2[6], register_main_8_u2[7], register_main_8_u2[8], register_main_8_u2[9], register_main_8_u2[10], register_main_8_u2[11], register_main_8_u2[12], register_main_8_u2[13], register_main_8_u2[14], register_main_8_u2[15], register_main_8_u2[16], register_main_8_u2[17], register_main_8_u2[18], register_main_8_u2[19], register_main_8_u2[20], register_main_8_u2[21], register_main_8_u2[22], register_main_8_u2[23], register_main_8_u2[24], register_main_8_u2[25], register_main_8_u2[26], register_main_8_u2[27], register_main_8_u2[28], register_main_8_u2[29], register_main_8_u2[30], register_main_8_u2[31]}

  // Notes on the sheet:
  //   (0=mar,1=pc)
  //   S1
  //   S2
  //   address
  //   mux
  //   data
  //   mux
  //   (1=data from
  //   outside)
  //   C
endmodule

module rf_read_write_logic (
  input  in_1,
  input  [4:0] in_2,
  input  in_3,
  input  [31:0] do_1,
  input  [4:0] in_5,
  input  in_6,
  input  [31:0] do_2,
  input  [31:0] in_8,
  input  [4:0] in_9,
  input  in_10,
  output [4:0] a_r1,
  output we1,
  output oe1,
  output ck_r1,
  output [31:0] d_r1,
  output [31:0] out_16,
  output [4:0] a_r2,
  output we2,
  output oe2,
  output ck_r2,
  output [31:0] d_r2,
  output [31:0] out_22
);

  Multiplexer #(.width(5)) multiplexer_1 (.in0(in_2), .in1(in_9), .out(a_r1), .sel(in_10));
  Multiplexer #(.width(5)) multiplexer_2 (.in0(in_5), .in1(in_9), .out(a_r2), .sel(in_10));

  assign ck_r1 = in_1;
  assign ck_r2 = in_1;
  assign d_r1 = in_8;
  assign d_r2 = in_8;
  assign oe1 = in_3;
  assign oe2 = in_6;
  assign out_16 = do_1;
  assign out_22 = do_2;
  assign we1 = in_10;
  assign we2 = in_10;

  // Other names for the same wires on the sheet: ck = in_1

  // Notes on the sheet:
  //   Register File
endmodule

module dp_test (
);

  dp_main dp_main_1 ();  // open: WR, c_en, Waddr, addrMux, cost_en, RD1, Raddr1, a_en, b_en, Raddr2, RD2, pc_en, temp_en, iar_en, mar_en, mdr_en, cost_in, alu_ctrl, dataMux, CK, data_in, address_out, data_out, flags
endmodule
