// Logisim project Udc.circ as structural Verilog: 3 circuits, main circuit udc_main
module udc_main (
  input  CK,
  input  [1:0] in_2,
  input  ask_ready,
  input  ready,
  input  [31:0] ir_in,
  output out_6,
  output [31:0] reg_ctrl
);

  wire counter_control_1_ck_counter, counter_control_1_count, counter_control_1_reset_counter, ir_wr;
  wire [3:0] counter_1_q, counter_control_1_current_cycle;
  wire [15:0] multiplexer_1_out, rom_1_data;
  wire [25:0] register_main_1_u1;
  wire [31:0] alu_main_1_u, register_main_1_state, register_main_1_u2;
  wire [31:26] register_main_1_u1_2;
  wire [63:32] rom_2_data;

  ROM #(.addrWidth(6), .dataWidth(16)) rom_1 (.addr(register_main_1_u1_2), .data(rom_1_data));
  register_main register_main_1 (
    .D(ir_in), .CK(CK), .reg_ctrl({2'b01, ir_wr}), .state(register_main_1_state),
    .U1({register_main_1_u1_2, register_main_1_u1}), .U2(register_main_1_u2));
  // Probe on register_main_1_state
  Multiplexer #(.select(2), .width(16)) multiplexer_1 (
    .in0(16'h1), .in3(rom_1_data), .out(multiplexer_1_out), .sel(in_2));  // open: in1, in2
  counter_control counter_control_1 (
    .in_1(CK), .n_cycles(multiplexer_1_out[3:0]), .ready(ready), .ask_ready(ask_ready),
    .Q_counter(counter_1_q), .count(counter_control_1_count), .ck_counter(counter_control_1_ck_counter),
    .reset_counter(counter_control_1_reset_counter), .current_cycle(counter_control_1_current_cycle),
    .cycles_finished(out_6));
  Counter #(.max('hf), .width(4)) counter_1 (
    .count(counter_control_1_count), .Q(counter_1_q), .clk(counter_control_1_ck_counter),
    .clr(counter_control_1_reset_counter));  // open: load, D, carry, up
  alu_main alu_main_1 (
    .alu_ctrl(3'b000), .A({{22{1'b0}}, multiplexer_1_out[13:4]}),
    .B({{28{1'b0}}, counter_control_1_current_cycle}), .M(1'b1), .CI(1'b0), .U(alu_main_1_u));  // open: out_flags
  ROM #(.addrWidth(10), .dataWidth(64)) rom_2 (
    .addr(alu_main_1_u[9:0]), .data({rom_2_data[63:50], ir_wr, rom_2_data[48:32], reg_ctrl}));
  // also tied to GND on the sheet: {register_main_1_u2[0], register_main_1_u2[1], register_main_1_u2[2], register_main_1_u2[3], register_main_1_u2[4], register_main_1_u2[5], register_main_1_u2[6], register_main_1_u2[7], register_main_1_u2[8], register_main_1_u2[9], register_main_1_u2[10], register_main_1_u2[11], register_main_1_u2[12], register_main_1_u2[13], register_main_1_u2[14], register_main_1_u2[15], register_main_1_u2[16], register_main_1_u2[17], register_main_1_u2[18], register_main_1_u2[19], register_main_1_u2[20], register_main_1_u2[21], register_main_1_u2[22], register_main_1_u2[23], register_main_1_u2[24], register_main_1_u2[25], register_main_1_u2[26], register_main_1_u2[27], register_main_1_u2[28], register_main_1_u2[29], register_main_1_u2[30], register_main_1_u2[31], alu_main_1_u[10], alu_main_1_u[11], alu_main_1_u[12], alu_main_1_u[13], alu_main_1_u[14], alu_main_1_u[15], alu_main_1_u[16], alu_main_1_u[17], alu_main_1_u[18], alu_main_1_u[19], alu_main_1_u[20], alu_main_1_u[21], alu_main_1_u[22], alu_main_1_u[23], alu_main_1_u[24], alu_main_1_u[25], alu_main_1_u[26], alu_main_1_u[27], alu_main_1_u[28], alu_main_1_u[29], alu_main_1_u[30], alu_main_1_u[31]}

  // Notes on the sheet:
  //   contents of rom_1 (hex, n*v repeats v):
  //   21
  //   COP
  //   ir[25...0]
  //   istr_type
  //   start_addr
  //   contents of rom_2 (hex, n*v repeats v):
  //   2000400010000 3000000c13a c50 8000001000
endmodule

module compare_counter (
  input  [3:0] in_1,
  input  [3:0] in_2,
  output out_3
);

  wire or_1_out;
  wire [3:0] xor_1_out;

  assign xor_1_out = in_1 ^ in_2;  // XOR_Gate xor_1, 4 bits wide
  or or_1 (or_1_out, xor_1_out[0], xor_1_out[1], xor_1_out[2], xor_1_out[3]);
  not not_1 (out_3, or_1_out);
endmodule

module counter_control (
  input  in_1,
  input  ask_ready,
  input  [3:0] Q_counter,
  input  ready,
  input  [3:0] n_cycles,
  output [3:0] current_cycle,
  output count,
  output ck_counter,
  output reset_counter,
  output cycles_finished
);

  wire [3:0] adder_1_out;

  Multiplexer multiplexer_1 (.in0(1'b1), .in1(ready), .out(count), .sel(ask_ready));
  Adder #(.width(4)) adder_1 (.a(n_cycles), .b(4'b0000), .out(adder_1_out), .cin(1'b1));  // open: cout
  Counter #(.max('hf), .width(4)) counter_1 ();  // open: load, D, count, Q, carry, up, clk, clr
  compare_counter compare_counter_1 (.in_1(Q_counter), .in_2(adder_1_out), .out_3(reset_counter));
  compare_counter compare_counter_2 (.in_1(Q_counter), .in_2(n_cycles), .out_3(cycles_finished));

  assign ck_counter = in_1;
  assign current_cycle = Q_counter;

  // Other names for the same wires on the sheet: ck = in_1
endmodule
