// Logisim project RegisterFile.circ as structural Verilog: 3 circuits, main circuit RegisterFile_main
module RegisterFile_main (
  input  ck,
  input  RD1_not,
  input  [4:0] Raddr1,
  output [31:0] out_4,
  output [31:0] out_5,
  output [31:0] out_6,
  output [31:0] out_7,
  output [31:0] out_8,
  output [31:0] out_9,
  output [31:0] out_10,
  output [31:0] out_11,
  output [31:0] out_12,
  output [31:0] out_13,
  output [31:0] out_14,
  output [31:0] out_15,
  output [31:0] out_16,
  output [31:0] out_17,
  output [31:0] out_18,
  output [31:0] out_19,
  output [31:0] out_20,
  output [31:0] out_21,
  output [31:0] out_22,
  output [31:0] out_23,
  output [31:0] out_24,
  output [31:0] out_25,
  output [31:0] out_26,
  output [31:0] out_27,
  output [31:0] out_28,
  output [31:0] out_29,
  output [31:0] out_30,
  output [31:0] out_31,
  output [31:0] out_32,
  output [31:0] out_33,
  output [31:0] out_34,
  output [31:0] out_35
);

  wire decoder_1_out0, decoder_1_out1, decoder_1_out2, decoder_1_out3, decoder_1_out4, decoder_1_out5,
       decoder_1_out6, decoder_1_out7, decoder_1_out8, decoder_1_out9, decoder_1_out10, decoder_1_out11,
       decoder_1_out12, decoder_1_out13, decoder_1_out14, decoder_1_out15, decoder_1_out16, decoder_1_out17,
       decoder_1_out18, decoder_1_out19, decoder_1_out20, decoder_1_out21, decoder_1_out22, decoder_1_out23,
       decoder_1_out24, decoder_1_out25, decoder_1_out26, decoder_1_out27, decoder_1_out28, decoder_1_out29,
       decoder_1_out30, decoder_1_out31, not_1_out, priority_encoder_1_en_out, priority_encoder_2_en_out,
       priority_encoder_3_en_out, priority_encoder_4_en_out, priority_encoder_5_en_out,
       priority_encoder_6_en_out, priority_encoder_7_en_out, priority_encoder_8_en_out;
  wire [1:0] priority_encoder_1_out, priority_encoder_2_out, priority_encoder_3_out, priority_encoder_4_out,
       priority_encoder_5_out, priority_encoder_6_out, priority_encoder_7_out, priority_encoder_8_out;

  not not_1 (not_1_out, RD1_not);
  Decoder #(.select(5)) decoder_1 (
    .out0(decoder_1_out0), .out1(decoder_1_out1), .out2(decoder_1_out2), .out3(decoder_1_out3),
    .out4(decoder_1_out4), .out5(decoder_1_out5), .out6(decoder_1_out6), .out7(decoder_1_out7),
    .out8(decoder_1_out8), .out9(decoder_1_out9), .out10(decoder_1_out10), .out11(decoder_1_out11),
    .out12(decoder_1_out12), .out13(decoder_1_out13), .out14(decoder_1_out14), .out15(decoder_1_out15),
    .out16(decoder_1_out16), .out17(decoder_1_out17), .out18(decoder_1_out18), .out19(decoder_1_out19),
    .out20(decoder_1_out20), .out21(decoder_1_out21), .out22(decoder_1_out22), .out23(decoder_1_out23),
    .out24(decoder_1_out24), .out25(decoder_1_out25), .out26(decoder_1_out26), .out27(decoder_1_out27),
    .out28(decoder_1_out28), .out29(decoder_1_out29), .out30(decoder_1_out30), .out31(decoder_1_out31),
    .sel(Raddr1), .en(not_1_out));
  Priority_Encoder #(.select(2)) priority_encoder_1 (
    .in0(decoder_1_out0), .in1(decoder_1_out1), .in2(decoder_1_out2), .in3(decoder_1_out3),
    .out(priority_encoder_1_out), .en_out(priority_encoder_1_en_out));  // open: gs, en_in
  Priority_Encoder #(.select(2)) priority_encoder_2 (
    .in0(decoder_1_out4), .in1(decoder_1_out5), .in2(decoder_1_out6), .in3(decoder_1_out7),
    .out(priority_encoder_2_out), .en_out(priority_encoder_2_en_out));  // open: gs, en_in
  Priority_Encoder #(.select(2)) priority_encoder_3 (
    .in0(decoder_1_out8), .in1(decoder_1_out9), .in2(decoder_1_out10), .in3(decoder_1_out11),
    .out(priority_encoder_3_out), .en_out(priority_encoder_3_en_out));  // open: gs, en_in
  Priority_Encoder #(.select(2)) priority_encoder_4 (
    .in0(decoder_1_out12), .in1(decoder_1_out13), .in2(decoder_1_out14), .in3(decoder_1_out15),
    .out(priority_encoder_4_out), .en_out(priority_encoder_4_en_out));  // open: gs, en_in
  Priority_Encoder #(.select(2)) priority_encoder_5 (
    .in0(decoder_1_out16), .in1(decoder_1_out17), .in2(decoder_1_out18), .in3(decoder_1_out19),
    .out(priority_encoder_5_out), .en_out(priority_encoder_5_en_out));  // open: gs, en_in
  Priority_Encoder #(.select(2)) priority_encoder_6 (
    .in0(decoder_1_out20), .in1(decoder_1_out21), .in2(decoder_1_out22), .in3(decoder_1_out23),
    .out(priority_encoder_6_out), .en_out(priority_encoder_6_en_out));  // open: gs, en_in
  Priority_Encoder #(.select(2)) priority_encoder_7 (
    .in0(decoder_1_out24), .in1(decoder_1_out25), .in2(decoder_1_out26), .in3(decoder_1_out27),
    .out(priority_encoder_7_out), .en_out(priority_encoder_7_en_out));  // open: gs, en_in
  Priority_Encoder #(.select(2)) priority_encoder_8 (
    .in0(decoder_1_out28), .in1(decoder_1_out29), .in2(decoder_1_out30), .in3(decoder_1_out31),
    .out(priority_encoder_8_out), .en_out(priority_encoder_8_en_out));  // open: gs, en_in
  // FourReg_RegisterFile fourreg_registerfile_1: pin names not known; wires that end beside it: out_4, out_5, out_6, out_7
  // FourReg_RegisterFile fourreg_registerfile_2: pin names not known; wires that end beside it: out_8, out_9, out_10, out_11
  // FourReg_RegisterFile fourreg_registerfile_3: pin names not known; wires that end beside it: out_12, out_13, out_14, out_15
  // FourReg_RegisterFile fourreg_registerfile_4: pin names not known; wires that end beside it: out_16, out_17, out_18, out_19
  // FourReg_RegisterFile fourreg_registerfile_5: pin names not known; wires that end beside it: out_20, out_21, out_22, out_23
  // FourReg_RegisterFile fourreg_registerfile_6: pin names not known; wires that end beside it: out_24, out_25, out_26, out_27
  // FourReg_RegisterFile fourreg_registerfile_7: pin names not known; wires that end beside it: out_28, out_29, out_30, out_31
  // FourReg_RegisterFile fourreg_registerfile_8: pin names not known; wires that end beside it: out_32, out_33, out_34, out_35
endmodule

module FourReg_RegisterFile (
  input  ck,
  input  [31:0] i,
  input  [1:0] Raddr1,
  input  RD1_not,
  input  WR_not,
  input  [1:0] Waddr,
  input  RD2_not,
  input  [1:0] Raddr2,
  output [31:0] st_0,
  output [31:0] st_1,
  output [31:0] st_2,
  output [31:0] st_3,
  output [31:0] U2,
  output [31:0] U1,
  output [3:0] leds
);

  wire not_1_out, not_2_out, not_15_out, rd1_led_0, rd1_led_1, rd1_led_2, rd1_led_3, rd2_led_0, rd2_led_1,
       rd2_led_2, rd2_led_3, wr_led_0, wr_led_1, wr_led_2, wr_led_3;
  wire [2:0] not_11_out, not_12_out, not_13_out, not_14_out;

  Decoder #(.select(2)) decoder_1 (
    .out0(rd1_led_0), .out1(rd1_led_1), .out2(rd1_led_2), .out3(rd1_led_3), .sel(Raddr1), .en(not_1_out));
  not not_1 (not_1_out, RD1_not);
  Decoder #(.select(2)) decoder_2 (
    .out0(rd2_led_0), .out1(rd2_led_1), .out2(rd2_led_2), .out3(rd2_led_3), .sel(Raddr2), .en(not_2_out));
  not not_2 (not_2_out, RD2_not);
  or or_1 (leds[0], rd1_led_0, rd2_led_0, wr_led_0);
  or or_2 (leds[1], rd1_led_1, rd2_led_1, wr_led_1);
  or or_3 (leds[2], rd1_led_2, rd2_led_2, wr_led_2);
  or or_4 (leds[3], rd1_led_3, rd2_led_3, wr_led_3);
  not not_3 (not_11_out[1], rd1_led_0);
  not not_4 (not_12_out[1], rd1_led_1);
  not not_5 (not_13_out[1], rd1_led_2);
  not not_6 (not_14_out[1], rd1_led_3);
  not not_7 (not_11_out[2], rd2_led_0);
  not not_8 (not_12_out[2], rd2_led_1);
  not not_9 (not_13_out[2], rd2_led_2);
  not not_10 (not_14_out[2], rd2_led_3);
  register_main register_main_1 (.D(i), .CK(ck), .reg_ctrl(not_11_out), .state(st_0), .U1(U1), .U2(U2));
  register_main register_main_2 (.D(i), .CK(ck), .reg_ctrl(not_12_out), .state(st_1), .U1(U1), .U2(U2));
  register_main register_main_3 (.D(i), .CK(ck), .reg_ctrl(not_13_out), .state(st_2), .U1(U1), .U2(U2));
  register_main register_main_4 (.D(i), .CK(ck), .reg_ctrl(not_14_out), .state(st_3), .U1(U1), .U2(U2));
  not not_11 (not_11_out[0], wr_led_0);
  not not_12 (not_12_out[0], wr_led_1);
  not not_13 (not_13_out[0], wr_led_2);
  not not_14 (not_14_out[0], wr_led_3);
  Decoder #(.select(2)) decoder_3 (
    .out0(wr_led_0), .out1(wr_led_1), .out2(wr_led_2), .out3(wr_led_3), .sel(Waddr), .en(not_15_out));
  not not_15 (not_15_out, WR_not);
endmodule

module test (
  input  [1:0] in_1,
  input  [1:0] in_2,
  input  in_3,
  input  in_4,
  input  [31:0] in_5,
  input  in_6,
  input  [1:0] in_7,
  output [31:0] out_8,
  output [31:0] out_9
);

  wire clock_1_out;
  wire [31:0] fourreg_registerfile_1_st_0, fourreg_registerfile_1_st_1, fourreg_registerfile_1_st_2,
       fourreg_registerfile_1_st_3;

  DotMatrix #(.matrixcols(1), .matrixrows(4)) dotmatrix_1 ();  // open: col0
  FourReg_RegisterFile fourreg_registerfile_1 (
    .Raddr1(in_1), .Waddr(in_2), .WR_not(in_4), .ck(clock_1_out), .Raddr2(in_7), .RD1_not(in_3),
    .RD2_not(in_6), .i(in_5), .U2(out_9), .U1(out_8), .st_0(fourreg_registerfile_1_st_0),
    .st_1(fourreg_registerfile_1_st_1), .st_2(fourreg_registerfile_1_st_2), .st_3(fourreg_registerfile_1_st_3));  // open: leds
  // Probe on fourreg_registerfile_1_st_0
  // Probe on fourreg_registerfile_1_st_1
  // Probe on fourreg_registerfile_1_st_2
  // Probe on fourreg_registerfile_1_st_3
  Clock clock_1 (.out(clock_1_out));
endmodule
