// Logisim project BCD_encoder.circ as structural Verilog: 2 circuits, main circuit main
module main (
  input  [3:0] in_1
);

  _7_Segment_Display u_7_segment_display_1 ();  // open: g, f, a, b, e, d, c, dp
  // BCD_to_7_Segment_decoder bcd_to_7_segment_decoder_1: pin names not known; wires that end beside it: in_1
  Hex_Digit_Display hex_digit_display_1 (.value(in_1));  // open: dp
endmodule

module blocco_encoder (
  input  [3:0] in_1,
  output [6:0] out_2
);
endmodule
