// Logisim project chip_select.circ as structural Verilog: 2 circuits, main circuit main
module main (
  input  [31:0] ADD,
  input  WE,
  input  [7:0] DATA
);

  wire and_1_out, and_2_out, clock_1_out, cs_1_cs_not_1, cs_1_cs_not_2, not_1_out, not_2_out;

  not not_1 (not_1_out, cs_1_cs_not_1);
  cs cs_1 (
    .BA31(ADD[31]), .in_2(ADD[30]), .BA29(ADD[29]), .in_4(ADD[28]), .BA27(ADD[27]), .in_6(ADD[26]),
    .BA25(ADD[25]), .CS_not_1(cs_1_cs_not_1), .CS_not_2(cs_1_cs_not_2));
  not not_2 (not_2_out, cs_1_cs_not_2);
  Clock clock_1 (.out(clock_1_out));
  RAM ram_1 (.addr(ADD[7:0]), .we(and_1_out), .clk(clock_1_out), .din(DATA));  // open: oe, dout
  and and_1 (and_1_out, WE, not_1_out);
  RAM ram_2 (.addr(ADD[7:0]), .we(and_2_out), .clk(clock_1_out), .din(DATA));  // open: oe, dout
  and and_2 (and_2_out, WE, not_2_out);

  // Notes on the sheet:
  //   CS
  //   i
  //   i
  //   RAM1
  //   RAM2
endmodule

module cs (
  input  BA31,
  input  in_2,
  input  BA29,
  input  in_4,
  input  BA27,
  input  in_6,
  input  BA25,
  output CS_not_1,
  output CS_not_2
);

  wire not_1_out, not_2_out, not_3_out, not_4_out;

  not not_1 (not_1_out, in_4);
  not not_2 (not_2_out, BA27);
  not not_3 (not_3_out, BA29);
  not not_4 (not_4_out, BA25);
  or or_1 (CS_not_1, not_1_out, not_2_out);
  or or_2 (CS_not_2, not_3_out, BA27, not_4_out);
endmodule
