// Logisim project mini_udc.circ as structural Verilog: 6 circuits, main circuit main
module main (
  input  RESET,
  input  COP,
  input  [2:0] in_3,
  input  in_4,
  input  [31:0] in_5,
  input  [31:0] in_6,
  output [31:0] out_7
);

  wire CK, udc_1_m, udc_1_we_ab, udc_1_we_c;
  wire [2:0] alu_main_1_out_flags;
  wire [31:0] A_u, alu_main_1_u, B_u;

  Clock clock_1 (.out(CK));
  udc udc_1 (
    .Reset_not(RESET), .SF(alu_main_1_out_flags[1]), .OP(COP), .CK(CK), .WE_C(udc_1_we_c),
    .WE_AB(udc_1_we_ab), .M(udc_1_m));
  ThirtyTwoBitRegister A (.i(in_5), .in_1(udc_1_we_ab), .in_3(CK), .u(A_u));
  ThirtyTwoBitRegister B (.i(in_6), .in_1(udc_1_we_ab), .in_3(CK), .u(B_u));
  alu_main alu_main_1 (
    .alu_ctrl(in_3), .A(A_u), .B(B_u), .M(udc_1_m), .CI(in_4), .U(alu_main_1_u),
    .out_flags(alu_main_1_out_flags));
  ThirtyTwoBitRegister C (.i(alu_main_1_u), .in_1(udc_1_we_c), .in_3(CK), .u(out_7));
endmodule

module udc (
  input  SF,
  input  OP,
  input  Reset_not,
  input  CK,
  output WE_C,
  output WE_AB,
  output M
);

  wire [2:0] register_1_q, udc_g_1_u;

  Register #(.width(3)) register_1 (.D(udc_g_1_u), .Q(register_1_q), .clk(CK));  // open: en, clr
  UDC_F udc_f_1 (.q(register_1_q), .i({Reset_not, OP, SF}), .u({M, WE_AB, WE_C}));
  UDC_G udc_g_1 (.q(register_1_q), .i({Reset_not, OP, SF}), .u(udc_g_1_u));

  // Notes on the sheet:
  //   # RETE SEQUENZIALE UDC
  //   S.P.
  //   S.F.
endmodule

module UDC_F (
  input  [2:0] q,
  input  [2:0] i,
  output [2:0] u
);

  wire and_1_out, and_2_out, and_3_out, and_4_out;

  and and_1 (and_1_out, q[1], ~i[2]);  // AND_Gate
  and and_2 (and_2_out, ~q[1], q[0], i[2]);  // AND_Gate
  and and_3 (and_3_out, q[1], ~i[2]);  // AND_Gate
  and and_4 (and_4_out, q[0], i[2]);
  or or_1 (u[1], and_1_out, and_2_out);
  or or_2 (u[2], and_3_out, and_4_out);

  assign u[0] = q[1];

  // Notes on the sheet:
  //   q2
  //   q1
  //   q0
  //   I2
  //   I1
  //   I0
endmodule

module UDC_G (
  input  [2:0] q,
  input  [2:0] i,
  output [2:0] u
);

  wire and_1_out, and_2_out, and_3_out, and_4_out, or_1_out, or_3_out;

  and and_1 (and_1_out, ~q[0], ~i[0], i[2]);  // AND_Gate
  and and_2 (and_2_out, ~q[1], ~q[0], i[2]);  // AND_Gate
  and and_3 (and_3_out, q[1], ~i[0], i[2]);  // AND_Gate
  and and_4 (and_4_out, ~q[1], i[2], i[1]);  // AND_Gate
  and and_5 (u[1], ~q[1], q[0], i[2]);  // AND_Gate
  and and_6 (u[2], q[1], i[0], i[2]);
  or or_1 (or_1_out, and_1_out, and_2_out);
  or or_2 (u[0], or_1_out, or_3_out);
  or or_3 (or_3_out, and_3_out, and_4_out);

  // Notes on the sheet:
  //   q2
  //   q1
  //   q0
  //   I2
  //   I1
  //   I0
endmodule

module ThirtyTwoBitRegister (
  input  in_1,
  input  [31:0] i,
  input  in_3,
  output [31:0] u
);

  wire [31:0] multiplexer_1_out;

  Multiplexer #(.width(32)) multiplexer_1 (.in0(i), .in1(u), .out(multiplexer_1_out), .sel(in_1));
  Register #(.width(32)) register_1 (.D(multiplexer_1_out), .Q(u), .clk(in_3));  // open: en, clr
endmodule

module example (
  input  WE,
  input  in_2,
  input  in_3,
  input  in_4,
  input  in_5
);

  wire d_ff_1_q, d_ff_2_q, d_ff_3_q, d_ff_4_q, multiplexer_1_out, multiplexer_2_out, multiplexer_3_out,
       multiplexer_4_out;

  Multiplexer multiplexer_1 (.in0(in_2), .in1(d_ff_1_q), .out(multiplexer_1_out), .sel(WE));
  Multiplexer multiplexer_2 (.in0(in_3), .in1(d_ff_2_q), .out(multiplexer_2_out), .sel(WE));
  Multiplexer multiplexer_3 (.in0(in_4), .in1(d_ff_3_q), .out(multiplexer_3_out), .sel(WE));
  Multiplexer multiplexer_4 (.in0(in_5), .in1(d_ff_4_q), .out(multiplexer_4_out), .sel(WE));
  D_Flip_Flop d_ff_1 (.D(multiplexer_1_out), .Q(d_ff_1_q));  // open: clk, Qn, preset, reset
  D_Flip_Flop d_ff_2 (.D(multiplexer_2_out), .Q(d_ff_2_q));  // open: clk, Qn, preset, reset
  D_Flip_Flop d_ff_3 (.D(multiplexer_3_out), .Q(d_ff_3_q));  // open: clk, Qn, preset, reset
  D_Flip_Flop d_ff_4 (.D(multiplexer_4_out), .Q(d_ff_4_q));  // open: clk, Qn, preset, reset
endmodule
