// Logisim project analysis.circ as structural Verilog: 4 circuits, main circuit main
module main (
  input  in_1,
  output [1:0] out_2
);

  wire CK, not_1_out, wavegen_1_u;
  wire [1:0] counter_1_q, counter_2_q;

  Clock clock_1 (.out(CK));
  Counter #(.max('h3), .width(2)) counter_1 (
    .load(in_1), .D(2'b11), .Q(counter_1_q), .clk(CK));  // open: count, carry, up, clr
  waveGen wavegen_1 (
    .CK(CK), .in_2(1'b1), .in_3(1'b1), .in_4(1'b0), .in_5(1'b0), .in_6(1'b0), .in_7(1'b0), .in_8(1'b0),
    .U(wavegen_1_u));  // open: t0
  twoBitShifter twobitshifter_1 (.in_3(counter_1_q), .A0(counter_2_q[0]), .in_1(CK), .out_4(out_2));
  not not_1 (not_1_out, wavegen_1_u);
  Counter #(.max('h3), .width(2)) counter_2 (
    .load(in_1), .D(2'b01), .count(not_1_out), .Q(counter_2_q), .clk(CK));  // open: carry, up, clr

  // Other names for the same wires on the sheet: init = in_1
endmodule

module twoBitShifter (
  input  in_1,
  input  A0,
  input  [1:0] in_3,
  output [1:0] out_4
);

  wire multiplexer_1_out, multiplexer_2_out;

  Multiplexer multiplexer_1 (.in0(1'b0), .in1(in_3[1]), .out(multiplexer_1_out), .sel(A0));
  D_Flip_Flop d_ff_1 (.clk(in_1), .D(multiplexer_1_out), .Q(out_4[1]));  // open: Qn, preset, reset
  Multiplexer multiplexer_2 (.in0(out_4[1]), .in1(in_3[0]), .out(multiplexer_2_out), .sel(A0));
  D_Flip_Flop d_ff_2 (.clk(in_1), .D(multiplexer_2_out), .Q(out_4[0]));  // open: Qn, preset, reset

  // Other names for the same wires on the sheet: CK = in_1
endmodule

module test (
  input  in_1,
  input  in_2,
  input  [1:0] in_3,
  output [1:0] out_4
);

  twoBitShifter twobitshifter_1 (.in_3(in_3), .A0(in_1), .in_1(in_2), .out_4(out_4));
endmodule

module waveGen (
  input  t0,
  input  in_2,
  input  in_3,
  input  in_4,
  input  in_5,
  input  in_6,
  input  in_7,
  input  in_8,
  input  CK,
  output U
);

  wire decoder_1_out0, decoder_1_out1, decoder_1_out2, decoder_1_out3, decoder_1_out4, decoder_1_out5,
       decoder_1_out6, decoder_1_out7;
  wire [2:0] counter_1_q;

  Decoder #(.enable("false"), .select(3)) decoder_1 (
    .out0(decoder_1_out0), .out1(decoder_1_out1), .out2(decoder_1_out2), .out3(decoder_1_out3),
    .out4(decoder_1_out4), .out5(decoder_1_out5), .out6(decoder_1_out6), .out7(decoder_1_out7),
    .sel(counter_1_q));
  Counter #(.max('h7), .width(3)) counter_1 (.Q(counter_1_q), .clk(CK));  // open: load, D, count, carry, up, clr
  assign U = decoder_1_out0 ? t0 : 1'bz;  // Controlled_Buffer controlled_buffer_1
  assign U = decoder_1_out1 ? in_2 : 1'bz;  // Controlled_Buffer controlled_buffer_2
  assign U = decoder_1_out2 ? in_3 : 1'bz;  // Controlled_Buffer controlled_buffer_3
  assign U = decoder_1_out3 ? in_4 : 1'bz;  // Controlled_Buffer controlled_buffer_4
  assign U = decoder_1_out4 ? in_5 : 1'bz;  // Controlled_Buffer controlled_buffer_5
  assign U = decoder_1_out5 ? in_6 : 1'bz;  // Controlled_Buffer controlled_buffer_6
  assign U = decoder_1_out6 ? in_7 : 1'bz;  // Controlled_Buffer controlled_buffer_7
  assign U = decoder_1_out7 ? in_8 : 1'bz;  // Controlled_Buffer controlled_buffer_8
endmodule
