// Logisim project synthesis.circ as structural Verilog: 2 circuits, main circuit main
module main (
  output out_1
);

  wire CK, undriven;

  Clock clock_1 (.out(CK));
  Multiplexer multiplexer_1 ();  // open: in0, in1, out, sel
  impulseMonitor impulsemonitor_1 (.I(undriven), .in_1(CK), .U(out_1));
endmodule

module impulseMonitor (
  input  in_1,
  input  I,
  output U
);

  wire and_1_out, and_2_out, and_3_out, and_4_out, and_5_out, and_6_out, and_7_out, and_8_out, not_1_out,
       not_2_out, not_3_out, not_4_out, not_5_out, not_6_out, not_7_out, not_8_out, not_9_out, not_10_out,
       or_2_out, or_3_out, or_4_out, or_5_out, q0, q1, q2;

  and and_1 (and_1_out, q2, not_1_out);
  not not_1 (not_1_out, q0);
  not not_2 (not_2_out, q1);
  and and_2 (and_2_out, I, not_2_out, q0);
  not not_3 (not_3_out, q2);
  and and_3 (and_3_out, I, not_3_out, not_4_out);
  not not_4 (not_4_out, q0);
  not not_5 (not_5_out, I);
  not not_6 (not_6_out, q2);
  and and_4 (and_4_out, not_5_out, not_6_out, not_7_out, q0);
  not not_7 (not_7_out, q1);
  not not_8 (not_8_out, I);
  and and_5 (and_5_out, not_8_out, q2, not_9_out);
  not not_9 (not_9_out, q0);
  and and_6 (and_6_out, q1, not_10_out);
  not not_10 (not_10_out, q0);
  and and_7 (and_7_out, I, q2);
  and and_8 (and_8_out, I, q0);
  D_Flip_Flop d_ff_1 (.clk(in_1), .D(or_5_out), .Q(q2));  // open: Qn, preset, reset
  D_Flip_Flop d_ff_2 (.clk(in_1), .D(or_4_out), .Q(q1));  // open: Qn, preset, reset
  D_Flip_Flop d_ff_3 (.clk(in_1), .D(or_2_out), .Q(q0));  // open: Qn, preset, reset
  or or_1 (U, and_1_out, q1);
  or or_2 (or_2_out, and_2_out, and_3_out);
  or or_3 (or_3_out, and_4_out, and_5_out);
  or or_4 (or_4_out, or_3_out, and_6_out);
  or or_5 (or_5_out, and_7_out, and_8_out);

  // Other names for the same wires on the sheet: CK = in_1

  // Notes on the sheet:
  //   - attiva: n. dispari di impulsi da 1CK
  //   - disattiva: n. pari di impulsi da 1 CK
  //   q2
  //   # RETE SEQUENZIALE SINCRONA 2024-05-04
  //   q1
  //   q0
  //   # SP
  //   # RETE F #
  //   # RETE G #
  //   # REGISTRI #
  //   Q0
  //   Q1
  //   Q2
  //   # SF
endmodule
