// Logisim project test.circ as structural Verilog: 1 circuit, main circuit main
module main (
  input  in_1,
  input  in_2,
  input  in_3,
  input  in_4,
  input  in_5,
  input  in_6,
  input  t3,
  input  in_8,
  input  in_9,
  input  in_10,
  input  in_11,
  input  [1:0] in_12,
  input  in_13,
  output out_14,
  output out_15,
  output [1:0] out_16,
  output out_17
);

  wire clock_1_out, clock_2_out, clock_3_out, clock_4_out, controlled_buffer_1_out, d_ff_1_q, d_ff_2_q,
       decoder_1_out0, decoder_1_out1, decoder_1_out2, decoder_1_out3, decoder_2_out0, decoder_3_out0,
       decoder_3_out1, decoder_3_out2, decoder_3_out3, multiplexer_2_out, multiplexer_3_out,
       multiplexer_4_out, multiplexer_5_out, not_1_out, or_1_out;
  wire [1:0] counter_1_q, counter_2_q;

  Clock clock_1 (.out(clock_1_out));
  Counter #(.max('h3), .width(2)) counter_1 (
    .Q(counter_1_q), .clk(clock_2_out));  // open: load, D, count, carry, up, clr
  Clock clock_2 (.out(clock_2_out));
  Decoder #(.enable("false"), .select(2)) decoder_1 (
    .out0(decoder_1_out0), .out1(decoder_1_out1), .out2(decoder_1_out2), .out3(decoder_1_out3),
    .sel(counter_1_q));
  Clock clock_3 (.out(clock_3_out));
  Multiplexer multiplexer_1 (.in0(in_9), .in1(in_10), .out(out_17), .sel(in_11));
  not not_1 (not_1_out, in_3);
  Clock clock_4 (.out(clock_4_out));
  Decoder #(.enable("false"), .select(2)) decoder_2 (
    .out0(decoder_2_out0), .sel(counter_2_q));  // open: out1, out2, out3
  Counter #(.max('h3), .width(2)) counter_2 (
    .Q(counter_2_q), .clk(clock_3_out));  // open: load, D, count, carry, up, clr
  D_Flip_Flop d_ff_1 (.clk(clock_1_out), .D(in_1), .Q(d_ff_1_q));  // open: Qn, preset, reset
  D_Flip_Flop d_ff_2 (.clk(clock_1_out), .D(in_2), .Q(d_ff_2_q));  // open: Qn, preset, reset
  Counter #(.max('h3), .width(2)) counter_3 (
    .count(not_1_out), .Q(out_16), .clk(clock_4_out));  // open: load, D, carry, up, clr
  assign controlled_buffer_1_out = decoder_1_out0 ? in_4 : 1'bz;  // Controlled_Buffer controlled_buffer_1
  assign controlled_buffer_1_out = decoder_1_out1 ? in_5 : 1'bz;  // Controlled_Buffer controlled_buffer_2
  assign controlled_buffer_1_out = decoder_1_out2 ? in_6 : 1'bz;  // Controlled_Buffer controlled_buffer_3
  assign controlled_buffer_1_out = decoder_1_out3 ? t3 : 1'bz;  // Controlled_Buffer controlled_buffer_4
  Decoder #(.enable("false"), .select(2)) decoder_3 (
    .out0(decoder_3_out0), .out1(decoder_3_out1), .out2(decoder_3_out2), .out3(decoder_3_out3), .sel(in_12));
  // Digital_Oscilloscope digital_oscilloscope_1: pin names not known; wires that end beside it: clock_4_out, controlled_buffer_1_out
  LED led_1 (.in(controlled_buffer_1_out));
  Multiplexer multiplexer_2 (.in0(1'b0), .in1(in_8), .out(multiplexer_2_out), .sel(decoder_2_out0));
  Multiplexer multiplexer_3 (.out(multiplexer_3_out));  // open: in0, in1, sel
  Multiplexer multiplexer_4 (.out(multiplexer_4_out));  // open: in0, in1, sel
  Multiplexer multiplexer_5 (.out(multiplexer_5_out));  // open: in0, in1, sel
  D_Flip_Flop d_ff_3 (.clk(clock_1_out), .D(d_ff_1_q), .Q(out_14));  // open: Qn, preset, reset
  D_Flip_Flop d_ff_4 (.clk(clock_1_out), .D(d_ff_2_q), .Q(out_15));  // open: Qn, preset, reset
  or or_1 (or_1_out, multiplexer_2_out, multiplexer_3_out, multiplexer_4_out, multiplexer_5_out);
  Multiplexer multiplexer_6 (.in1(decoder_3_out3), .sel(in_13));  // open: in0, out

  // Notes on the sheet:
  //   t0
endmodule
