// Logisim project ESERCITAZIONE.circ as structural Verilog: 4 circuits, main circuit main
module main (
);

  wire and_1_out, and_2_out, and_3_out, and_4_out, and_5_out, clock_1_out, clock_2_out, decoder_1_out0,
       decoder_1_out1, decoder_1_out2, decoder_1_out3, ha_1_c, ha_1_s, multiplexer_1_out, not_1_out,
       not_2_out, not_3_out, or_1_out, or_2_out, or_3_out, xor_1_out;
  wire [5:0] counter_1_q;

  Counter #(.max('h3f), .width(6)) counter_1 (
    .clk(clock_1_out), .Q(counter_1_q));  // open: clr, load, up, count, D, carry
  Clock clock_1 (.out(clock_1_out));
  Decoder #(.enable("false"), .select(2)) decoder_1 (
    .out0(decoder_1_out0), .out1(decoder_1_out1), .out2(decoder_1_out2), .out3(decoder_1_out3),
    .sel(counter_1_q[3:2]));
  not not_1 (not_1_out, counter_1_q[0]);
  and and_1 (and_1_out, not_1_out, not_2_out);
  not not_2 (not_2_out, counter_1_q[3]);
  not not_3 (not_3_out, counter_1_q[0]);
  and and_2 (and_2_out, not_3_out, counter_1_q[1]);
  and and_3 (and_3_out, counter_1_q[0], counter_1_q[3]);
  and and_4 (and_4_out, counter_1_q[0], counter_1_q[4]);
  and and_5 (and_5_out, counter_1_q[0], counter_1_q[5]);
  or or_1 (or_1_out, counter_1_q[1], decoder_1_out0, decoder_1_out1);
  HA ha_1 (.A(decoder_1_out3), .B(counter_1_q[4]), .S(ha_1_s), .C(ha_1_c));
  or or_2 (or_2_out, and_1_out, and_2_out, and_3_out, and_4_out, and_5_out);
  or or_3 (or_3_out, decoder_1_out2, ha_1_s, ha_1_c, counter_1_q[5]);
  Multiplexer multiplexer_1 (.in0(or_1_out), .in1(or_3_out), .out(multiplexer_1_out), .sel(counter_1_q[0]));
  xor xor_1 (xor_1_out, multiplexer_1_out, or_2_out);
  Clock clock_2 (.out(clock_2_out));
  // Digital_Oscilloscope digital_oscilloscope_1: pin names not known; wires that end beside it: clock_2_out, xor_1_out

  // Notes on the sheet:
  //   # 17/3/2023
  //   # ESERCITAZIONE RETI COMBINATORIE
  //   # Componenti: Decoder, HalfAdder, Mux, OR
  //   x0
  //   x1
  //   y0
  //   y3
  //   A
  //   i0
  //   i1
endmodule

module HA (
  input  A,
  input  B,
  output S,
  output C
);

  xor xor_1 (S, A, B);
  and and_1 (C, A, B);

  // Notes on the sheet:
  //   # HALF ADDER
endmodule

module bcd (
  input  [5:0] in_1,
  output [3:0] out_2,
  output [3:0] out_3
);

  // Binary_to_BCD_converter binary_to_bcd_converter_1: pin names not known; wires that end beside it: {3'b000, in_1}, out_2, out_3

  // Notes on the sheet:
  //   # BINARY TO BCD CIRCUIT
endmodule

module contatore (
);

  Counter counter_1 ();  // open: clr, load, up, count, clk, D, carry, Q
endmodule
