// Logisim project DATAPATH.circ as structural Verilog: 3 circuits, main circuit main
module main (
  input  [4:0] in_1,
  input  [2:0] in_2,
  input  in_3,
  input  [31:0] in_4,
  input  [31:0] in_5,
  input  [31:0] in_6,
  input  [2:0] WE,
  input  [2:0] B,
  input  [2:0] C,
  input  [2:0] PC,
  input  [2:0] TEMP,
  input  [2:0] IAR,
  input  [2:0] MAR,
  input  [2:0] MDR,
  input  [1:0] MUX,
  input  [31:0] in_16,
  input  [31:0] in_17,
  input  CLOCK,
  output [1:0] FLAG,
  output out_20,
  output [31:0] out_21,
  output [31:0] out_22,
  output [31:0] out_23
);

  wire [31:0] main_1_p7, multiplexer_2_out, n32b_register_8_out_6, register_file_1_out_6,
       register_file_1_out_7;

  _32b_register u_32b_register_1 (
    .OE1(WE[1]), .OE2(WE[2]), .WE(WE[0]), .CK(CLOCK), .in_5(register_file_1_out_6), .out_6(out_21),
    .out_7(in_17));
  _32b_register u_32b_register_2 (
    .OE1(B[1]), .OE2(B[2]), .WE(B[0]), .CK(CLOCK), .in_5(register_file_1_out_7), .out_6(out_21), .out_7(in_17));
  Multiplexer #(.width(32), .enable("false")) multiplexer_1 (.in0(in_17), .in1(in_17), .out(out_22), .sel(MUX[1]));
  // SuperAlu_main main_1: pin names not known; wires that end beside it: in_2, out_21, in_17, in_1, FLAG, in_3, main_1_p7, out_20
  _32b_register u_32b_register_3 (
    .OE1(PC[1]), .OE2(PC[2]), .WE(PC[0]), .CK(CLOCK), .in_5(main_1_p7), .out_6(out_21), .out_7(in_17));
  _32b_register u_32b_register_4 (
    .OE1(TEMP[1]), .OE2(TEMP[2]), .WE(TEMP[0]), .CK(CLOCK), .in_5(main_1_p7), .out_6(out_21), .out_7(in_17));
  _32b_register u_32b_register_5 (
    .OE1(IAR[1]), .OE2(IAR[2]), .WE(IAR[0]), .CK(CLOCK), .in_5(main_1_p7), .out_6(out_21), .out_7(in_17));
  _32b_register u_32b_register_6 (
    .OE1(MAR[1]), .OE2(MAR[2]), .WE(MAR[0]), .CK(CLOCK), .in_5(main_1_p7), .out_6(out_21), .out_7(in_17));
  _32b_register u_32b_register_7 (
    .OE1(MDR[1]), .OE2(MDR[2]), .WE(MDR[0]), .CK(CLOCK), .in_5(multiplexer_2_out), .out_6(out_21),
    .out_7(in_17));
  REGISTER_FILE register_file_1 (
    .out_6(register_file_1_out_6), .out_7(register_file_1_out_7), .in_1(in_4), .in_2(in_5), .in_3(in_6),
    .in_4(n32b_register_8_out_6), .in_5(CLOCK));
  Multiplexer #(.width(32), .enable("false")) multiplexer_2 (
    .in0(main_1_p7), .in1(in_16), .out(multiplexer_2_out), .sel(MUX[0]));
  _32b_register u_32b_register_8 (
    .OE1(C[1]), .WE(C[0]), .CK(CLOCK), .in_5(main_1_p7), .out_6(n32b_register_8_out_6));  // open: OE2, out_7

  assign out_23 = out_21;

  // Notes on the sheet:
  //   ALU CTRL
  //   WERF
  //   OE1RF
  //   OE2RF
  //   A
  //   O1
  //   O2
  //   DATI
  //   IND
  //   S1
  //   S2
  //   A
  //   B
  //   INDIRIZZI
  //   DATI OUT
  //   PC
  //   TEMP
  //   IAR
  //   MAR
  //   MDR
  //   DATI INPUT
endmodule

module REGISTER_FILE (
  input  [31:0] in_1,
  input  [31:0] in_2,
  input  [31:0] in_3,
  input  [31:0] in_4,
  input  in_5,
  output [31:0] out_6,
  output [31:0] out_7
);

  _8reg u_8reg_1 (
    .out_6(out_6), .out_7(out_7), .WE(in_1[7:0]), .OE1(in_2[7:0]), .OE2(in_3[7:0]), .in_4(in_4), .in_5(in_5));
  _8reg u_8reg_2 (
    .out_6(out_6), .out_7(out_7), .WE(in_1[15:8]), .OE1(in_2[15:8]), .OE2(in_3[15:8]), .in_4(in_4),
    .in_5(in_5));
  _8reg u_8reg_3 (
    .out_6(out_6), .out_7(out_7), .WE(in_1[23:16]), .OE1(in_2[23:16]), .OE2(in_3[23:16]), .in_4(in_4),
    .in_5(in_5));
  _8reg u_8reg_4 (
    .out_6(out_6), .out_7(out_7), .WE(in_1[31:24]), .OE1(in_2[31:24]), .OE2(in_3[31:24]), .in_4(in_4),
    .in_5(in_5));
endmodule

module _8reg (
  input  [7:0] WE,
  input  [7:0] OE1,
  input  [7:0] OE2,
  input  [31:0] in_4,
  input  in_5,
  output [31:0] out_6,
  output [31:0] out_7
);

  _32b_register u_32b_register_1 (
    .OE1(OE1[0]), .OE2(OE2[0]), .WE(WE[0]), .CK(in_5), .in_5(in_4), .out_6(out_6), .out_7(out_7));
  _32b_register u_32b_register_2 (
    .OE1(OE1[1]), .OE2(OE2[1]), .WE(WE[1]), .CK(in_5), .in_5(in_4), .out_6(out_6), .out_7(out_7));
  _32b_register u_32b_register_3 (
    .OE1(OE1[2]), .OE2(OE2[2]), .WE(WE[2]), .CK(in_5), .in_5(in_4), .out_6(out_6), .out_7(out_7));
  _32b_register u_32b_register_4 (
    .OE1(OE1[3]), .OE2(OE2[3]), .WE(WE[3]), .CK(in_5), .in_5(in_4), .out_6(out_6), .out_7(out_7));
  _32b_register u_32b_register_5 (
    .OE1(OE1[4]), .OE2(OE2[4]), .WE(WE[4]), .CK(in_5), .in_5(in_4), .out_6(out_6), .out_7(out_7));
  _32b_register u_32b_register_6 (
    .OE1(OE1[5]), .OE2(OE2[5]), .WE(WE[5]), .CK(in_5), .in_5(in_4), .out_6(out_6), .out_7(out_7));
  _32b_register u_32b_register_7 (
    .OE1(OE1[6]), .OE2(OE2[6]), .WE(WE[6]), .CK(in_5), .in_5(in_4), .out_6(out_6), .out_7(out_7));
  _32b_register u_32b_register_8 (
    .OE1(OE1[7]), .OE2(OE2[7]), .WE(WE[7]), .CK(in_5), .in_5(in_4), .out_6(out_6), .out_7(out_7));
endmodule
