// Logisim project BCD_ENCODER.circ as structural Verilog: 2 circuits, main circuit main
module main (
  input  [3:0] in_1,
  output [3:0] out_2,
  output [3:0] out_3
);

  wire or_1_out, or_2_out, or_3_out, or_4_out, or_6_out, or_7_out, or_8_out, or_9_out, or_10_out, or_11_out,
       or_12_out, or_13_out, or_14_out, or_15_out, or_16_out, or_17_out, or_18_out, or_19_out, or_20_out,
       or_21_out;

  or or_1 (or_1_out, ~in_1[0], in_1[1], in_1[2], in_1[3]);  // OR_Gate
  or or_2 (or_2_out, in_1[0], in_1[1], ~in_1[2], in_1[3]);  // OR_Gate
  or or_3 (or_3_out, ~in_1[0], in_1[1], ~in_1[2], in_1[3]);  // OR_Gate
  or or_4 (or_4_out, in_1[0], ~in_1[1], ~in_1[2], in_1[3]);  // OR_Gate
  or or_5 (out_3[1], in_1[0], ~in_1[1], in_1[2], in_1[3]);  // OR_Gate
  or or_6 (or_6_out, ~in_1[0], in_1[1], in_1[2], in_1[3]);  // OR_Gate
  or or_7 (or_7_out, in_1[0], in_1[1], ~in_1[2], in_1[3]);  // OR_Gate
  or or_8 (or_8_out, ~in_1[0], ~in_1[1], ~in_1[2], in_1[3]);  // OR_Gate
  or or_9 (or_9_out, ~in_1[0], in_1[1], in_1[2], in_1[3]);  // OR_Gate
  or or_10 (or_10_out, ~in_1[0], ~in_1[1], in_1[2], in_1[3]);  // OR_Gate
  or or_11 (or_11_out, in_1[0], in_1[1], ~in_1[2], in_1[3]);  // OR_Gate
  or or_12 (or_12_out, ~in_1[0], in_1[1], ~in_1[2], in_1[3]);  // OR_Gate
  or or_13 (or_13_out, ~in_1[0], ~in_1[1], ~in_1[2], in_1[3]);  // OR_Gate
  or or_14 (or_14_out, ~in_1[0], in_1[1], in_1[2], ~in_1[3]);  // OR_Gate
  or or_15 (or_15_out, ~in_1[0], in_1[1], in_1[2], in_1[3]);  // OR_Gate
  or or_16 (or_16_out, in_1[0], ~in_1[1], in_1[2], in_1[3]);  // OR_Gate
  or or_17 (or_17_out, ~in_1[0], ~in_1[1], in_1[2], in_1[3]);  // OR_Gate
  or or_18 (or_18_out, ~in_1[0], ~in_1[1], ~in_1[2], in_1[3]);  // OR_Gate
  or or_19 (or_19_out, in_1[0], in_1[1], in_1[2], in_1[3]);
  or or_20 (or_20_out, ~in_1[0], in_1[1], in_1[2], in_1[3]);  // OR_Gate
  or or_21 (or_21_out, ~in_1[0], ~in_1[1], ~in_1[2], in_1[3]);  // OR_Gate
  and and_1 (out_2[1], or_1_out, or_2_out);
  and and_2 (out_2[0], or_3_out, or_4_out);
  and and_3 (out_3[2], or_6_out, or_7_out, or_8_out);
  and and_4 (out_2[2], or_15_out, or_16_out, or_17_out, or_18_out);
  and and_5 (out_2[3], or_19_out, or_20_out, or_21_out);
  and and_6 (out_3[3], or_9_out, or_10_out, or_11_out, or_12_out, or_13_out, or_14_out);

  // Notes on the sheet:
  //   b3
  //   b0
  //   c
  //   d
  //   e
  //   f
  //   b
  //   g
  //   a
endmodule

module temp (
  input  [31:0] in_1
);

  wire [3:0] main_1_out_2, main_1_out_3;

  _7_Segment_Display u_7_segment_display_1 (
    .g(main_1_out_2[3]), .f(main_1_out_2[2]), .a(main_1_out_2[1]), .b(main_1_out_2[0]), .e(main_1_out_3[0]),
    .d(main_1_out_3[1]), .c(main_1_out_3[2]), .dp(main_1_out_3[3]));
  main main_1 (.in_1(in_1[3:0]), .out_2(main_1_out_2), .out_3(main_1_out_3));
endmodule
