// Logisim project DATAPATH.circ as structural Verilog: 8 circuits, main circuit main
module main (
  input  [2:0] in_1,
  input  [4:0] in_2,
  input  in_3,
  input  [31:0] in_4,
  input  [31:0] in_5,
  input  [31:0] in_6,
  input  [2:0] A,
  input  [2:0] B,
  input  [2:0] C,
  input  [2:0] PC,
  input  [2:0] TEMP,
  input  [2:0] IAR,
  input  [2:0] MAR,
  input  [2:0] MDR,
  input  [1:0] MUX,
  input  [31:0] in_16,
  input  [31:0] in_17,
  input  CLOCK,
  output [1:0] FLAG,
  output out_20,
  output [31:0] out_21,
  output [31:0] out_22,
  output [31:0] out_23
);

  wire l_32b_register_c8a703a4_1_p9, l_32b_register_c8a703a4_2_p7, thirtytwobitencoder_1_out_3,
       thirtytwobitencoder_2_out_3;
  wire [4:0] thirtytwobitencoder_1_out_2, thirtytwobitencoder_2_out_2;
  wire [31:0] l_32b_register_c8a703a4_1_p1, l_32b_register_c8a703a4_1_p2, l_32b_register_c8a703a4_7_p7,
       l_32b_register_c8a703a4_8_p1, main_1_out_8;

  // L_32b_register_c8a703a4 l_32b_register_c8a703a4_1: pin names not known; wires that end beside it: l_32b_register_c8a703a4_1_p1, l_32b_register_c8a703a4_1_p2, out_21, in_17, A[1], A[2], CLOCK, A[0], l_32b_register_c8a703a4_1_p9, l_32b_register_c8a703a4_1_p9
  // L_32b_register_c8a703a4 l_32b_register_c8a703a4_2: pin names not known; wires that end beside it: out_21, in_17, B[1], B[2], CLOCK, B[0], l_32b_register_c8a703a4_2_p7, l_32b_register_c8a703a4_2_p7
  RAM #(.addrWidth(5), .dataWidth(32)) ram_1 (
    .addr(thirtytwobitencoder_1_out_2), .oe(thirtytwobitencoder_1_out_3), .clk(CLOCK),
    .din(l_32b_register_c8a703a4_8_p1), .dout(l_32b_register_c8a703a4_1_p1));  // open: we
  thirtytwoBitEncoder thirtytwobitencoder_1 (
    .in_1(in_5), .out_2(thirtytwobitencoder_1_out_2), .out_3(thirtytwobitencoder_1_out_3));
  RAM #(.addrWidth(5), .dataWidth(32)) ram_2 (
    .addr(thirtytwobitencoder_2_out_2), .oe(thirtytwobitencoder_2_out_3), .clk(CLOCK),
    .din(l_32b_register_c8a703a4_8_p1), .dout(l_32b_register_c8a703a4_1_p2));  // open: we
  thirtytwoBitEncoder thirtytwobitencoder_2 (
    .in_1(in_6), .out_2(thirtytwobitencoder_2_out_2), .out_3(thirtytwobitencoder_2_out_3));
  Multiplexer #(.width(32)) multiplexer_1 (.in0(in_17), .in1(in_17), .out(out_22), .sel(MUX[1]));
  SuperAlu_main main_1 (
    .in_3(in_2), .in_4(out_21), .in_5(in_17), .out_8(main_1_out_8), .CF(FLAG), .in_7(in_3), .in_6(in_1),
    .out_10(out_20));  // open: _0___disattiva, in_1
  // L_32b_register_c8a703a4 l_32b_register_c8a703a4_3: pin names not known; wires that end beside it: out_21, in_17, PC[1], PC[2], CLOCK, PC[0], main_1_out_8
  // L_32b_register_c8a703a4 l_32b_register_c8a703a4_4: pin names not known; wires that end beside it: out_21, in_17, TEMP[1], TEMP[2], CLOCK, TEMP[0], main_1_out_8
  // L_32b_register_c8a703a4 l_32b_register_c8a703a4_5: pin names not known; wires that end beside it: out_21, in_17, IAR[1], IAR[2], CLOCK, IAR[0], main_1_out_8
  // L_32b_register_c8a703a4 l_32b_register_c8a703a4_6: pin names not known; wires that end beside it: out_21, in_17, MAR[1], MAR[2], CLOCK, MAR[0], main_1_out_8
  // L_32b_register_c8a703a4 l_32b_register_c8a703a4_7: pin names not known; wires that end beside it: out_21, in_17, MDR[1], MDR[2], CLOCK, MDR[0], l_32b_register_c8a703a4_7_p7
  Multiplexer #(.width(32)) multiplexer_2 (
    .in0(main_1_out_8), .in1(in_16), .out(l_32b_register_c8a703a4_7_p7), .sel(MUX[0]));
  // L_32b_register_c8a703a4 l_32b_register_c8a703a4_8: pin names not known; wires that end beside it: l_32b_register_c8a703a4_8_p1, C[1], CLOCK, C[0], main_1_out_8

  assign out_23 = out_21;

  // Notes on the sheet:
  //   ALU CTRL
  //   WERF
  //   OE1RF
  //   OE2RF
  //   O2
  //   IND
  //   O1
  //   WE
  //   DATI
  //   S1
  //   S2
  //   A
  //   B
  //   INDIRIZZI
  //   MDR
  //   DATI OUT
  //   PC
  //   TEMP
  //   IAR
  //   MAR
  //   DATI INPUT
endmodule

module REGISTER_FILE (
  input  [31:0] in_1,
  input  [31:0] in_2,
  input  [31:0] in_3,
  input  [31:0] in_4,
  input  in_5,
  output [31:0] out_6,
  output [31:0] out_7
);

  L_8reg_f7baeb64 l_8reg_f7baeb64_1 (
    .in_4(in_4), .OE2(in_3[7:0]), .OE1(in_2[7:0]), .WE(in_1[7:0]), .in_5(in_5), .out_6(out_6), .out_7(out_7));
  L_8reg_f7baeb64 l_8reg_f7baeb64_2 (
    .in_4(in_4), .OE2(in_3[15:8]), .OE1(in_2[15:8]), .WE(in_1[15:8]), .in_5(in_5), .out_6(out_6),
    .out_7(out_7));
  L_8reg_f7baeb64 l_8reg_f7baeb64_3 (
    .in_4(in_4), .OE2(in_3[23:16]), .OE1(in_2[23:16]), .WE(in_1[23:16]), .in_5(in_5), .out_6(out_6),
    .out_7(out_7));
  L_8reg_f7baeb64 l_8reg_f7baeb64_4 (
    .in_4(in_4), .OE2(in_3[31:24]), .OE1(in_2[31:24]), .WE(in_1[31:24]), .in_5(in_5), .out_6(out_6),
    .out_7(out_7));
endmodule

module L_8reg_f7baeb64 (
  input  [7:0] WE,
  input  [7:0] OE1,
  input  [7:0] OE2,
  input  [31:0] in_4,
  input  in_5,
  output [31:0] out_6,
  output [31:0] out_7
);
endmodule

module tests (
  input  [4:0] in_1,
  input  in_2,
  input  [31:0] in_3,
  input  [31:0] in_4
);

  wire [31:0] ram_1_dout;

  Priority_Encoder priority_encoder_1 ();  // open: in0, in1, in2, in3, in4, in5, in6, in7, out, en_in, gs, en_out
  Priority_Encoder priority_encoder_2 ();  // open: in0, in1, in2, in3, in4, in5, in6, in7, out, en_in, gs, en_out
  Priority_Encoder priority_encoder_3 ();  // open: in0, in1, in2, in3, in4, in5, in6, in7, out, en_in, gs, en_out
  // Probe on nothing
  RAM #(.addrWidth(5), .dataWidth(32)) ram_1 (
    .addr(in_1), .we(1'b1), .clk(in_2), .din(in_4), .dout(ram_1_dout));  // open: oe
endmodule

module eightBitEncoder (
  input  [7:0] I,
  output [2:0] U,
  output en
);

  wire priority_encoder_1_en_out;

  Priority_Encoder priority_encoder_1 (
    .in0(I[0]), .in1(I[1]), .in2(I[2]), .in3(I[3]), .in4(I[4]), .in5(I[5]), .in6(I[6]), .in7(I[7]), .out(U),
    .en_in(1'b1), .en_out(priority_encoder_1_en_out));  // open: gs
  not not_1 (en, priority_encoder_1_en_out);
endmodule

module thirtytwoBitEncoder (
  input  [31:0] in_1,
  output [4:0] out_2,
  output out_3
);

  wire eightbitencoder_1_en, eightbitencoder_2_en, eightbitencoder_3_en, eightbitencoder_4_en;
  wire [2:0] eightbitencoder_1_u, eightbitencoder_2_u, eightbitencoder_3_u, eightbitencoder_4_u;
  wire [4:0] adder_1_out, adder_2_out, adder_3_out;

  eightBitEncoder eightbitencoder_1 (.I(in_1[7:0]), .U(eightbitencoder_1_u), .en(eightbitencoder_1_en));
  eightBitEncoder eightbitencoder_2 (.I(in_1[15:8]), .U(eightbitencoder_2_u), .en(eightbitencoder_2_en));
  eightBitEncoder eightbitencoder_3 (.I(in_1[23:16]), .U(eightbitencoder_3_u), .en(eightbitencoder_3_en));
  eightBitEncoder eightbitencoder_4 (.I(in_1[31:24]), .U(eightbitencoder_4_u), .en(eightbitencoder_4_en));
  // Probe on eightbitencoder_1_u
  // Probe on eightbitencoder_2_u
  // Probe on eightbitencoder_3_u
  // Probe on eightbitencoder_4_u
  or or_1 (out_3, eightbitencoder_1_en, eightbitencoder_2_en, eightbitencoder_3_en, eightbitencoder_4_en);
  // Probe on adder_1_out
  Adder #(.width(5)) adder_1 (
    .a({2'b00, eightbitencoder_2_u}), .b(5'b01000), .out(adder_1_out), .cin(1'b0));  // open: cout
  // Probe on adder_2_out
  Adder #(.width(5)) adder_2 (
    .a({2'b00, eightbitencoder_3_u}), .b(5'b10000), .out(adder_2_out), .cin(1'b0));  // open: cout
  // Probe on adder_3_out
  Adder #(.width(5)) adder_3 (
    .a({2'b00, eightbitencoder_4_u}), .b(5'b11000), .out(adder_3_out), .cin(1'b0));  // open: cout
  assign out_2 = eightbitencoder_1_en ? {2'b00, eightbitencoder_1_u} : 5'bz;  // Controlled_Buffer controlled_buffer_1
  assign out_2 = eightbitencoder_2_en ? adder_1_out : 5'bz;  // Controlled_Buffer controlled_buffer_2
  assign out_2 = eightbitencoder_3_en ? adder_2_out : 5'bz;  // Controlled_Buffer controlled_buffer_3
  assign out_2 = eightbitencoder_4_en ? adder_3_out : 5'bz;  // Controlled_Buffer controlled_buffer_4
endmodule

module CleanDatapath (
  input  [2:0] in_1,
  input  [4:0] in_2,
  input  in_3,
  input  in_4,
  input  [31:0] in_5,
  input  [31:0] in_6,
  input  [31:0] in_7,
  input  [2:0] A,
  input  [2:0] B,
  input  [2:0] C,
  input  [2:0] PC,
  input  [2:0] TEMP,
  input  [2:0] IAR,
  input  [2:0] MAR,
  input  [2:0] MDR,
  input  [1:0] MUX,
  input  [31:0] in_17,
  input  [31:0] in_18,
  input  CLOCK,
  output [1:0] FLAG,
  output out_21,
  output [31:0] out_22,
  output [31:0] out_23,
  output [31:0] out_24
);

  wire rfencoderblock_1_oe1, rfencoderblock_1_oe2, rfencoderblock_1_we;
  wire [4:0] rfencoderblock_1_a1, rfencoderblock_1_a2;
  wire [31:0] l_32b_register_c8a703a4_1_p7, l_32b_register_c8a703a4_2_p7, l_32b_register_c8a703a4_7_p7,
       l_32b_register_c8a703a4_8_p1, main_1_out_8;

  Register #(.width(32)) register_1 ();  // open: D, en, clk, Q, clr
  // L_32b_register_c8a703a4 l_32b_register_c8a703a4_1: pin names not known; wires that end beside it: out_22, in_18, A[1], A[2], CLOCK, A[0], l_32b_register_c8a703a4_1_p7
  // L_32b_register_c8a703a4 l_32b_register_c8a703a4_2: pin names not known; wires that end beside it: out_22, in_18, B[1], B[2], CLOCK, B[0], l_32b_register_c8a703a4_2_p7
  Multiplexer #(.width(32)) multiplexer_1 (.in0(in_18), .in1(in_18), .out(out_23), .sel(MUX[1]));
  SuperAlu_main main_1 (
    .in_3(in_2), .in_4(out_22), .in_5(in_18), .out_8(main_1_out_8), .CF(FLAG), .in_7(in_3), .in_6(in_1),
    .out_10(out_21));  // open: _0___disattiva, in_1
  // L_32b_register_c8a703a4 l_32b_register_c8a703a4_3: pin names not known; wires that end beside it: out_22, in_18, PC[1], CLOCK, PC[2], CLOCK, PC[0], main_1_out_8
  // L_32b_register_c8a703a4 l_32b_register_c8a703a4_4: pin names not known; wires that end beside it: out_22, in_18, TEMP[1], TEMP[2], CLOCK, TEMP[0], main_1_out_8
  // L_32b_register_c8a703a4 l_32b_register_c8a703a4_5: pin names not known; wires that end beside it: out_22, in_18, IAR[1], IAR[2], CLOCK, IAR[0], main_1_out_8
  // L_32b_register_c8a703a4 l_32b_register_c8a703a4_6: pin names not known; wires that end beside it: out_22, in_18, MAR[1], MAR[2], CLOCK, MAR[0], main_1_out_8
  // L_32b_register_c8a703a4 l_32b_register_c8a703a4_7: pin names not known; wires that end beside it: out_22, in_18, MDR[1], MDR[2], CLOCK, MDR[0], l_32b_register_c8a703a4_7_p7
  rfEncoderBlock rfencoderblock_1 (
    .WERF(in_5), .OE1RF(in_6), .OE2RF(in_7), .A1(rfencoderblock_1_a1), .A2(rfencoderblock_1_a2),
    .WE(rfencoderblock_1_we), .OE1(rfencoderblock_1_oe1), .OE2(rfencoderblock_1_oe2));
  Multiplexer #(.width(32)) multiplexer_2 (
    .in0(main_1_out_8), .in1(in_17), .out(l_32b_register_c8a703a4_7_p7), .sel(MUX[0]));
  RAM #(.addrWidth(5), .dataWidth(32)) ram_1 (
    .addr(rfencoderblock_1_a1), .we(rfencoderblock_1_we), .oe(rfencoderblock_1_oe1), .clk(in_4),
    .din(l_32b_register_c8a703a4_8_p1), .dout(l_32b_register_c8a703a4_1_p7));
  RAM #(.addrWidth(5), .dataWidth(32)) ram_2 (
    .addr(rfencoderblock_1_a2), .we(rfencoderblock_1_we), .oe(rfencoderblock_1_oe2), .clk(in_4),
    .din(l_32b_register_c8a703a4_8_p1), .dout(l_32b_register_c8a703a4_2_p7));
  // L_32b_register_c8a703a4 l_32b_register_c8a703a4_8: pin names not known; wires that end beside it: l_32b_register_c8a703a4_8_p1, C[1], CLOCK, C[0], main_1_out_8

  assign out_24 = out_22;

  // Other names for the same wires on the sheet: CK = in_4

  // Notes on the sheet:
  //   ALU CTRL
  //   WERF
  //   OE1RF
  //   OE2RF
  //   O2
  //   IND
  //   O1
  //   WE
  //   DATI
  //   S1
  //   S2
  //   A
  //   B
  //   INDIRIZZI
  //   MDR
  //   DATI OUT
  //   PC
  //   TEMP
  //   IAR
  //   MAR
  //   DATI INPUT
endmodule

module rfEncoderBlock (
  input  [31:0] WERF,
  input  [31:0] OE1RF,
  input  [31:0] OE2RF,
  output [4:0] A1,
  output [4:0] A2,
  output WE,
  output OE1,
  output OE2
);

  wire [4:0] thirtytwobitencoder_1_out_2, thirtytwobitencoder_2_out_2, thirtytwobitencoder_3_out_2;

  thirtytwoBitEncoder thirtytwobitencoder_1 (.in_1(WERF), .out_2(thirtytwobitencoder_1_out_2), .out_3(WE));
  thirtytwoBitEncoder thirtytwobitencoder_2 (.in_1(OE1RF), .out_2(thirtytwobitencoder_2_out_2), .out_3(OE1));
  thirtytwoBitEncoder thirtytwobitencoder_3 (.in_1(OE2RF), .out_2(thirtytwobitencoder_3_out_2), .out_3(OE2));
  Multiplexer #(.width(5)) multiplexer_1 (
    .in0(thirtytwobitencoder_2_out_2), .in1(thirtytwobitencoder_1_out_2), .out(A1), .sel(WE));
  Multiplexer #(.width(5)) multiplexer_2 (
    .in0(thirtytwobitencoder_3_out_2), .in1(thirtytwobitencoder_1_out_2), .out(A2), .sel(WE));
endmodule
