// Logisim project ESERCITAZIONE.circ as structural Verilog
module main (
  input  [7:0] in_1
);

  wire clock_1_out, clock_2_out, multiplexer_1_out;
  wire [2:0] counter_1_q;

  Counter #(.max('h7), .width(3)) counter_1 (
    .clk(clock_1_out), .Q(counter_1_q));  // open: clr, load, up, count, D, carry
  Clock clock_1 (.out(clock_1_out));
  Multiplexer #(.select(3)) multiplexer_1 (
    .in0(in_1[7]), .in1(in_1[6]), .in2(in_1[5]), .in3(in_1[4]), .in4(in_1[3]), .in5(in_1[2]), .in6(in_1[1]),
    .in7(in_1[0]), .out(multiplexer_1_out), .sel(counter_1_q));
  Clock clock_2 (.out(clock_2_out));
  // Digital_Oscilloscope digital_oscilloscope_1: pin names not known; wires that end beside it: clock_2_out, multiplexer_1_out
endmodule

module caso_due (
);

  wire and_1_out, and_2_out, and_3_out, CK, d_ff_1_q, d_ff_2_q, d_ff_3_q, d_ff_4_q, d_ff_5_q, not_1_out,
       not_2_out, not_3_out, not_4_out, or_1_out;

  Clock clock_1 (.out(CK));
  D_Flip_Flop d_ff_1 (.D(d_ff_2_q), .clk(CK), .Q(d_ff_1_q));  // open: Qn, preset, reset
  D_Flip_Flop d_ff_2 (.D(d_ff_3_q), .clk(CK), .Q(d_ff_2_q));  // open: Qn, preset, reset
  D_Flip_Flop d_ff_3 (.D(not_1_out), .clk(CK), .Q(d_ff_3_q));  // open: Qn, preset, reset
  not not_1 (not_1_out, d_ff_1_q);
  not not_2 (not_2_out, d_ff_2_q);
  not not_3 (not_3_out, d_ff_3_q);
  not not_4 (not_4_out, d_ff_2_q);
  and and_1 (and_1_out, d_ff_3_q, not_2_out);
  and and_2 (and_2_out, not_3_out, d_ff_1_q);
  and and_3 (and_3_out, not_4_out, d_ff_1_q);
  or or_1 (or_1_out, and_1_out, and_2_out, and_3_out);
  D_Flip_Flop d_ff_4 (.D(or_1_out), .clk(CK), .Q(d_ff_4_q));  // open: Qn, preset, reset
  D_Flip_Flop d_ff_5 (.D(d_ff_4_q), .clk(CK), .Q(d_ff_5_q));  // open: Qn, preset, reset
  // Digital_Oscilloscope digital_oscilloscope_1: pin names not known; wires that end beside it: CK, or_1_out, d_ff_4_q, d_ff_5_q

  // Notes on the sheet:
  //   Y0
  //   Y1
  //   Y2
  //   y0
  //   y1
  //   y2
endmodule

module four_bit_adder (
  input  CI,
  input  [3:0] A,
  input  [3:0] B,
  output [3:0] U,
  output CO
);

  wire fa_1_co, fa_2_co, fa_3_co;

  FA fa_1 (.CI(CI), .A(A[0]), .B(B[0]), .S(U[0]), .CO(fa_1_co));
  FA fa_2 (.CI(fa_1_co), .A(A[1]), .B(B[1]), .S(U[1]), .CO(fa_2_co));
  FA fa_3 (.CI(fa_2_co), .A(A[2]), .B(B[2]), .S(U[2]), .CO(fa_3_co));
  FA fa_4 (.CI(fa_3_co), .A(A[3]), .B(B[3]), .S(U[3]), .CO(CO));
endmodule

module nbitadder_sincrono (
  input  LOAD,
  input  [3:0] A_in,
  input  [3:0] B_in,
  output [3:0] S_out,
  output out_5
);

  wire CK, LOAD_t;
  wire [3:0] A_p5, B_p11, four_bit_adder_1_u;

  Clock clock_1 (.out(CK));
  not not_1 (LOAD_t, LOAD);
  // Shift_Register #(.length(4)) A: pin names not known; wires that end beside it: LOAD_t, CK, A_in[0], A_in[1], A_p5[0], A_p5[1]
  // Shift_Register #(.length(4)) B: pin names not known; wires that end beside it: A_in[2], A_in[3], LOAD_t, CK, B_in[0], B_in[1], B_in[2], B_in[3], A_p5[2], A_p5[3], B_p11[0], B_p11[1], B_p11[2], B_p11[3]
  four_bit_adder four_bit_adder_1 (.CI(1'b0), .A(A_p5), .B(B_p11), .U(four_bit_adder_1_u), .CO(out_5));
  // Shift_Register #(.length(4)) C: pin names not known; wires that end beside it: LOAD_t, CK, four_bit_adder_1_u[0], four_bit_adder_1_u[1], four_bit_adder_1_u[2], four_bit_adder_1_u[3], S_out[0], S_out[1], S_out[2], S_out[3]
endmodule

module FA_sincrono (
  input  [3:0] in_1,
  input  [3:0] in_2,
  input  in_3,
  output [3:0] out_4
);

  wire CK, d_ff_1_q, fa_1_co, fa_1_s, right_shift_register_1_q, right_shift_register_2_q,
       right_shift_register_3_p3;

  Clock clock_1 (.out(CK));
  right_shift_register right_shift_register_1 (
    .MSB(1'b0), .I(in_1), .Q(right_shift_register_1_q));  // open: LSB, OE, A, in_7, in_6, U, out_10
  right_shift_register right_shift_register_2 (
    .MSB(1'b0), .I(in_2), .Q(right_shift_register_2_q));  // open: LSB, OE, A, in_7, in_6, U, out_10
  FA fa_1 (.CI(d_ff_1_q), .A(right_shift_register_1_q), .B(right_shift_register_2_q), .S(fa_1_s), .CO(fa_1_co));
  D_Flip_Flop d_ff_1 (.D(fa_1_co), .clk(CK), .Q(d_ff_1_q), .reset(in_3));  // open: Qn, preset
  // right_shift_register right_shift_register_3: pin names not known; wires that end beside it: fa_1_s, CK, right_shift_register_3_p3, right_shift_register_3_p3
  // right_shift_register right_shift_register_4: pin names not known; wires that end beside it: CK, right_shift_register_3_p3, out_4, out_4
endmodule

module FA (
  input  CI,
  input  A,
  input  B,
  output S,
  output CO
);

  wire ha_1_out_3, ha_1_out_4, ha_2_out_4;

  HA ha_1 (.in_1(A), .in_2(B), .out_3(ha_1_out_3), .out_4(ha_1_out_4));
  HA ha_2 (.in_1(CI), .in_2(ha_1_out_3), .out_3(S), .out_4(ha_2_out_4));
  or or_1 (CO, ha_2_out_4, ha_1_out_4);
endmodule

module HA (
  input  in_1,
  input  in_2,
  output out_3,
  output out_4
);

  xor xor_1 (out_3, in_1, in_2);
  and and_1 (out_4, in_1, in_2);
endmodule

module right_shift_register (
  input  [1:0] A,
  input  [3:0] I,
  input  LSB,
  input  MSB,
  input  OE,
  input  in_6,
  input  in_7,
  output Q,
  output [3:0] U,
  output out_10
);

  wire clock_1_out, clock_2_out, d_ff_1_q, d_ff_3_q, d_ff_4_q, d_ff_5_q, multiplexer_1_out,
       multiplexer_2_out, multiplexer_3_out, multiplexer_4_out, multiplexer_5_out, not_1_out;

  Clock clock_1 (.out(clock_1_out));
  Multiplexer #(.select(2)) multiplexer_1 (
    .in0(d_ff_1_q), .in1(d_ff_3_q), .in2(MSB), .in3(I[3]), .out(multiplexer_1_out), .sel(A));
  D_Flip_Flop d_ff_1 (.D(multiplexer_1_out), .clk(clock_1_out), .Q(d_ff_1_q));  // open: Qn, preset, reset
  not not_1 (not_1_out, OE);
  assign U[3] = not_1_out ? d_ff_1_q : 1'bz;  // Controlled_Buffer controlled_buffer_1
  Clock clock_2 (.out(clock_2_out));
  Multiplexer #(.select(2)) multiplexer_2 (
    .in0(d_ff_3_q), .in1(d_ff_4_q), .in2(d_ff_1_q), .in3(I[2]), .out(multiplexer_2_out), .sel(A));
  Multiplexer multiplexer_3 (.in0(in_7), .in1(out_10), .out(multiplexer_3_out), .sel(in_6));
  D_Flip_Flop d_ff_2 (.D(multiplexer_3_out), .clk(clock_2_out), .Q(out_10));  // open: Qn, preset, reset
  D_Flip_Flop d_ff_3 (.D(multiplexer_2_out), .clk(clock_1_out), .Q(d_ff_3_q));  // open: Qn, preset, reset
  assign U[2] = not_1_out ? d_ff_3_q : 1'bz;  // Controlled_Buffer controlled_buffer_2
  Multiplexer #(.select(2)) multiplexer_4 (
    .in0(d_ff_4_q), .in1(d_ff_5_q), .in2(d_ff_3_q), .in3(I[1]), .out(multiplexer_4_out), .sel(A));
  D_Flip_Flop d_ff_4 (.D(multiplexer_4_out), .clk(clock_1_out), .Q(d_ff_4_q));  // open: Qn, preset, reset
  assign U[1] = not_1_out ? d_ff_4_q : 1'bz;  // Controlled_Buffer controlled_buffer_3
  Multiplexer #(.select(2)) multiplexer_5 (
    .in0(d_ff_5_q), .in1(LSB), .in2(d_ff_4_q), .in3(I[0]), .out(multiplexer_5_out), .sel(A));
  D_Flip_Flop d_ff_5 (.D(multiplexer_5_out), .clk(clock_1_out), .Q(d_ff_5_q));  // open: Qn, preset, reset
  assign Q = not_1_out ? d_ff_5_q : 1'bz;  // Controlled_Buffer controlled_buffer_4
  assign U[0] = not_1_out ? d_ff_5_q : 1'bz;  // Controlled_Buffer controlled_buffer_5
endmodule

module riconoscitore_sequenze (
  input  I
);

  wire and_1_out, and_2_out, and_3_out, and_4_out, and_5_out, and_6_out, and_7_out, and_8_out, and_9_out,
       clock_1_out, clock_2_out, d_ff_1_q, d_ff_2_q, d_ff_3_q, not_1_out, not_2_out, not_3_out, not_4_out,
       not_5_out, not_6_out, not_7_out, not_8_out, not_9_out, not_10_out, not_11_out, not_12_out, or_1_out,
       or_2_out, or_3_out, or_4_out;

  not not_1 (not_1_out, d_ff_2_q);
  and and_1 (and_1_out, not_1_out, not_2_out);
  not not_2 (not_2_out, I);
  not not_3 (not_3_out, d_ff_1_q);
  and and_2 (and_2_out, not_3_out, d_ff_2_q, not_4_out);
  not not_4 (not_4_out, d_ff_3_q);
  not not_5 (not_5_out, d_ff_2_q);
  and and_3 (and_3_out, d_ff_1_q, not_5_out, not_6_out);
  not not_6 (not_6_out, d_ff_3_q);
  not not_7 (not_7_out, d_ff_1_q);
  and and_4 (and_4_out, not_7_out, d_ff_2_q, not_8_out, I);
  not not_8 (not_8_out, d_ff_3_q);
  not not_9 (not_9_out, d_ff_2_q);
  and and_5 (and_5_out, not_9_out, d_ff_3_q, I);
  not not_10 (not_10_out, d_ff_2_q);
  and and_6 (and_6_out, d_ff_1_q, not_10_out, I);
  and and_7 (and_7_out, d_ff_2_q, d_ff_3_q, not_11_out);
  not not_11 (not_11_out, I);
  and and_8 (and_8_out, d_ff_1_q, d_ff_2_q, not_12_out);
  not not_12 (not_12_out, I);
  D_Flip_Flop d_ff_1 (.D(or_3_out), .clk(clock_1_out), .Q(d_ff_1_q));  // open: Qn, preset, reset
  D_Flip_Flop d_ff_2 (.D(or_2_out), .clk(clock_1_out), .Q(d_ff_2_q));  // open: Qn, preset, reset
  D_Flip_Flop d_ff_3 (.D(or_1_out), .clk(clock_1_out), .Q(d_ff_3_q));  // open: Qn, preset, reset
  Clock clock_1 (.out(clock_1_out));
  or or_1 (or_1_out, and_1_out, and_2_out, and_3_out);
  or or_2 (or_2_out, and_4_out, and_5_out);
  or or_3 (or_3_out, and_6_out, and_7_out, and_8_out);
  and and_9 (and_9_out, d_ff_2_q, d_ff_3_q);
  or or_4 (or_4_out, and_9_out, d_ff_1_q);
  Clock clock_2 (.out(clock_2_out));
  // Digital_Oscilloscope digital_oscilloscope_1: pin names not known; wires that end beside it: clock_2_out, I, or_4_out

  // Notes on the sheet:
  //   S2
  //   S1
  //   S0
  //   S0*
  //   S2*
  //   S1*
endmodule

module shift_reg_esercitazione (
  input  A,
  input  I1,
  input  I3,
  input  I2,
  input  I0,
  input  MSB,
  output out_7
);

  wire clock_1_out, d_ff_1_q, d_ff_2_q, d_ff_3_q, multiplexer_1_out, multiplexer_2_out, multiplexer_3_out,
       multiplexer_4_out, not_1_out;

  Multiplexer multiplexer_1 (.in0(I3), .in1(MSB), .out(multiplexer_1_out), .sel(not_1_out));
  Clock clock_1 (.out(clock_1_out));
  D_Flip_Flop d_ff_1 (.D(multiplexer_1_out), .clk(clock_1_out), .Q(d_ff_1_q));  // open: Qn, preset, reset
  not not_1 (not_1_out, A);
  Multiplexer multiplexer_2 (.in0(I2), .in1(d_ff_1_q), .out(multiplexer_2_out), .sel(not_1_out));
  D_Flip_Flop d_ff_2 (.D(multiplexer_2_out), .clk(clock_1_out), .Q(d_ff_2_q));  // open: Qn, preset, reset
  Multiplexer multiplexer_3 (.in0(I1), .in1(d_ff_2_q), .out(multiplexer_3_out), .sel(not_1_out));
  D_Flip_Flop d_ff_3 (.D(multiplexer_3_out), .clk(clock_1_out), .Q(d_ff_3_q));  // open: Qn, preset, reset
  Multiplexer #(.select(2)) multiplexer_4 (.in0(I0), .in3(d_ff_3_q), .out(multiplexer_4_out));  // open: in1, in2, sel
  D_Flip_Flop d_ff_4 (.D(multiplexer_4_out), .clk(clock_1_out), .Q(out_7));  // open: Qn, preset, reset
endmodule

module contatore_gray (
  input  U_D
);

  wire and_1_out, and_2_out, and_3_out, and_4_out, and_5_out, and_6_out, and_7_out, and_8_out, and_9_out,
       and_10_out, clock_1_out, not_1_out, not_2_out, not_3_out, not_4_out, not_5_out, not_6_out, not_7_out,
       not_8_out, not_9_out, not_10_out, not_11_out, not_12_out, not_13_out, or_1_out, or_2_out, or_3_out;
  wire [2:0] d_ff_1_q;

  not not_1 (not_1_out, d_ff_1_q[2]);
  Clock clock_1 (.out(clock_1_out));
  not not_2 (not_2_out, U_D);
  not not_3 (not_3_out, d_ff_1_q[1]);
  and and_1 (and_1_out, not_2_out, not_3_out, not_4_out);
  not not_4 (not_4_out, d_ff_1_q[0]);
  and and_2 (and_2_out, d_ff_1_q[2], d_ff_1_q[0]);
  and and_3 (and_3_out, U_D, d_ff_1_q[1], not_5_out);
  not not_5 (not_5_out, d_ff_1_q[0]);
  and and_4 (and_4_out, d_ff_1_q[1], not_6_out);
  not not_6 (not_6_out, d_ff_1_q[0]);
  not not_7 (not_7_out, U_D);
  and and_5 (and_5_out, not_7_out, d_ff_1_q[2], d_ff_1_q[0]);
  and and_6 (and_6_out, U_D, not_1_out, d_ff_1_q[0]);
  not not_8 (not_8_out, U_D);
  not not_9 (not_9_out, d_ff_1_q[2]);
  and and_7 (and_7_out, not_8_out, not_9_out, d_ff_1_q[1]);
  not not_10 (not_10_out, U_D);
  and and_8 (and_8_out, not_10_out, d_ff_1_q[2], not_11_out);
  not not_11 (not_11_out, d_ff_1_q[1]);
  and and_9 (and_9_out, U_D, d_ff_1_q[2], d_ff_1_q[1]);
  not not_12 (not_12_out, d_ff_1_q[2]);
  and and_10 (and_10_out, U_D, not_12_out, not_13_out);
  not not_13 (not_13_out, d_ff_1_q[1]);
  D_Flip_Flop d_ff_1 (.D(or_3_out), .clk(clock_1_out), .Q(d_ff_1_q[0]));  // open: Qn, preset, reset
  D_Flip_Flop d_ff_2 (.D(or_2_out), .clk(clock_1_out), .Q(d_ff_1_q[1]));  // open: Qn, preset, reset
  D_Flip_Flop d_ff_3 (.D(or_1_out), .clk(clock_1_out), .Q(d_ff_1_q[2]));  // open: Qn, preset, reset
  or or_1 (or_1_out, and_1_out, and_2_out, and_3_out);
  or or_2 (or_2_out, and_4_out, and_5_out, and_6_out);
  or or_3 (or_3_out, and_7_out, and_8_out, and_9_out, and_10_out);
  _7_Segment_Display u_7_segment_display_1 ();  // open: g, f, a, b, e, d, c, dp
  // BCD_to_7_Segment_decoder bcd_to_7_segment_decoder_1: pin names not known; wires that end beside it: {1'b0, d_ff_1_q}

  // Notes on the sheet:
  //   q0
  //   q1
  //   q2
  //   Q1
  //   Q0
  //   Q2
endmodule

module test (
);

  ROM rom_1 ();  // open: addr, data
endmodule
