// Logisim project MicroCodice.circ as structural Verilog: 13 circuits, main circuit main
module main (
  input  [31:0] IR
);

  wire CK, Cost_Enable, countercompare_1_out_3, Rd, Rs1, Rs2, ZF;
  wire [3:0] counter_1_q;
  wire [4:0] instrtypemanager_1_rd, instrtypemanager_1_rs1, instrtypemanager_1_rs2;
  wire [15:0] rom_2_data;
  wire [21:0] rom_1_data;
  wire [31:0] alumain_1_s, instrtypemanager_1_cost, rom_3_data;

  Clock clock_1 (.out(CK));
  ROM #(.addrWidth(6), .dataWidth(22)) rom_1 (.addr(IR[31:26]), .data(rom_1_data));
  // Probe on rom_1_data[19:4]
  // Probe on rom_1_data[21:20]
  // Probe on rom_1_data[3:0]
  instrTypeManager instrtypemanager_1 (
    .istr_type(rom_1_data[21:20]), .IR_senzaCop(IR[25:0]), .RS1(instrtypemanager_1_rs1),
    .RS2(instrtypemanager_1_rs2), .RD(instrtypemanager_1_rd), .COST(instrtypemanager_1_cost));
  Counter #(.max('hf), .width(4)) counter_1 (
    .Q(counter_1_q), .clk(CK), .clr(countercompare_1_out_3));  // open: load, D, count, carry, up
  CounterCompare countercompare_1 (.in_1(counter_1_q), .in_2(rom_1_data[3:0]), .out_3(countercompare_1_out_3));
  // Probe on instrtypemanager_1_rs1
  // Probe on instrtypemanager_1_rs2
  // Probe on instrtypemanager_1_rd
  // Probe on instrtypemanager_1_cost
  aluMain alumain_1 (
    .A({{16{1'b0}}, rom_1_data[19:4]}), .B({{28{1'b0}}, counter_1_q}), .in_2(5'b10000), .S(alumain_1_s));  // open: in_5, Ci4, in_6, Co, ZF, ris
  ROM #(.addrWidth(16), .dataWidth(16)) rom_2 (
    .addr(alumain_1_s[15:0]), .data({rom_2_data[15:10], Rs1, Rs2, Rd, Cost_Enable, rom_2_data[5:0]}));
  ROM #(.addrWidth(16), .dataWidth(32)) rom_3 (.addr(alumain_1_s[15:0]), .data(rom_3_data));
  // mainDataPath maindatapath_1: pin names not known; wires that end beside it: rom_3_data[31], rom_3_data[4:0], rom_3_data[7:5], rom_3_data[10:8], rom_3_data[13:11], rom_3_data[16:14], rom_3_data[19:17], rom_3_data[22:20], rom_3_data[25:23], rom_3_data[28:26], rom_3_data[30:29], Cost_Enable, instrtypemanager_1_cost, CK, Rs1, instrtypemanager_1_rs1, Rs2, instrtypemanager_1_rs2, Rd, instrtypemanager_1_rd, ZF

  // Notes on the sheet:
  //   contents of rom_1 (hex, n*v repeats v):
  //   100003 32
  //   CopMemory
  //   contents of rom_2 (hex, n*v repeats v):
  //   300 40 80 300
  //   contents of rom_3 (hex, n*v repeats v):
  //   8000c130 850 1000 8000c130 4042
  //   Microcode Memory #2
  //   Microcode Memory #1
endmodule

module ram_e_indirizzi (
  input  [15:0] IND,
  output [31:0] CTRL
);

  ROM #(.addrWidth(16), .dataWidth(32)) rom_1 (.addr(IND), .data(CTRL));

  // Notes on the sheet:
  //   contents of rom_1 (hex, n*v repeats v):
  //   8000c130 850 1000
  //   Microcode Memory
endmodule

module ram_e_offset (
  input  [15:0] IND1,
  input  [3:0] OFFSET,
  output [31:0] CTRL
);

  wire [31:0] alumain_1_p2;

  // aluMain alumain_1: pin names not known; wires that end beside it: 5'b10000, alumain_1_p2
  ROM #(.addrWidth(16), .dataWidth(32)) rom_1 (.addr(alumain_1_p2[15:0]), .data(CTRL));

  // Notes on the sheet:
  //   contents of rom_1 (hex, n*v repeats v):
  //   8000c130 850 1000
  //   Microcode Memory
endmodule

module ram_e_counter (
  input  [15:0] IND1,
  output [31:0] CTRL
);

  wire clock_1_out;
  wire [3:0] counter_1_q;
  wire [31:0] alumain_1_p2;

  Counter #(.max('hf), .width(4)) counter_1 (
    .Q(counter_1_q), .clk(clock_1_out));  // open: load, D, count, carry, up, clr
  Clock clock_1 (.out(clock_1_out));
  // aluMain alumain_1: pin names not known; wires that end beside it: 5'b10000, alumain_1_p2
  ROM #(.addrWidth(16), .dataWidth(32)) rom_1 (.addr(alumain_1_p2[15:0]), .data(CTRL));

  // Notes on the sheet:
  //   offset
  //   (microprogramcounter)
  //   contents of rom_1 (hex, n*v repeats v):
  //   8000c130 850 1000 8000c130 4042
  //   Microcode Memory
endmodule

module ram_e_reset_counter (
  input  [15:0] IND1,
  input  [3:0] CPI,
  output [31:0] out_3
);

  wire and_1_out, clock_1_out, xnor_1_out, xnor_2_out, xnor_3_out, xnor_4_out;
  wire [3:0] counter_1_q;
  wire [31:0] alumain_1_p2;

  xnor xnor_1 (xnor_1_out, CPI[3], counter_1_q[3]);
  Clock clock_1 (.out(clock_1_out));
  xnor xnor_2 (xnor_2_out, CPI[2], counter_1_q[2]);
  and and_1 (and_1_out, xnor_1_out, xnor_2_out, xnor_4_out, xnor_3_out);
  Counter #(.max('hf), .width(4)) counter_1 (
    .Q(counter_1_q), .clk(clock_1_out), .clr(and_1_out));  // open: load, D, count, carry, up
  xnor xnor_3 (xnor_3_out, CPI[0], counter_1_q[0]);
  xnor xnor_4 (xnor_4_out, CPI[1], counter_1_q[1]);
  // aluMain alumain_1: pin names not known; wires that end beside it: 5'b10000, alumain_1_p2
  ROM #(.addrWidth(16), .dataWidth(32)) rom_1 (.addr(alumain_1_p2[15:0]), .data(out_3));

  // Notes on the sheet:
  //   contents of rom_1 (hex, n*v repeats v):
  //   8000c130 850 1000 8000c130 4042
  //   Microcode Memory
endmodule

module ram_e_integrate_resCounter (
  input  [15:0] IND1,
  input  [3:0] CPI
);

  wire clock_1_out, countercompare_1_out_3;
  wire [3:0] counter_1_q;
  wire [31:0] alumain_1_p2, rom_1_data;

  Clock clock_1 (.out(clock_1_out));
  CounterCompare countercompare_1 (.in_1(counter_1_q), .in_2(CPI), .out_3(countercompare_1_out_3));
  Counter #(.max('hf), .width(4)) counter_1 (
    .Q(counter_1_q), .clk(clock_1_out), .clr(countercompare_1_out_3));  // open: load, D, count, carry, up
  // aluMain alumain_1: pin names not known; wires that end beside it: 5'b10000, alumain_1_p2
  ROM #(.addrWidth(16), .dataWidth(32)) rom_1 (.addr(alumain_1_p2[15:0]), .data(rom_1_data));
  // Probe on rom_1_data
  // mainDataPath maindatapath_1: pin names not known; wires that end beside it: rom_1_data[31], rom_1_data[4:0], rom_1_data[7:5], rom_1_data[10:8], rom_1_data[13:11], rom_1_data[16:14], rom_1_data[19:17], rom_1_data[22:20], rom_1_data[25:23], rom_1_data[28:26], rom_1_data[30:29], clock_1_out

  // Notes on the sheet:
  //   contents of rom_1 (hex, n*v repeats v):
  //   8000c130 850 1000 8000c130 4042
  //   Microcode Memory
endmodule

module ram_e_cop_memory (
  input  [5:0] COP,
  output [31:0] Ctrl
);

  wire clock_1_out, countercompare_1_out_3;
  wire [3:0] counter_1_q;
  wire [19:0] rom_1_data;
  wire [31:0] alumain_1_p2;

  ROM #(.addrWidth(6), .dataWidth(20)) rom_1 (.addr(COP), .data(rom_1_data));
  // Probe on rom_1_data[19:4]
  // Probe on rom_1_data[3:0]
  Clock clock_1 (.out(clock_1_out));
  CounterCompare countercompare_1 (.in_1(counter_1_q), .in_2(rom_1_data[3:0]), .out_3(countercompare_1_out_3));
  Counter #(.max('hf), .width(4)) counter_1 (
    .Q(counter_1_q), .clk(clock_1_out), .clr(countercompare_1_out_3));  // open: load, D, count, carry, up
  // aluMain alumain_1: pin names not known; wires that end beside it: 5'b10000, alumain_1_p2
  ROM #(.addrWidth(16), .dataWidth(32)) rom_2 (.addr(alumain_1_p2[15:0]), .data(Ctrl));

  // Notes on the sheet:
  //   contents of rom_1 (hex, n*v repeats v):
  //   3 32
  //   CopMemory
  //   contents of rom_2 (hex, n*v repeats v):
  //   8000c130 850 1000 8000c130 4042
  //   Microcode Memory
endmodule

module ram_e_datapath (
  input  [31:0] IR
);

  wire CK, Cost_Enable, countercompare_1_out_3, Rd, Rs1, Rs2;
  wire [3:0] counter_1_q;
  wire [4:0] instrtypemanager_1_rd, instrtypemanager_1_rs1, instrtypemanager_1_rs2;
  wire [15:0] rom_2_data;
  wire [21:0] rom_1_data;
  wire [31:0] alumain_1_s, instrtypemanager_1_cost, rom_3_data;

  Clock clock_1 (.out(CK));
  ROM #(.addrWidth(6), .dataWidth(22)) rom_1 (.addr(IR[31:26]), .data(rom_1_data));
  // Probe on rom_1_data[19:4]
  // Probe on rom_1_data[21:20]
  // Probe on rom_1_data[3:0]
  instrTypeManager instrtypemanager_1 (
    .istr_type(rom_1_data[21:20]), .IR_senzaCop(IR[25:0]), .RS1(instrtypemanager_1_rs1),
    .RS2(instrtypemanager_1_rs2), .RD(instrtypemanager_1_rd), .COST(instrtypemanager_1_cost));
  Counter #(.max('hf), .width(4)) counter_1 (
    .Q(counter_1_q), .clk(CK), .clr(countercompare_1_out_3));  // open: load, D, count, carry, up
  CounterCompare countercompare_1 (.in_1(counter_1_q), .in_2(rom_1_data[3:0]), .out_3(countercompare_1_out_3));
  // Probe on instrtypemanager_1_rs1
  // Probe on instrtypemanager_1_rs2
  // Probe on instrtypemanager_1_rd
  // Probe on instrtypemanager_1_cost
  aluMain alumain_1 (
    .A({{16{1'b0}}, rom_1_data[19:4]}), .B({{28{1'b0}}, counter_1_q}), .in_2(5'b10000), .S(alumain_1_s));  // open: in_5, Ci4, in_6, Co, ZF, ris
  ROM #(.addrWidth(16), .dataWidth(16)) rom_2 (
    .addr(alumain_1_s[15:0]), .data({rom_2_data[15:10], Rs1, Rs2, Rd, Cost_Enable, rom_2_data[5:0]}));
  ROM #(.addrWidth(16), .dataWidth(32)) rom_3 (.addr(alumain_1_s[15:0]), .data(rom_3_data));
  // mainDataPath maindatapath_1: pin names not known; wires that end beside it: rom_3_data[31], rom_3_data[4:0], rom_3_data[7:5], rom_3_data[10:8], rom_3_data[13:11], rom_3_data[16:14], rom_3_data[19:17], rom_3_data[22:20], rom_3_data[25:23], rom_3_data[28:26], rom_3_data[30:29], Cost_Enable, instrtypemanager_1_cost, CK, Rs1, instrtypemanager_1_rs1, Rs2, instrtypemanager_1_rs2, Rd, instrtypemanager_1_rd

  // Notes on the sheet:
  //   contents of rom_1 (hex, n*v repeats v):
  //   100003 32
  //   CopMemory
  //   contents of rom_2 (hex, n*v repeats v):
  //   300 40 80 300
  //   contents of rom_3 (hex, n*v repeats v):
  //   8000c130 850 1000 8000c130 4042
  //   Microcode Memory #2
  //   Microcode Memory #1
endmodule

module ram_e_programmazione (
  input  MemRd,
  input  in_2
);

  wire CI, CK, CopReset, Cost_Enable, CounterRd, CounterReset, maindatapath_1_p21, or_1_out, Rd, Rs1, Rs2,
       WE_IR;
  wire [2:0] mastercontrol_1_u;
  wire [3:0] counter_1_q, rom_4_data;
  wire [4:0] instrtypemanager_1_rd, instrtypemanager_1_rs1, instrtypemanager_1_rs2;
  wire [5:0] register_1_q_2;
  wire [7:4] rom_2_data;
  wire [20:0] rom_4_data_2;
  wire [21:0] multiplexer_1_out, rom_1_data;
  wire [25:0] register_1_q;
  wire [31:0] alumain_1_s, controlled_buffer_1_out, instrtypemanager_1_cost, maindatapath_1_p23, rom_3_data,
       rom_5_data;

  Clock clock_1 (.out(CK));
  or or_1 (or_1_out, MemRd, CounterRd);
  ROM #(.addrWidth(6), .dataWidth(22)) rom_1 (.addr(register_1_q_2), .data(rom_1_data));
  MasterControl mastercontrol_1 (.RD(or_1_out), .CK(CK), .INT(in_2), .U(mastercontrol_1_u));
  _7_Segment_Display u_7_segment_display_1 ();  // open: g, f, a, b, e, d, c, dp
  // BCD_to_7_Segment_decoder bcd_to_7_segment_decoder_1: pin names not known; wires that end beside it: {1'b0, mastercontrol_1_u}
  Register #(.width(32)) register_1 (
    .D(controlled_buffer_1_out), .en(WE_IR), .clk(CK), .Q({register_1_q_2, register_1_q}));  // open: clr
  ROM #(.addrWidth(3)) rom_2 (.addr(mastercontrol_1_u), .data({rom_2_data, WE_IR, CI, CopReset, CounterReset}));
  // Probe on multiplexer_1_out[19:4]
  Multiplexer #(.width(22)) multiplexer_1 (.in0(rom_1_data), .in1({22{1'b0}}), .out(multiplexer_1_out), .sel(CopReset));
  // Probe on multiplexer_1_out[21:20]
  // Probe on multiplexer_1_out[3:0]
  instrTypeManager instrtypemanager_1 (
    .istr_type(multiplexer_1_out[21:20]), .IR_senzaCop(register_1_q), .RS1(instrtypemanager_1_rs1),
    .RS2(instrtypemanager_1_rs2), .RD(instrtypemanager_1_rd), .COST(instrtypemanager_1_cost));
  ROM #(.addrWidth(16), .dataWidth(32)) rom_3 (.addr(maindatapath_1_p23[15:0]), .data(rom_3_data));
  CounterCompare countercompare_1 (.in_1(counter_1_q), .in_2(multiplexer_1_out[3:0]), .out_3(CounterRd));
  // Probe on instrtypemanager_1_rs1
  // Probe on instrtypemanager_1_rs2
  Counter #(.max('hf), .width(4)) counter_1 (
    .Q(counter_1_q), .clk(CK), .clr(CounterReset));  // open: load, D, count, carry, up
  // Probe on instrtypemanager_1_rd
  // Probe on instrtypemanager_1_cost
  aluMain alumain_1 (
    .A({{16{1'b0}}, multiplexer_1_out[19:4]}), .B({{28{1'b0}}, counter_1_q}), .in_2({1'b1, CI, 3'b000}),
    .S(alumain_1_s));  // open: in_5, Ci4, in_6, Co, ZF, ris
  assign controlled_buffer_1_out = rom_4_data[0] ? rom_3_data : 32'bz;  // Controlled_Buffer controlled_buffer_1
  ROM #(.addrWidth(16), .dataWidth(21)) rom_4 (
    .addr(alumain_1_s[15:0]),
    .data({rom_4_data_2[20:10], Rs1, Rs2, Rd, Cost_Enable, rom_4_data, rom_4_data_2[1:0]}));
  ROM #(.addrWidth(16), .dataWidth(32)) rom_5 (.addr(alumain_1_s[15:0]), .data(rom_5_data));
  // mainDataPath maindatapath_1: pin names not known; wires that end beside it: rom_5_data[31], rom_5_data[4:0], rom_5_data[7:5], rom_5_data[10:8], rom_5_data[13:11], rom_5_data[16:14], rom_5_data[19:17], rom_5_data[22:20], rom_5_data[25:23], rom_5_data[28:26], rom_5_data[30:29], Cost_Enable, instrtypemanager_1_cost, CK, Rs1, instrtypemanager_1_rs1, Rs2, instrtypemanager_1_rs2, Rd, instrtypemanager_1_rd, maindatapath_1_p21, controlled_buffer_1_out, maindatapath_1_p23

  // Notes on the sheet:
  //   DATIIN
  //   DATIOUT
  //   CMD
  //   IND
  //   contents of rom_1 (hex, n*v repeats v):
  //   100021 40 300050 63 1000a1 1000c2
  //   CopMemory
  //   contents of rom_2 (hex, n*v repeats v):
  //   b 7
  //   contents of rom_3 (hex, n*v repeats v):
  //   10004 4200000
  //   contents of rom_4 (hex, n*v repeats v):
  //   4 300 40 80 0 40 30000 20000 0 80 8000 40 40 0 8
  //   contents of rom_5 (hex, n*v repeats v):
  //   40010000 c138 850 1000 4042 c010 459 81f 81e 1000 452 c010 800050 4000200 a000000
  //   Microcode Memory #2
  //   Microcode Memory #1
endmodule

module CPU (
  input  MemRd,
  input  in_2
);

  wire BRANCH, CI, CK, controlled_buffer_1_out, CopReset, Cost_Enable, CounterRd, CounterReset, cs0, cs1,
       maindatapath_1_p24, microJ_en, multiplexer_1_out, not_1_out, or_1_out, Rd, RIS, Rs1, Rs2, U, WE_IR,
       ZF, ZF_EN;
  wire [1:0] rom_4_data_2;
  wire [2:0] mastercontrol_1_u, set_cond;
  wire [3:0] microjump, multiplexer_4_out, register_2_q, rom_4_data;
  wire [4:0] instrtypemanager_1_rd, instrtypemanager_1_rs1, instrtypemanager_1_rs2;
  wire [5:0] register_1_q_2;
  wire [21:0] multiplexer_2_out, rom_1_data;
  wire [25:0] register_1_q;
  wire [31:0] alumain_1_s, alumain_2_s, controlled_buffer_2_out, controlled_buffer_3_out,
       instrtypemanager_1_cost, maindatapath_1_p25, maindatapath_1_p27, multiplexer_3_out, ram_1_dout,
       rom_3_data, rom_5_data;

  Clock clock_1 (.out(CK));
  not not_1 (not_1_out, ZF);
  Multiplexer multiplexer_1 (.in0(not_1_out), .in1(ZF), .out(multiplexer_1_out), .sel(BRANCH));
  or or_1 (or_1_out, MemRd, CounterRd, controlled_buffer_1_out);
  assign controlled_buffer_1_out = ZF_EN ? multiplexer_1_out : 1'bz;  // Controlled_Buffer controlled_buffer_1
  ROM #(.addrWidth(6), .dataWidth(22)) rom_1 (.addr(register_1_q_2), .data(rom_1_data));
  MasterControl mastercontrol_1 (.RD(or_1_out), .CK(CK), .INT(in_2), .U(mastercontrol_1_u));
  _7_Segment_Display u_7_segment_display_1 ();  // open: g, f, a, b, e, d, c, dp
  // BCD_to_7_Segment_decoder bcd_to_7_segment_decoder_1: pin names not known; wires that end beside it: {1'b0, mastercontrol_1_u}
  Register #(.width(32)) register_1 (
    .D(controlled_buffer_3_out), .en(WE_IR), .clk(CK), .Q({register_1_q_2, register_1_q}));  // open: clr
  ROM #(.addrWidth(3), .dataWidth(4)) rom_2 (.addr(mastercontrol_1_u), .data({WE_IR, CI, CopReset, CounterReset}));
  // Probe on multiplexer_2_out[19:4]
  Multiplexer #(.width(22)) multiplexer_2 (.in0(rom_1_data), .in1({22{1'b0}}), .out(multiplexer_2_out), .sel(CopReset));
  // Probe on multiplexer_2_out[21:20]
  ROM #(.addrWidth(15), .dataWidth(32)) rom_3 (.addr(maindatapath_1_p27[14:0]), .data(rom_3_data));
  // Probe on multiplexer_2_out[3:0]
  CounterCompare countercompare_1 (.in_1(register_2_q), .in_2(multiplexer_2_out[3:0]), .out_3(CounterRd));
  instrTypeManager instrtypemanager_1 (
    .istr_type(multiplexer_2_out[21:20]), .IR_senzaCop(register_1_q), .RS1(instrtypemanager_1_rs1),
    .RS2(instrtypemanager_1_rs2), .RD(instrtypemanager_1_rd), .COST(instrtypemanager_1_cost));
  // Probe on instrtypemanager_1_rs1
  // Probe on instrtypemanager_1_rs2
  Multiplexer #(.width(32)) multiplexer_3 (
    .in0({32{1'b0}}), .in1({{28{1'b0}}, microjump}), .out(multiplexer_3_out), .sel(RIS));
  Register #(.width(4)) register_2 (.D(alumain_2_s[3:0]), .en(1'b1), .clk(CK), .Q(register_2_q), .clr(CounterReset));
  // Probe on instrtypemanager_1_rd
  // Probe on instrtypemanager_1_cost
  aluMain alumain_1 (
    .A({{16{1'b0}}, multiplexer_2_out[19:4]}), .B({{28{1'b0}}, register_2_q}), .in_2({1'b1, CI, 3'b000}),
    .S(alumain_1_s));  // open: in_5, Ci4, in_6, Co, ZF, ris
  assign controlled_buffer_2_out = rom_4_data[0] ? rom_3_data : 32'bz;  // Controlled_Buffer controlled_buffer_2
  assign controlled_buffer_3_out = cs0 ? controlled_buffer_2_out : 32'bz;  // Controlled_Buffer controlled_buffer_3
  ROM #(.addrWidth(16), .dataWidth(21)) rom_4 (
    .addr(alumain_1_s[15:0]),
    .data({microjump, microJ_en, ZF_EN, BRANCH, U, set_cond, Rs1, Rs2, Rd, Cost_Enable, rom_4_data, rom_4_data_2}));
  ROM #(.addrWidth(16), .dataWidth(32)) rom_5 (.addr(alumain_1_s[15:0]), .data(rom_5_data));
  aluMain alumain_2 (
    .A(multiplexer_3_out), .B({{28{1'b0}}, register_2_q}), .in_2(5'b11000), .S(alumain_2_s));  // open: in_5, Ci4, in_6, Co, ZF, ris
  // Probe on alumain_2_s[3:0]
  Multiplexer #(.width(4)) multiplexer_4 (.in0(4'b0000), .in1(rom_4_data), .out(multiplexer_4_out), .sel(cs1));
  RAM #(.addrWidth(15), .asyncread("true"), .dataWidth(32)) ram_1 (
    .addr(maindatapath_1_p27[14:0]), .we(multiplexer_4_out[1]), .oe(multiplexer_4_out[0]), .clk(CK),
    .din(maindatapath_1_p25), .dout(ram_1_dout));
  assign controlled_buffer_3_out = cs1 ? ram_1_dout : 32'bz;  // Controlled_Buffer controlled_buffer_4
  // mainDataPath maindatapath_1: pin names not known; wires that end beside it: rom_5_data[31], rom_5_data[4:0], rom_5_data[7:5], rom_5_data[10:8], rom_5_data[13:11], rom_5_data[16:14], rom_5_data[19:17], rom_5_data[22:20], rom_5_data[25:23], rom_5_data[28:26], rom_5_data[30:29], Cost_Enable, instrtypemanager_1_cost, CK, Rs1, instrtypemanager_1_rs1, Rs2, instrtypemanager_1_rs2, Rd, instrtypemanager_1_rd, U, set_cond, ZF, maindatapath_1_p24, maindatapath_1_p25, controlled_buffer_3_out, {maindatapath_1_p27[31:16], cs1, maindatapath_1_p27[14:0]}
  Multiplexer multiplexer_5 (.in0(1'b1), .in1(maindatapath_1_p24), .out(RIS), .sel(microJ_en));
  not not_2 (cs0, cs1);

  // Notes on the sheet:
  //   DOUT
  //   CMD
  //   IND
  //   DIN
  //   contents of rom_1 (hex, n*v repeats v):
  //   100021 40 300050 63 1000a1 1000c2
  //   CopMemory
  //   contents of rom_2 (hex, n*v repeats v):
  //   b 7
  //   IR
  //   contents of rom_3 (hex, n*v repeats v):
  //   10001 20002 c220800 10200002 30009 8000001 30005 14038000
  //   #Program Memory
  //   contents of rom_4 (hex, n*v repeats v):
  //   4 300 40 80 0 40 30000 20000 0 80 8000 40 40 0 8
  //   contents of rom_5 (hex, n*v repeats v):
  //   40010000 c138 850 1000 4042 c010 459 81f 81e 1000 452 c010 800050 4000200 a000000
  //   Microcode Memory #2
  //   Microcode Memory #1
  //   #Variables
endmodule

module CounterCompare (
  input  [3:0] in_1,
  input  [3:0] in_2,
  output out_3
);

  wire xnor_1_out, xnor_2_out, xnor_3_out, xnor_4_out;

  xnor xnor_1 (xnor_1_out, in_1[3], in_2[3]);
  xnor xnor_2 (xnor_2_out, in_1[2], in_2[2]);
  and and_1 (out_3, xnor_1_out, xnor_2_out, xnor_4_out, xnor_3_out);
  xnor xnor_3 (xnor_3_out, in_1[0], in_2[0]);
  xnor xnor_4 (xnor_4_out, in_1[1], in_2[1]);
endmodule

module instrTypeManager (
  input  [1:0] istr_type,
  input  [25:0] IR_senzaCop,
  output [4:0] RS1,
  output [4:0] RS2,
  output [4:0] RD,
  output [31:0] COST
);

  wire I, J, R;

  Decoder #(.enable("false"), .select(2)) decoder_1 (.out0(R), .out1(I), .out3(J), .sel(istr_type));  // open: out2
  assign COST = I ? {{17{IR_senzaCop[15]}}, IR_senzaCop[14:0]} : 32'bz;  // Controlled_Buffer controlled_buffer_1
  assign COST = J ? {{7{IR_senzaCop[25]}}, IR_senzaCop[24:0]} : 32'bz;  // Controlled_Buffer controlled_buffer_2
  assign RD = I ? IR_senzaCop[20:16] : 5'bz;  // Controlled_Buffer controlled_buffer_3
  assign RD = R ? IR_senzaCop[15:11] : 5'bz;  // Controlled_Buffer controlled_buffer_4

  assign RS1 = IR_senzaCop[25:21];
  assign RS2 = IR_senzaCop[20:16];

  // Notes on the sheet:
  //   op-imm-26
  //   op-imm-16
endmodule

module MasterControl (
  input  INT,
  input  RD,
  input  CK,
  output [2:0] U
);

  wire and_1_out, and_2_out, and_3_out, and_4_out, and_5_out, and_6_out, not_1_out, not_2_out, not_3_out,
       not_4_out, not_5_out, not_6_out, not_7_out, not_8_out, not_9_out, not_10_out, not_11_out, not_12_out,
       not_13_out, not_14_out, or_1_out, or_2_out;

  not not_1 (not_1_out, U[2]);
  not not_2 (not_2_out, U[1]);
  not not_3 (not_3_out, U[0]);
  not not_4 (not_4_out, U[2]);
  not not_5 (not_5_out, U[1]);
  not not_6 (not_6_out, U[0]);
  not not_7 (not_7_out, U[2]);
  not not_8 (not_8_out, U[1]);
  not not_9 (not_9_out, U[2]);
  not not_10 (not_10_out, U[1]);
  not not_11 (not_11_out, U[2]);
  not not_12 (not_12_out, U[0]);
  not not_13 (not_13_out, RD);
  not not_14 (not_14_out, U[2]);
  and and_1 (and_1_out, not_1_out, not_2_out, not_3_out, RD);
  and and_2 (and_2_out, not_4_out, not_5_out, not_6_out, INT);
  and and_3 (and_3_out, not_7_out, not_8_out, INT);
  and and_4 (and_4_out, not_9_out, not_10_out, U[0]);
  and and_5 (and_5_out, not_11_out, U[1], not_12_out, not_13_out);
  and and_6 (and_6_out, not_14_out, U[1], U[0]);
  D_Flip_Flop d_ff_1 (.clk(CK), .D(and_6_out), .Q(U[2]));  // open: Qn, preset, reset
  D_Flip_Flop d_ff_2 (.clk(CK), .D(or_2_out), .Q(U[1]));  // open: Qn, preset, reset
  D_Flip_Flop d_ff_3 (.clk(CK), .D(or_1_out), .Q(U[0]));  // open: Qn, preset, reset
  or or_1 (or_1_out, and_1_out, and_2_out);
  or or_2 (or_2_out, and_3_out, and_4_out, and_5_out);

  // Notes on the sheet:
  //   q2
  //   q1
  //   q0
  //   Q2
  //   Q0
  //   Q1
endmodule
