// Logisim project Alu.circ as structural Verilog: 6 circuits, main circuit HA
module aluMain (
  input  Ci4,
  input  [4:0] in_2,
  input  [31:0] A,
  input  [31:0] B,
  input  [2:0] in_5,
  input  in_6,
  output [31:0] S,
  output Co,
  output ZF,
  output ris
);

  wire and_1_out, fa_1_s, multiplexer_2_out, multiplexer_3_out, not_2_out, not_3_out, not_4_out, not_5_out,
       not_6_out, or_1_out, or_2_out, or_3_out, or_5_out, or_6_out, sommatoretrentaduebit_1_co,
       sommatoretrentaduebit_2_co;
  wire [31:0] multiplexer_1_out, retepreelab_1_ao, retepreelab_1_bo, sommatoretrentaduebit_1_s;

  RetePreelab retepreelab_1 (.c2c1c0(in_2[2:0]), .A(A), .B(B), .Ao(retepreelab_1_ao), .Bo(retepreelab_1_bo));
  SommatoreTrentadueBit sommatoretrentaduebit_1 (
    .B(retepreelab_1_bo), .A(retepreelab_1_ao), .Ci(in_2[3]), .M(in_2[4]), .Co(sommatoretrentaduebit_1_co),
    .S(sommatoretrentaduebit_1_s));
  or or_1 (or_1_out, sommatoretrentaduebit_1_s[0], sommatoretrentaduebit_1_s[1], sommatoretrentaduebit_1_s[2], sommatoretrentaduebit_1_s[3], sommatoretrentaduebit_1_s[4], sommatoretrentaduebit_1_s[5], sommatoretrentaduebit_1_s[6], sommatoretrentaduebit_1_s[7], sommatoretrentaduebit_1_s[8], sommatoretrentaduebit_1_s[9], sommatoretrentaduebit_1_s[10], sommatoretrentaduebit_1_s[11], sommatoretrentaduebit_1_s[12], sommatoretrentaduebit_1_s[13], sommatoretrentaduebit_1_s[14], sommatoretrentaduebit_1_s[15], sommatoretrentaduebit_1_s[16]);
  or or_2 (or_2_out, sommatoretrentaduebit_1_s[17], sommatoretrentaduebit_1_s[18], sommatoretrentaduebit_1_s[19], sommatoretrentaduebit_1_s[20], sommatoretrentaduebit_1_s[21], sommatoretrentaduebit_1_s[22], sommatoretrentaduebit_1_s[23], sommatoretrentaduebit_1_s[24], sommatoretrentaduebit_1_s[25], sommatoretrentaduebit_1_s[26], sommatoretrentaduebit_1_s[27], sommatoretrentaduebit_1_s[28], sommatoretrentaduebit_1_s[29], sommatoretrentaduebit_1_s[30], sommatoretrentaduebit_1_s[31]);
  Multiplexer #(.width(32)) multiplexer_1 (.in0({32{1'b0}}), .in1(32'h4), .out(multiplexer_1_out), .sel(Ci4));
  or or_3 (or_3_out, or_1_out, or_2_out);
  SommatoreTrentadueBit sommatoretrentaduebit_2 (
    .B(sommatoretrentaduebit_1_s), .A(multiplexer_1_out), .Ci(1'b0), .M(1'b1),
    .Co(sommatoretrentaduebit_2_co), .S(S));
  not not_1 (ZF, or_3_out);
  or or_4 (Co, sommatoretrentaduebit_2_co, sommatoretrentaduebit_1_co);
  Multiplexer multiplexer_2 (.in0(retepreelab_1_ao[31]), .in1(1'b0), .out(multiplexer_2_out), .sel(in_6));
  not not_2 (not_2_out, retepreelab_1_bo[31]);
  Multiplexer multiplexer_3 (.in0(not_2_out), .in1(1'b1), .out(multiplexer_3_out), .sel(in_6));
  FA fa_1 (.CI(Co), .A(multiplexer_2_out), .B(multiplexer_3_out), .S(fa_1_s));  // open: Co
  not not_3 (not_3_out, fa_1_s);
  not not_4 (not_4_out, fa_1_s);
  and and_1 (and_1_out, ZF, not_3_out);
  or or_5 (or_5_out, not_4_out, and_1_out);
  or or_6 (or_6_out, and_1_out, fa_1_s);
  not not_5 (not_5_out, fa_1_s);
  Multiplexer #(.select(3)) multiplexer_4 (
    .in0(fa_1_s), .in1(not_5_out), .in2(or_6_out), .in3(or_5_out), .in4(and_1_out), .in5(not_6_out),
    .out(ris), .sel(in_5));  // open: in6, in7
  not not_6 (not_6_out, and_1_out);

  // Notes on the sheet:
  //   A
  //   B
  //   slt
  //   seq
  //   sge
  //   sle
endmodule

module HA (
  input  A,
  input  B,
  output S,
  output Co
);

  xor xor_1 (S, A, B);
  and and_1 (Co, A, B);
endmodule

module FA (
  input  CI,
  input  A,
  input  B,
  output S,
  output Co
);

  wire ha_1_co, ha_1_s, ha_2_co;

  HA ha_1 (.A(A), .B(B), .S(ha_1_s), .Co(ha_1_co));
  HA ha_2 (.A(CI), .B(ha_1_s), .S(S), .Co(ha_2_co));
  or or_1 (Co, ha_2_co, ha_1_co);
endmodule

module SommatoreQuattroBit (
  input  M,
  input  CI,
  input  [3:0] A,
  input  [3:0] B,
  output [3:0] S,
  output CO
);

  wire and_1_out, and_2_out, and_3_out, and_4_out, fa_1_co, fa_2_co, fa_3_co, fa_4_co;

  FA fa_1 (.CI(and_1_out), .A(A[0]), .B(B[0]), .S(S[0]), .Co(fa_1_co));
  FA fa_2 (.CI(and_2_out), .A(A[1]), .B(B[1]), .S(S[1]), .Co(fa_2_co));
  FA fa_3 (.CI(and_3_out), .A(A[2]), .B(B[2]), .S(S[2]), .Co(fa_3_co));
  FA fa_4 (.CI(and_4_out), .A(A[3]), .B(B[3]), .S(S[3]), .Co(fa_4_co));
  and and_1 (and_1_out, CI, M);
  and and_2 (and_2_out, fa_1_co, M);
  and and_3 (and_3_out, fa_2_co, M);
  and and_4 (and_4_out, fa_3_co, M);
  and and_5 (CO, fa_4_co, M);
endmodule

module SommatoreTrentadueBit (
  input  M,
  input  Ci,
  input  [31:0] A,
  input  [31:0] B,
  output [31:0] S,
  output Co
);

  wire sommatorequattrobit_1_co, sommatorequattrobit_2_co, sommatorequattrobit_3_co,
       sommatorequattrobit_4_co, sommatorequattrobit_5_co, sommatorequattrobit_6_co, sommatorequattrobit_7_co;

  SommatoreQuattroBit sommatorequattrobit_1 (
    .A(A[3:0]), .B(B[3:0]), .M(M), .CI(Ci), .CO(sommatorequattrobit_1_co), .S(S[3:0]));
  SommatoreQuattroBit sommatorequattrobit_2 (
    .A(A[7:4]), .B(B[7:4]), .M(M), .CI(sommatorequattrobit_1_co), .CO(sommatorequattrobit_2_co), .S(S[7:4]));
  SommatoreQuattroBit sommatorequattrobit_3 (
    .A(A[11:8]), .B(B[11:8]), .M(M), .CI(sommatorequattrobit_2_co), .CO(sommatorequattrobit_3_co), .S(S[11:8]));
  SommatoreQuattroBit sommatorequattrobit_4 (
    .A(A[15:12]), .B(B[15:12]), .M(M), .CI(sommatorequattrobit_3_co), .CO(sommatorequattrobit_4_co),
    .S(S[15:12]));
  SommatoreQuattroBit sommatorequattrobit_5 (
    .A(A[19:16]), .B(B[19:16]), .M(M), .CI(sommatorequattrobit_4_co), .CO(sommatorequattrobit_5_co),
    .S(S[19:16]));
  SommatoreQuattroBit sommatorequattrobit_6 (
    .A(A[23:20]), .B(B[23:20]), .M(M), .CI(sommatorequattrobit_5_co), .CO(sommatorequattrobit_6_co),
    .S(S[23:20]));
  SommatoreQuattroBit sommatorequattrobit_7 (
    .A(A[27:24]), .B(B[27:24]), .M(M), .CI(sommatorequattrobit_6_co), .CO(sommatorequattrobit_7_co),
    .S(S[27:24]));
  SommatoreQuattroBit sommatorequattrobit_8 (
    .A(A[31:28]), .B(B[31:28]), .M(M), .CI(sommatorequattrobit_7_co), .CO(Co), .S(S[31:28]));
endmodule

module RetePreelab (
  input  [2:0] c2c1c0,
  input  [31:0] A,
  input  [31:0] B,
  output [31:0] Ao,
  output [31:0] Bo
);

  wire [31:0] multiplexer_1_out, not_1_out;

  Multiplexer #(.width(32)) multiplexer_1 (.in0(B), .in1({32{1'b0}}), .out(multiplexer_1_out), .sel(c2c1c0[1]));
  assign not_1_out = ~multiplexer_1_out;  // NOT_Gate not_1, 32 bits wide
  Multiplexer #(.width(32)) multiplexer_2 (.in0(A), .in1({32{1'b0}}), .out(Ao), .sel(c2c1c0[2]));
  Multiplexer #(.width(32)) multiplexer_3 (.in0(multiplexer_1_out), .in1(not_1_out), .out(Bo), .sel(c2c1c0[0]));
endmodule
