// Logisim project DataPath_old.circ as structural Verilog: 3 circuits, main circuit datapath
module datapath (
  input  CK,
  input  CI4,
  input  [4:0] AluCtrl,
  input  [31:0] WERF,
  input  [31:0] OE1RF,
  input  [31:0] OE2RF,
  input  [2:0] A,
  input  [2:0] B,
  input  [2:0] C,
  input  [2:0] P_C,
  input  [2:0] TEMP,
  input  [2:0] IAR,
  input  [2:0] MAR,
  input  [2:0] MDR,
  input  [1:0] MUX,
  input  [31:0] DATI_IN,
  input  [31:0] CONST,
  output [1:0] flags,
  output out_19,
  output [31:0] INDIRIZZI,
  output [31:0] DATI_OUT
);

  wire rfencoderblock_1_oe1, rfencoderblock_1_oe2, rfencoderblock_1_we;
  wire [4:0] rfencoderblock_1_a1, rfencoderblock_1_a2;
  wire [31:0] alu_1_p6, bubius_1_p4, bubius_2_p4, bubius_7_p5, bubius_8_p1, multiplexer_1_out;

  // Probe on nothing
  // bubius bubius_1: pin names not known; wires that end beside it: DATI_OUT, CONST, CK, bubius_1_p4
  // Probe on nothing
  // bubius bubius_2: pin names not known; wires that end beside it: DATI_OUT, CONST, CK, bubius_2_p4
  // Probe on DATI_OUT
  rfEncoderBlock rfencoderblock_1 (
    .OE1RF(OE1RF), .OE2RF(OE2RF), .WERF(WERF), .A1(rfencoderblock_1_a1), .A2(rfencoderblock_1_a2),
    .WE(rfencoderblock_1_we), .OE1(rfencoderblock_1_oe1), .OE2(rfencoderblock_1_oe2));
  Multiplexer #(.width(32)) multiplexer_1 (.in0(CONST), .in1(CONST), .out(multiplexer_1_out), .sel(MUX[1]));
  // Probe on CONST
  RAM #(.addrWidth(5), .asyncread("true"), .dataWidth(32)) ram_1 (
    .addr(rfencoderblock_1_a1), .we(rfencoderblock_1_we), .oe(rfencoderblock_1_oe1), .clk(CK),
    .din(bubius_8_p1), .dout(bubius_1_p4));
  RAM #(.addrWidth(5), .asyncread("true"), .dataWidth(32)) ram_2 (
    .addr(rfencoderblock_1_a2), .we(rfencoderblock_1_we), .oe(rfencoderblock_1_oe2), .clk(CK),
    .din(bubius_8_p1), .dout(bubius_2_p4));
  // alu alu_1: pin names not known; wires that end beside it: DATI_OUT, CONST, AluCtrl, CI4, out_19, alu_1_p6, flags
  // Probe on nothing
  // bubius bubius_3: pin names not known; wires that end beside it: DATI_OUT, CONST, CK, alu_1_p6
  // Probe on nothing
  // bubius bubius_4: pin names not known; wires that end beside it: DATI_OUT, CONST, CK, alu_1_p6
  // Probe on nothing
  // bubius bubius_5: pin names not known; wires that end beside it: DATI_OUT, CONST, CK, alu_1_p6
  // Probe on nothing
  // bubius bubius_6: pin names not known; wires that end beside it: DATI_OUT, CONST, CK, alu_1_p6
  // Probe on nothing
  // bubius bubius_7: pin names not known; wires that end beside it: INDIRIZZI, DATI_OUT, CONST, CK, bubius_7_p5
  Multiplexer #(.width(32)) multiplexer_2 (.in0(alu_1_p6), .in1(DATI_IN), .out(bubius_7_p5), .sel(MUX[0]));
  // Probe on alu_1_p6
  // Probe on nothing
  // bubius bubius_8: pin names not known; wires that end beside it: bubius_8_p1, CK, alu_1_p6

  // Other names for the same wires on the sheet: Mux_dati = MUX[0]; Mux_ind = MUX[1]; PC[2:0] = P_C

  // Notes on the sheet:
  //   O2 O1 WE
  //   O2 O1 WE
  //   S1
  //   S2
  //   A
  //   B
  //   PC
  //   TEMP
  //   IAR
  //   MAR
  //   MDR
  //   C
endmodule

module test (
  input  [7:0] in_1,
  input  in_2,
  output [7:0] out_3
);

  wire clock_1_out;

  Clock clock_1 (.out(clock_1_out));
  RAM #(.asyncread("true")) ram_1 (.addr(in_1), .oe(in_2), .clk(clock_1_out), .dout(out_3));  // open: we, din
endmodule

module datapath_counter (
  input  [31:0] in_1,
  input  [31:0] in_2,
  input  [31:0] in_3,
  input  [31:0] in_4,
  input  in_5
);

  wire CK;
  wire [3:0] counter_1_q;
  wire [31:0] controlled_buffer_1_out, rom_1_data;

  Counter #(.max('hf), .width(4)) counter_1 (.clk(CK), .Q(counter_1_q));  // open: clr, load, up, count, D, carry
  Clock clock_1 (.out(CK));
  ROM #(.addrWidth(4), .dataWidth(32)) rom_1 (.addr(counter_1_q), .data(rom_1_data));
  assign controlled_buffer_1_out = in_5 ? in_4 : 32'bz;  // Controlled_Buffer controlled_buffer_1
  datapath datapath_1 (
    .CI4(rom_1_data[31]), .MUX(rom_1_data[30:29]), .A(rom_1_data[7:5]), .B(rom_1_data[10:8]),
    .C(rom_1_data[13:11]), .P_C(rom_1_data[16:14]), .TEMP(rom_1_data[19:17]), .IAR(rom_1_data[22:20]),
    .MAR(rom_1_data[25:23]), .MDR(rom_1_data[28:26]), .AluCtrl(rom_1_data[4:0]), .WERF(in_3), .OE1RF(in_2),
    .OE2RF(in_1), .CK(CK), .CONST(controlled_buffer_1_out));  // open: DATI_IN, INDIRIZZI, DATI_OUT, flags, out_19

  // Notes on the sheet:
  //   contents of rom_1 (hex, n*v repeats v):
  //   0 8000c130 850 1000 10101010
endmodule
