// Logisim project SOMMATORE.circ as structural Verilog: 4 circuits, main circuit main
module main (
  input  in_1,
  input  [3:0] in_2,
  input  [3:0] in_3,
  output [3:0] out_4,
  output out_5
);

  FourBitAdder fourbitadder_1 (.in_1(in_1), .in_2(in_2), .in_3(in_3), .out_4(out_4), .out_5(out_5));
  _7_Segment_Display u_7_segment_display_1 ();  // open: g, f, a, b, e, d, c, dp
  _7_Segment_Display u_7_segment_display_2 ();  // open: g, f, a, b, e, d, c, dp
  // BCD_to_7_Segment_decoder bcd_to_7_segment_decoder_1: pin names not known
  // BCD_to_7_Segment_decoder bcd_to_7_segment_decoder_2: pin names not known
  // Binary_to_BCD_converter binary_to_bcd_converter_1: pin names not known; wires that end beside it: {{5{1'b0}}, out_4}
  _7_Segment_Display u_7_segment_display_3 ();  // open: g, f, a, b, e, d, c, dp
  // BCD_to_7_Segment_decoder bcd_to_7_segment_decoder_3: pin names not known
endmodule

module HalfAdder (
  input  in_1,
  input  in_2,
  output out_3,
  output out_4
);

  xor xor_1 (out_3, in_1, in_2);
  and and_1 (out_4, in_1, in_2);
endmodule

module FullAdder (
  input  in_1,
  input  in_2,
  input  in_3,
  output out_4,
  output out_5
);

  wire halfadder_1_out_3, halfadder_1_out_4, halfadder_2_out_4;

  HalfAdder halfadder_1 (.in_1(in_2), .in_2(in_3), .out_3(halfadder_1_out_3), .out_4(halfadder_1_out_4));
  HalfAdder halfadder_2 (.in_1(in_1), .in_2(halfadder_1_out_3), .out_3(out_4), .out_4(halfadder_2_out_4));
  or or_1 (out_5, halfadder_2_out_4, halfadder_1_out_4);
endmodule

module FourBitAdder (
  input  in_1,
  input  [3:0] in_2,
  input  [3:0] in_3,
  output [3:0] out_4,
  output out_5
);

  wire fulladder_1_out_5, fulladder_2_out_5, fulladder_3_out_5;

  FullAdder fulladder_1 (.in_1(in_1), .in_2(in_2[0]), .in_3(in_3[0]), .out_4(out_4[0]), .out_5(fulladder_1_out_5));
  FullAdder fulladder_2 (
    .in_1(fulladder_1_out_5), .in_2(in_2[1]), .in_3(in_3[1]), .out_4(out_4[1]), .out_5(fulladder_2_out_5));
  FullAdder fulladder_3 (
    .in_1(fulladder_2_out_5), .in_2(in_2[2]), .in_3(in_3[2]), .out_4(out_4[2]), .out_5(fulladder_3_out_5));
  FullAdder fulladder_4 (.in_1(fulladder_3_out_5), .in_2(in_2[3]), .in_3(in_3[3]), .out_4(out_4[3]), .out_5(out_5));
endmodule
