// Logisim project counters.circ as structural Verilog: 1 circuit, main circuit main
module main (
  input  in_1
);

  wire clock_1_out, clock_2_out, d_ff_1_q, d_ff_2_q, d_ff_3_q, d_ff_4_q, d_ff_5_q, d_ff_6_q, d_ff_7_q,
       d_ff_8_q, d_ff_9_q, d_ff_10_q, d_ff_11_q, d_ff_12_q, d_ff_13_q, d_ff_14_q, d_ff_15_q, d_ff_16_q,
       not_1_out, or_1_out;

  Clock clock_1 (.out(clock_1_out));
  D_Flip_Flop d_ff_1 (.clk(clock_1_out), .D(or_1_out), .Q(d_ff_1_q));  // open: Qn, preset, reset
  or or_1 (or_1_out, in_1, d_ff_14_q);
  LED led_1 (.in(d_ff_1_q));
  Clock clock_2 (.out(clock_2_out));
  D_Flip_Flop d_ff_2 (.clk(clock_2_out), .D(not_1_out), .Q(d_ff_2_q));  // open: Qn, preset, reset
  not not_1 (not_1_out, d_ff_16_q);
  LED led_2 (.in(d_ff_2_q));
  D_Flip_Flop d_ff_3 (.clk(clock_1_out), .D(d_ff_1_q), .Q(d_ff_3_q));  // open: Qn, preset, reset
  LED led_3 (.in(d_ff_3_q));
  D_Flip_Flop d_ff_4 (.clk(clock_2_out), .D(d_ff_2_q), .Q(d_ff_4_q));  // open: Qn, preset, reset
  LED led_4 (.in(d_ff_4_q));
  D_Flip_Flop d_ff_5 (.clk(clock_1_out), .D(d_ff_3_q), .Q(d_ff_5_q));  // open: Qn, preset, reset
  LED led_5 (.in(d_ff_5_q));
  D_Flip_Flop d_ff_6 (.clk(clock_2_out), .D(d_ff_4_q), .Q(d_ff_6_q));  // open: Qn, preset, reset
  LED led_6 (.in(d_ff_6_q));
  D_Flip_Flop d_ff_7 (.clk(clock_1_out), .D(d_ff_5_q), .Q(d_ff_7_q));  // open: Qn, preset, reset
  LED led_7 (.in(d_ff_7_q));
  D_Flip_Flop d_ff_8 (.clk(clock_2_out), .D(d_ff_6_q), .Q(d_ff_8_q));  // open: Qn, preset, reset
  LED led_8 (.in(d_ff_8_q));
  D_Flip_Flop d_ff_9 (.clk(clock_1_out), .D(d_ff_7_q), .Q(d_ff_9_q));  // open: Qn, preset, reset
  LED led_9 (.in(d_ff_9_q));
  D_Flip_Flop d_ff_10 (.clk(clock_2_out), .D(d_ff_8_q), .Q(d_ff_10_q));  // open: Qn, preset, reset
  LED led_10 (.in(d_ff_10_q));
  D_Flip_Flop d_ff_11 (.clk(clock_1_out), .D(d_ff_9_q), .Q(d_ff_11_q));  // open: Qn, preset, reset
  LED led_11 (.in(d_ff_11_q));
  D_Flip_Flop d_ff_12 (.clk(clock_2_out), .D(d_ff_10_q), .Q(d_ff_12_q));  // open: Qn, preset, reset
  LED led_12 (.in(d_ff_12_q));
  D_Flip_Flop d_ff_13 (.clk(clock_1_out), .D(d_ff_11_q), .Q(d_ff_13_q));  // open: Qn, preset, reset
  D_Flip_Flop d_ff_14 (.clk(clock_1_out), .D(d_ff_13_q), .Q(d_ff_14_q));  // open: Qn, preset, reset
  LED led_13 (.in(d_ff_13_q));
  D_Flip_Flop d_ff_15 (.clk(clock_2_out), .D(d_ff_12_q), .Q(d_ff_15_q));  // open: Qn, preset, reset
  D_Flip_Flop d_ff_16 (.clk(clock_2_out), .D(d_ff_15_q), .Q(d_ff_16_q));  // open: Qn, preset, reset
  LED led_14 (.in(d_ff_15_q));
  LED led_15 (.in(d_ff_14_q));
  LED led_16 (.in(d_ff_16_q));
endmodule
