// Logisim project test2.circ as structural Verilog: 1 circuit, main circuit main
module main (
  input  I,
  output out_2
);

  wire and_1_out, and_2_out, and_3_out, and_4_out, and_5_out, and_6_out, and_7_out, and_8_out, CK, d_ff_1_q,
       d_ff_2_q, d_ff_3_q, not_1_out, not_2_out, not_3_out, not_4_out, not_5_out, not_6_out, not_7_out,
       not_8_out, not_9_out, not_10_out, or_1_out, or_2_out, or_4_out;

  Clock clock_1 (.out(CK));
  not not_1 (not_1_out, d_ff_3_q);
  not not_2 (not_2_out, d_ff_2_q);
  and and_1 (and_1_out, I, not_2_out, d_ff_3_q);
  not not_3 (not_3_out, d_ff_1_q);
  and and_2 (and_2_out, I, not_3_out, not_4_out);
  not not_4 (not_4_out, d_ff_3_q);
  not not_5 (not_5_out, I);
  not not_6 (not_6_out, d_ff_1_q);
  and and_3 (and_3_out, not_5_out, not_6_out, not_7_out, d_ff_3_q);
  not not_7 (not_7_out, d_ff_2_q);
  not not_8 (not_8_out, I);
  and and_4 (and_4_out, not_8_out, d_ff_1_q, not_9_out);
  not not_9 (not_9_out, d_ff_3_q);
  and and_5 (and_5_out, d_ff_2_q, not_10_out);
  not not_10 (not_10_out, d_ff_3_q);
  and and_6 (and_6_out, I, d_ff_1_q);
  and and_7 (and_7_out, I, d_ff_3_q);
  and and_8 (and_8_out, d_ff_1_q, not_1_out);
  or or_1 (or_1_out, and_3_out, and_4_out, and_5_out);
  or or_2 (or_2_out, and_6_out, and_7_out);
  D_Flip_Flop d_ff_1 (.clk(CK), .D(or_2_out), .Q(d_ff_1_q));  // open: Qn, preset, reset
  D_Flip_Flop d_ff_2 (.clk(CK), .D(or_1_out), .Q(d_ff_2_q));  // open: Qn, preset, reset
  D_Flip_Flop d_ff_3 (.clk(CK), .D(or_4_out), .Q(d_ff_3_q));  // open: Qn, preset, reset
  or or_3 (out_2, and_8_out, d_ff_2_q);
  or or_4 (or_4_out, and_1_out, and_2_out);

  // Notes on the sheet:
  //   q2
  //   q1
  //   S.P.
  //   q0
  //   Q0
  //   Q1
  //   Q2
  //   S.F.
endmodule
